// Logisim project cpu24-上板.circ as structural Verilog: 12 circuits, main circuit single_mips
module single_mips (
  input  CLK,
  input  GO,
  output [7:0] SEG,
  output [7:0] NA
);

  wire ALU_equal, AluSrc, and_1_out, and_2_out, and_3_out, and_4_out, and_5_out, BEQ, BGTZ, BNE, Branch,
       comparator_1_eq, comparator_2_lt, JAL, JMP, JR, LHU, MemToReg, MemWrite, not_1_out, not_2_out,
       not_3_out, not_4_out, or_1_out, Pause, RegDst, RegWrite, SignedExt, SRAV, SUBU, Syscall;
  wire [3:0] AluOP;
  wire [4:0] multiplexer_2_out, multiplexer_3_out, multiplexer_4_out, multiplexer_5_out, multiplexer_9_out;
  wire [5:0] Func;
  wire [15:0] \总周期数 ;
  wire [25:6] index;
  wire [31:0] adder_1_out, adder_2_out, ALU_result, bit_extender_1_out, bit_extender_2_out,
       bit_extender_3_out, bit_extender_4_out, controlled_buffer_1_out, DATA_storage_data, LedData, MDin,
       multiplexer_1_out, multiplexer_7_out, multiplexer_8_out, multiplexer_10_out, multiplexer_11_out,
       multiplexer_12_out, PC, RDin, Reg_File_r1, target_offset;
  wire [31:26] IR;

  assign controlled_buffer_1_out = JR ? Reg_File_r1 : 32'bz;  // Controlled_Buffer controlled_buffer_1
  assign controlled_buffer_1_out = JMP ? {PC[31:28], index, Func, 2'b00} : 32'bz;  // Controlled_Buffer controlled_buffer_2
  assign controlled_buffer_1_out = Branch ? adder_1_out : 32'bz;  // Controlled_Buffer controlled_buffer_3
  Adder #(.width(32)) adder_1 (.a(adder_2_out), .b(target_offset), .out(adder_1_out), .cin(1'b0));  // open: cout
  or or_1 (or_1_out, JMP, JR, Branch);
  not not_1 (not_1_out, Pause);
  Counter #(.width(16), .max('hffff), .ongoal("wrap"), .trigger("rising"), .behavior("new")) counter_1 (
    .load(1'b0), .count(not_1_out), .Q(\总周期数 ), .clk(CLK), .clr(1'b0), .preset(1'b0), .down(1'b0));  // open: D, carry
  not not_2 (not_2_out, Pause);
  Multiplexer #(.select(1), .width(32), .disabled(0), .enable("false")) multiplexer_1 (
    .in0(adder_2_out), .in1(controlled_buffer_1_out), .out(multiplexer_1_out), .sel(or_1_out));
  Register #(.width(32), .trigger("rising"), .Select("low")) u_PC (
    .D(multiplexer_1_out), .en(not_2_out), .Q(PC), .clk(CLK), .clr(1'b0), .cs(1'b0), .preset(1'b0));
  Adder #(.width(32)) adder_2 (.a(PC), .b(32'h4), .out(adder_2_out), .cin(1'b0));  // open: cout
  control control (
    .Func(Func), .OP(IR), .ALU_OP(AluOP), .MemToReg(MemToReg), .MemWrite(MemWrite), .ALU_SRC(AluSrc),
    .RegWrite(RegWrite), .SysCALL(Syscall), .SignedExt(SignedExt), .RegDst(RegDst), .JR(JR), .JMP(JMP),
    .Beq(BEQ), .JAL(JAL), .Bne(BNE), .SRAV(SRAV), .SUBU(SUBU), .LHU(LHU), .BGTZ(BGTZ));  // open: ERET, MFC0, MTC0, MF
  ROM #(.addrWidth(10), .dataWidth(32)) IR_storage (.addr(PC[11:2]), .data({IR, index, Func}), .sel(1'b1));
  Multiplexer #(.select(1), .width(5), .disabled(0), .enable("false")) multiplexer_2 (
    .in0(index[20:16]), .in1(index[15:11]), .out(multiplexer_2_out), .sel(RegDst));
  not not_3 (not_3_out, JAL);
  not not_4 (not_4_out, Syscall);
  Multiplexer #(.select(1), .width(5), .disabled(0), .enable("false")) multiplexer_3 (
    .in0(5'b00010), .in1(index[25:21]), .out(multiplexer_3_out), .sel(not_4_out));
  Multiplexer #(.select(1), .width(5), .disabled(0), .enable("false")) multiplexer_4 (
    .in0(5'b00100), .in1(index[20:16]), .out(multiplexer_4_out), .sel(not_4_out));
  Multiplexer #(.select(1), .width(5), .disabled(0), .enable("false")) multiplexer_5 (
    .in0({5{1'b1}}), .in1(multiplexer_2_out), .out(multiplexer_5_out), .sel(not_3_out));
  Multiplexer #(.select(1), .width(32), .disabled(0), .enable("false")) multiplexer_6 (
    .in0(multiplexer_12_out), .in1(adder_2_out), .out(RDin), .sel(JAL));
  assign bit_extender_1_out = {{16{1'b0}}, {index[15:6], Func}};  // Bit_Extender bit_extender_1
  assign bit_extender_2_out = {{16{index[15]}}, {index[15:6], Func}};  // Bit_Extender bit_extender_2
  Multiplexer #(.select(1), .width(32), .disabled(0), .enable("false")) multiplexer_7 (
    .in0(bit_extender_1_out), .in1(bit_extender_2_out), .out(multiplexer_7_out), .sel(SignedExt));
  MIPS_Regifile Reg_File (
    .Din(RDin), .Clk(CLK), .R1(Reg_File_r1), .R2(MDin), .WE(RegWrite), .WAdr(multiplexer_5_out),
    .R1Adr(multiplexer_3_out), .R2Adr(multiplexer_4_out));  // open: out_8
  Comparator #(.width(32), .mode("unsigned")) comparator_1 (
    .a(32'h22), .b(Reg_File_r1), .eq(comparator_1_eq));  // open: gt, lt
  Multiplexer #(.select(1), .width(32), .disabled(0), .enable("false")) multiplexer_8 (
    .in0(MDin), .in1(multiplexer_7_out), .out(multiplexer_8_out), .sel(AluSrc));
  Multiplexer #(.select(1), .width(5), .disabled(0), .enable("false")) multiplexer_9 (
    .in0(index[10:6]), .in1(Reg_File_r1[4:0]), .out(multiplexer_9_out), .sel(SRAV));
  Shifter #(.width(32), .shift("ll")) shifter_1 (.in(multiplexer_7_out), .\dist (5'b00010), .out(target_offset));
  and and_1 (and_1_out, Syscall, comparator_1_eq);
  and and_2 (and_2_out, Syscall, ~comparator_1_eq);  // AND_Gate
  MIPS_ALU ALU (
    .X(Reg_File_r1), .Y(multiplexer_8_out), .AluOP(AluOP), .Equal(ALU_equal), .Result(ALU_result),
    .shamt(multiplexer_9_out));  // open: Result_2
  Register #(.width(32), .trigger("falling"), .Select("low")) register_1 (
    .D(MDin), .en(1'b1), .Q(LedData), .clk(and_1_out), .clr(1'b0), .cs(1'b0), .preset(1'b0));
  Register #(.width(1), .trigger("rising"), .Select("low")) register_2 (
    .D(and_2_out), .en(and_2_out), .Q(Pause), .clk(CLK), .clr(GO), .cs(1'b0), .preset(1'b0));
  Comparator #(.width(32), .mode("twosComplement")) comparator_2 (
    .a({32{1'b0}}), .b(Reg_File_r1), .lt(comparator_2_lt));  // open: gt, eq
  // FPGADigit #(.trigger("rising")) fpgadigit_1: pin names not known; wires that end beside it: ALU_result, LedData, CLK, SEG, NA
  and and_3 (and_3_out, BEQ, ALU_equal);
  and and_4 (and_4_out, BNE, ~ALU_equal);  // AND_Gate
  and and_5 (and_5_out, BGTZ, comparator_2_lt);
  RAM #(.addrWidth(10), .dataWidth(32), .bus("separate"), .Select("high")) DATA_storage (
    .addr(ALU_result[11:2]), .din(MDin), .data(DATA_storage_data), .str(MemWrite), .sel(1'b1), .clk(CLK),
    .ld(1'b1), .clr(1'b0));
  or or_2 (Branch, and_3_out, and_4_out, and_5_out);
  Multiplexer #(.select(1), .width(32), .disabled(0), .enable("false")) multiplexer_10 (
    .in0(ALU_result), .in1(DATA_storage_data), .out(multiplexer_10_out), .sel(MemToReg));
  assign bit_extender_3_out = {{16{1'b0}}, multiplexer_10_out[15:0]};  // Bit_Extender bit_extender_3
  Multiplexer #(.select(1), .width(32), .disabled(0), .enable("false")) multiplexer_11 (
    .in0(bit_extender_3_out), .in1(bit_extender_4_out), .out(multiplexer_11_out), .sel(ALU_result[1]));
  assign bit_extender_4_out = {{16{1'b0}}, multiplexer_10_out[31:16]};  // Bit_Extender bit_extender_4
  Multiplexer #(.select(1), .width(32), .disabled(0), .enable("false")) multiplexer_12 (
    .in0(multiplexer_10_out), .in1(multiplexer_11_out), .out(multiplexer_12_out), .sel(LHU));

  // Other names for the same wires on the sheet: index[5:0] = Func; IR[25:0] = {index, Func};
  //   Shamt[4:0] = index[10:6]; OP[5:0] = IR; PC31_28[3:0] = PC[31:28]

  // Notes on the sheet:
  //   JMP
  //   JR
  //   OP
  //   Func
  //   Beq
  //   Bne
  //   MemToReg
  //   MemWrite
  //   AluOP
  //   AluSrcB
  //   RegWrite
  //   JAL
  //   RegDst
  //   Syscall
  //   contents of IR_storage (hex, n*v repeats v):
  //   20110001 8000c05 20110001 20120002 20130003 8000c09 20110001 20120002 20130003 8000c0d 20110001
  //   20120002 20130003 8000c11 20110001 20120002 20130003 c000cb8 20100001 20110001 118fc0 112020
  //   20020022 c 118882 12200001 8000c15 112020 20020022 c 20110001 118880 112020 20020022 c 12200001
  //   8000c1f 20110001 118fc0 112020 20020022 c 1188c3 112020 20020022 c 118903 112020 20020022 c 118903
  //   112020 20020022 c 118903 112020 20020022 c 118903 112020 20020022 c 118903 112020 20020022 c 118903
  //   112020 20020022 c 118903 112020 20020022 c 20100001 109fc0 139fc3 8021 2012000c 24160003 26100001
  //   3210000f 20080008 20090001 139900 2709825 132020 20020022 c 1094022 1500fff9 22100001 2018000f
  //   2188024 108700 20080008 20090001 139902 2709825 132021 20020022 c 1094022 1500fff9 108702 2c9b022
  //   12c00001 8000c50 4020 1084027 84400 3508ffff 82021 20020022 c 2010ffff 20110000 ae300000 22100001
  //   22310004 ae300000 22100001 22310004 ae300000 22100001 22310004 ae300000 22100001 22310004 ae300000
  //   22100001 22310004 ae300000 22100001 22310004 ae300000 22100001 22310004 ae300000 22100001 22310004
  //   ae300000 22100001 22310004 ae300000 22100001 22310004 ae300000 22100001 22310004 ae300000 22100001
  //   22310004 ae300000 22100001 22310004 ae300000 22100001 22310004 ae300000 22100001 22310004 ae300000
  //   22100001 22310004 22100001 8020 2011003c 8e130000 8e340000 274402a 11000002 ae330000 ae140000
  //   2231fffc 1611fff8 102020 20020022 c 22100004 2011003c 1611fff2 20020032 c 20100000 22100001 102020
  //   20020022 c 22100002 102020 20020022 c 22100003 102020 20020022 c 22100004 102020 20020022 c 22100005
  //   102020 20020022 c 22100006 102020 20020022 c 22100007 102020 20020022 c 22100008 102020 20020022
  //   20020022 c 3e00008
  //   OP
  //   Func
  //   指令字
  //   rs
  //   rt
  //   rd
  //   sa
  //   Imm
  //   instr_index
endmodule

module control (
  input  [5:0] OP,
  input  [5:0] Func,
  input  [4:0] MF,
  output [3:0] ALU_OP,
  output MemToReg,
  output MemWrite,
  output ALU_SRC,
  output RegWrite,
  output SysCALL,
  output SignedExt,
  output RegDst,
  output Beq,
  output Bne,
  output JR,
  output JMP,
  output JAL,
  output SRAV,
  output SUBU,
  output LHU,
  output BGTZ,
  output MFC0,
  output MTC0,
  output ERET
);

  control_signal control_signal_1 (
    .OP0(OP[0]), .OP1(OP[1]), .OP2(OP[2]), .OP3(OP[3]), .OP4(OP[4]), .OP5(OP[5]), .F0(Func[0]), .F1(Func[1]),
    .F2(Func[2]), .F3(Func[3]), .F4(Func[4]), .F5(Func[5]), .S0(ALU_OP[0]), .S1(ALU_OP[1]), .S2(ALU_OP[2]),
    .S3(ALU_OP[3]));
  signal_auto signal_auto_1 (
    .OP0(OP[0]), .OP1(OP[1]), .OP2(OP[2]), .OP3(OP[3]), .OP4(OP[4]), .OP5(OP[5]), .F0(Func[0]), .F1(Func[1]),
    .F2(Func[2]), .F3(Func[3]), .F4(Func[4]), .F5(Func[5]), .MemToReg(MemToReg), .MemWrite(MemWrite),
    .ALU_SRC(ALU_SRC), .RegWrite(RegWrite), .SysCALL(SysCALL), .SignedExt(SignedExt), .RegDst(RegDst),
    .BEQ(Beq), .BNE(Bne), .JR(JR), .JUMP(JMP), .JAL(JAL), .SRAV(SRAV), .SUBU(SUBU), .LHU(LHU), .BGTZ(BGTZ));
  and and_1 (ERET, ~OP[0], ~OP[1], ~OP[2], ~OP[3], OP[4], ~OP[5], ~Func[0], ~Func[1], ~Func[2], Func[3], Func[4], ~Func[5]);  // AND_Gate
  and and_2 (MFC0, ~OP[0], ~OP[1], ~OP[2], ~OP[3], OP[4], ~OP[5], ~MF[0], ~MF[1], ~MF[2], ~MF[3], ~MF[4]);  // AND_Gate
  and and_3 (MTC0, ~OP[0], ~OP[1], ~OP[2], ~OP[3], OP[4], ~OP[5], ~MF[0], ~MF[1], MF[2], ~MF[3], ~MF[4]);  // AND_Gate

  // Other names for the same wires on the sheet: OP_CODE[5:0] = OP
endmodule

module control_signal (
  input  OP0,
  input  OP1,
  input  OP2,
  input  OP3,
  input  OP4,
  input  OP5,
  input  F0,
  input  F1,
  input  F2,
  input  F3,
  input  F4,
  input  F5,
  output S0,
  output S1,
  output S2,
  output S3
);

  wire and_1_out, and_2_out, and_3_out, and_4_out, and_5_out, and_6_out, and_7_out, and_8_out, and_9_out,
       and_10_out, and_11_out, and_12_out, and_13_out, and_14_out, and_15_out, and_16_out, and_17_out,
       and_18_out, and_19_out, and_20_out, and_21_out, and_22_out, and_23_out, and_24_out, and_25_out,
       and_26_out, not_1_out, not_2_out, not_3_out, not_4_out, not_5_out, not_6_out, not_7_out, not_8_out,
       not_9_out, not_10_out, not_11_out, not_12_out, not_13_out, not_14_out, not_15_out, not_16_out,
       not_17_out, not_18_out, not_19_out, not_20_out, not_21_out, not_22_out, not_23_out, not_24_out,
       not_25_out, not_26_out, not_27_out, not_28_out, not_29_out, not_30_out, not_31_out, not_32_out,
       not_33_out, not_34_out, not_35_out, not_36_out, not_37_out, not_38_out, not_39_out, not_40_out,
       not_41_out, not_42_out, not_43_out, not_44_out, not_45_out, not_46_out, not_47_out, not_48_out,
       not_49_out, not_50_out, not_51_out, not_52_out, not_53_out, not_54_out, not_55_out, not_56_out,
       not_57_out, not_58_out, not_59_out, not_60_out, not_61_out, not_62_out, not_63_out, not_64_out,
       not_65_out, not_66_out, not_67_out, not_68_out, not_69_out, not_70_out, not_71_out, not_72_out,
       not_73_out, not_74_out, not_75_out, not_76_out, not_77_out, not_78_out, not_79_out, not_80_out,
       not_81_out, not_82_out, not_83_out, not_84_out, not_85_out, not_86_out, not_87_out, not_88_out,
       not_89_out, not_90_out, not_91_out, not_92_out, not_93_out, not_94_out, not_95_out, not_96_out,
       not_97_out, not_98_out, not_99_out, not_100_out, not_101_out, not_102_out, not_103_out, not_104_out,
       not_105_out, not_106_out, not_107_out, not_108_out, not_109_out, not_110_out, not_111_out,
       not_112_out, not_113_out, not_114_out, not_115_out, not_116_out, not_117_out, not_118_out,
       not_119_out, not_120_out, not_121_out, not_122_out, not_123_out, not_124_out, not_125_out,
       not_126_out, not_127_out, not_128_out, not_129_out, not_130_out, not_131_out, not_132_out,
       not_133_out, not_134_out, not_135_out, not_136_out, not_137_out, not_138_out, not_139_out,
       not_140_out, not_141_out, not_142_out, not_143_out, not_144_out, not_145_out, not_146_out,
       not_147_out, not_148_out, not_149_out, not_150_out, not_151_out, not_152_out, not_153_out,
       not_154_out, not_155_out, not_156_out;

  not not_1 (not_1_out, OP0);
  not not_2 (not_2_out, OP1);
  not not_3 (not_3_out, OP2);
  not not_4 (not_4_out, OP4);
  not not_5 (not_5_out, OP5);
  not not_6 (not_6_out, F0);
  not not_7 (not_7_out, F1);
  not not_8 (not_8_out, F3);
  not not_9 (not_9_out, F4);
  not not_10 (not_10_out, OP0);
  not not_11 (not_11_out, OP1);
  not not_12 (not_12_out, OP2);
  not not_13 (not_13_out, OP4);
  not not_14 (not_14_out, OP5);
  not not_15 (not_15_out, F1);
  not not_16 (not_16_out, F2);
  not not_17 (not_17_out, F3);
  not not_18 (not_18_out, F4);
  not not_19 (not_19_out, OP0);
  not not_20 (not_20_out, OP1);
  not not_21 (not_21_out, OP2);
  not not_22 (not_22_out, OP4);
  not not_23 (not_23_out, OP5);
  not not_24 (not_24_out, F0);
  not not_25 (not_25_out, F2);
  not not_26 (not_26_out, F4);
  not not_27 (not_27_out, OP0);
  not not_28 (not_28_out, OP1);
  not not_29 (not_29_out, OP2);
  not not_30 (not_30_out, OP4);
  not not_31 (not_31_out, OP5);
  not not_32 (not_32_out, F3);
  not not_33 (not_33_out, F4);
  not not_34 (not_34_out, F5);
  not not_35 (not_35_out, OP0);
  not not_36 (not_36_out, OP1);
  not not_37 (not_37_out, OP4);
  not not_38 (not_38_out, OP5);
  not not_39 (not_39_out, OP0);
  not not_40 (not_40_out, OP2);
  not not_41 (not_41_out, OP4);
  not not_42 (not_42_out, OP5);
  not not_43 (not_43_out, OP1);
  not not_44 (not_44_out, OP2);
  not not_45 (not_45_out, OP4);
  not not_46 (not_46_out, OP5);
  not not_47 (not_47_out, OP1);
  not not_48 (not_48_out, OP3);
  not not_49 (not_49_out, OP4);
  not not_50 (not_50_out, OP2);
  not not_51 (not_51_out, OP4);
  not not_52 (not_52_out, OP0);
  not not_53 (not_53_out, OP1);
  not not_54 (not_54_out, OP2);
  not not_55 (not_55_out, OP3);
  not not_56 (not_56_out, OP4);
  not not_57 (not_57_out, OP5);
  not not_58 (not_58_out, F0);
  not not_59 (not_59_out, F1);
  not not_60 (not_60_out, F3);
  not not_61 (not_61_out, F4);
  not not_62 (not_62_out, OP0);
  not not_63 (not_63_out, OP1);
  not not_64 (not_64_out, OP2);
  not not_65 (not_65_out, OP3);
  not not_66 (not_66_out, OP4);
  not not_67 (not_67_out, OP5);
  not not_68 (not_68_out, F0);
  not not_69 (not_69_out, F2);
  not not_70 (not_70_out, F3);
  not not_71 (not_71_out, F4);
  not not_72 (not_72_out, OP0);
  not not_73 (not_73_out, OP1);
  not not_74 (not_74_out, OP2);
  not not_75 (not_75_out, OP3);
  not not_76 (not_76_out, OP4);
  not not_77 (not_77_out, OP5);
  not not_78 (not_78_out, F0);
  not not_79 (not_79_out, F2);
  not not_80 (not_80_out, F4);
  not not_81 (not_81_out, OP0);
  not not_82 (not_82_out, OP1);
  not not_83 (not_83_out, OP2);
  not not_84 (not_84_out, OP3);
  not not_85 (not_85_out, OP4);
  not not_86 (not_86_out, OP5);
  not not_87 (not_87_out, F3);
  not not_88 (not_88_out, F4);
  not not_89 (not_89_out, OP0);
  not not_90 (not_90_out, OP1);
  not not_91 (not_91_out, OP4);
  not not_92 (not_92_out, OP5);
  not not_93 (not_93_out, OP0);
  not not_94 (not_94_out, OP2);
  not not_95 (not_95_out, OP4);
  not not_96 (not_96_out, OP5);
  not not_97 (not_97_out, OP0);
  not not_98 (not_98_out, OP1);
  not not_99 (not_99_out, OP2);
  not not_100 (not_100_out, OP4);
  not not_101 (not_101_out, OP5);
  not not_102 (not_102_out, F0);
  not not_103 (not_103_out, F1);
  not not_104 (not_104_out, F3);
  not not_105 (not_105_out, F4);
  not not_106 (not_106_out, OP0);
  not not_107 (not_107_out, OP1);
  not not_108 (not_108_out, OP2);
  not not_109 (not_109_out, OP4);
  not not_110 (not_110_out, OP5);
  not not_111 (not_111_out, F2);
  not not_112 (not_112_out, F3);
  not not_113 (not_113_out, F4);
  not not_114 (not_114_out, OP0);
  not not_115 (not_115_out, OP1);
  not not_116 (not_116_out, OP2);
  not not_117 (not_117_out, OP4);
  not not_118 (not_118_out, OP5);
  not not_119 (not_119_out, F2);
  not not_120 (not_120_out, F4);
  not not_121 (not_121_out, OP0);
  not not_122 (not_122_out, OP1);
  not not_123 (not_123_out, OP4);
  not not_124 (not_124_out, OP5);
  not not_125 (not_125_out, OP1);
  not not_126 (not_126_out, OP2);
  not not_127 (not_127_out, OP4);
  not not_128 (not_128_out, OP5);
  not not_129 (not_129_out, OP1);
  not not_130 (not_130_out, OP3);
  not not_131 (not_131_out, OP4);
  not not_132 (not_132_out, OP2);
  not not_133 (not_133_out, OP4);
  not not_134 (not_134_out, OP0);
  not not_135 (not_135_out, OP1);
  not not_136 (not_136_out, OP2);
  not not_137 (not_137_out, OP3);
  not not_138 (not_138_out, OP4);
  not not_139 (not_139_out, OP5);
  not not_140 (not_140_out, F2);
  not not_141 (not_141_out, F4);
  not not_142 (not_142_out, OP0);
  not not_143 (not_143_out, OP1);
  not not_144 (not_144_out, OP2);
  not not_145 (not_145_out, OP3);
  not not_146 (not_146_out, OP4);
  not not_147 (not_147_out, OP5);
  not not_148 (not_148_out, F3);
  not not_149 (not_149_out, F4);
  not not_150 (not_150_out, OP0);
  not not_151 (not_151_out, OP2);
  not not_152 (not_152_out, OP4);
  not not_153 (not_153_out, OP5);
  not not_154 (not_154_out, OP1);
  not not_155 (not_155_out, OP4);
  not not_156 (not_156_out, OP5);
  and and_1 (and_1_out, not_1_out, not_2_out, not_3_out, not_4_out, not_5_out, not_6_out, not_7_out, not_8_out, not_9_out, F5);
  and and_2 (and_2_out, not_10_out, not_11_out, not_12_out, not_13_out, not_14_out, not_15_out, not_16_out, not_17_out, not_18_out, F5);
  and and_3 (and_3_out, not_19_out, not_20_out, not_21_out, not_22_out, not_23_out, not_24_out, F1, not_25_out, F3, not_26_out, F5);
  and and_4 (and_4_out, not_27_out, not_28_out, not_29_out, not_30_out, not_31_out, F0, F1, not_32_out, not_33_out, not_34_out);
  and and_5 (and_5_out, not_35_out, not_36_out, OP3, not_37_out, not_38_out);
  and and_6 (and_6_out, not_39_out, not_40_out, OP3, not_41_out, not_42_out);
  and and_7 (and_7_out, not_43_out, not_44_out, OP3, not_45_out, not_46_out);
  and and_8 (and_8_out, OP0, not_47_out, OP2, not_48_out, not_49_out, OP5);
  and and_9 (and_9_out, OP0, OP1, not_50_out, not_51_out, OP5);
  and and_10 (and_10_out, not_52_out, not_53_out, not_54_out, not_55_out, not_56_out, not_57_out, not_58_out, not_59_out, F2, not_60_out, not_61_out, F5);
  and and_11 (and_11_out, not_62_out, not_63_out, not_64_out, not_65_out, not_66_out, not_67_out, not_68_out, F1, not_69_out, not_70_out, not_71_out);
  and and_12 (and_12_out, not_72_out, not_73_out, not_74_out, not_75_out, not_76_out, not_77_out, not_78_out, F1, not_79_out, not_80_out, F5);
  and and_13 (and_13_out, not_81_out, not_82_out, not_83_out, not_84_out, not_85_out, not_86_out, F0, F1, not_87_out, not_88_out, F5);
  and and_14 (and_14_out, not_89_out, not_90_out, OP2, OP3, not_91_out, not_92_out);
  and and_15 (and_15_out, not_93_out, OP1, not_94_out, OP3, not_95_out, not_96_out);
  and and_16 (and_16_out, not_97_out, not_98_out, not_99_out, not_100_out, not_101_out, not_102_out, not_103_out, not_104_out, not_105_out, F5);
  and and_17 (and_17_out, not_106_out, not_107_out, not_108_out, not_109_out, not_110_out, not_111_out, not_112_out, not_113_out, F5);
  and and_18 (and_18_out, not_114_out, not_115_out, not_116_out, not_117_out, not_118_out, F0, F1, not_119_out, not_120_out, F5);
  and and_19 (and_19_out, not_121_out, not_122_out, OP3, not_123_out, not_124_out);
  and and_20 (and_20_out, not_125_out, not_126_out, OP3, not_127_out, not_128_out);
  and and_21 (and_21_out, OP0, not_129_out, OP2, not_130_out, not_131_out, OP5);
  and and_22 (and_22_out, OP0, OP1, not_132_out, not_133_out, OP5);
  and and_23 (and_23_out, not_134_out, not_135_out, not_136_out, not_137_out, not_138_out, not_139_out, F1, not_140_out, F3, not_141_out, F5);
  and and_24 (and_24_out, not_142_out, not_143_out, not_144_out, not_145_out, not_146_out, not_147_out, F0, F2, not_148_out, not_149_out, F5);
  and and_25 (and_25_out, not_150_out, OP1, not_151_out, OP3, not_152_out, not_153_out);
  and and_26 (and_26_out, OP0, not_154_out, OP2, OP3, not_155_out, not_156_out);
  or or_1 (S0, and_1_out, and_2_out, and_3_out, and_4_out, and_5_out, and_6_out, and_7_out, and_8_out, and_9_out);
  or or_2 (S1, and_10_out, and_11_out, and_12_out, and_13_out, and_14_out, and_15_out);
  or or_3 (S2, and_16_out, and_17_out, and_18_out, and_19_out, and_20_out, and_21_out, and_22_out);
  or or_4 (S3, and_23_out, and_24_out, and_25_out, and_26_out);
endmodule

module signal_auto (
  input  OP0,
  input  OP1,
  input  OP2,
  input  OP3,
  input  OP4,
  input  OP5,
  input  F0,
  input  F1,
  input  F2,
  input  F3,
  input  F4,
  input  F5,
  output MemToReg,
  output MemWrite,
  output ALU_SRC,
  output RegWrite,
  output SysCALL,
  output SignedExt,
  output RegDst,
  output BEQ,
  output BNE,
  output JR,
  output JUMP,
  output JAL,
  output SRAV,
  output SUBU,
  output LHU,
  output BGTZ
);

  wire and_1_out, and_2_out, and_4_out, and_5_out, and_6_out, and_7_out, and_8_out, and_9_out, and_10_out,
       and_11_out, and_12_out, and_13_out, and_14_out, and_15_out, and_17_out, and_18_out, and_19_out,
       and_20_out, and_21_out, and_22_out, and_23_out, and_24_out, not_1_out, not_2_out, not_3_out,
       not_4_out, not_5_out, not_6_out, not_7_out, not_8_out, not_9_out, not_10_out, not_11_out, not_12_out,
       not_13_out, not_14_out, not_15_out, not_16_out, not_17_out, not_18_out, not_19_out, not_20_out,
       not_21_out, not_22_out, not_23_out, not_24_out, not_25_out, not_26_out, not_27_out, not_28_out,
       not_29_out, not_30_out, not_31_out, not_32_out, not_33_out, not_34_out, not_35_out, not_36_out,
       not_37_out, not_38_out, not_39_out, not_40_out, not_41_out, not_42_out, not_43_out, not_44_out,
       not_45_out, not_46_out, not_47_out, not_48_out, not_49_out, not_50_out, not_51_out, not_52_out,
       not_53_out, not_54_out, not_55_out, not_56_out, not_57_out, not_58_out, not_59_out, not_60_out,
       not_61_out, not_62_out, not_63_out, not_64_out, not_65_out, not_66_out, not_67_out, not_68_out,
       not_69_out, not_70_out, not_71_out, not_72_out, not_73_out, not_74_out, not_75_out, not_76_out,
       not_77_out, not_78_out, not_79_out, not_80_out, not_81_out, not_82_out, not_83_out, not_84_out,
       not_85_out, not_86_out, not_87_out, not_88_out, not_89_out, not_90_out, not_91_out, not_92_out,
       not_93_out, not_94_out, not_95_out, not_96_out, not_97_out, not_98_out, not_99_out, not_100_out,
       not_101_out, not_102_out, not_103_out, not_104_out, not_105_out, not_106_out, not_107_out,
       not_108_out, not_109_out, not_110_out, not_111_out, not_112_out, not_113_out, not_114_out,
       not_115_out, not_116_out, not_117_out, not_118_out, not_119_out, not_120_out, not_121_out,
       not_122_out, not_123_out, not_124_out, not_125_out, not_126_out, not_127_out, not_128_out,
       not_129_out, not_130_out, not_131_out, not_132_out, not_133_out, not_134_out, not_135_out,
       not_136_out, not_137_out, not_138_out, not_139_out, not_140_out, not_141_out, not_142_out,
       not_143_out, not_144_out, not_145_out, not_146_out, not_147_out, not_148_out, not_149_out,
       not_150_out, not_151_out, not_152_out, not_153_out, not_154_out, not_155_out, not_156_out,
       not_157_out, not_158_out, not_159_out, not_160_out, not_161_out, not_162_out, not_163_out,
       not_164_out, not_165_out, not_166_out, not_167_out, not_168_out, not_169_out, not_170_out,
       not_171_out, not_172_out, not_173_out, not_174_out, not_175_out, not_176_out;

  not not_1 (not_1_out, OP1);
  not not_2 (not_2_out, OP3);
  not not_3 (not_3_out, OP4);
  not not_4 (not_4_out, OP2);
  not not_5 (not_5_out, OP3);
  not not_6 (not_6_out, OP4);
  not not_7 (not_7_out, OP2);
  not not_8 (not_8_out, OP4);
  not not_9 (not_9_out, OP0);
  not not_10 (not_10_out, OP2);
  not not_11 (not_11_out, OP4);
  not not_12 (not_12_out, OP5);
  not not_13 (not_13_out, OP1);
  not not_14 (not_14_out, OP4);
  not not_15 (not_15_out, OP5);
  not not_16 (not_16_out, OP1);
  not not_17 (not_17_out, OP3);
  not not_18 (not_18_out, OP4);
  not not_19 (not_19_out, OP2);
  not not_20 (not_20_out, OP4);
  not not_21 (not_21_out, OP0);
  not not_22 (not_22_out, OP1);
  not not_23 (not_23_out, OP2);
  not not_24 (not_24_out, OP4);
  not not_25 (not_25_out, OP5);
  not not_26 (not_26_out, F0);
  not not_27 (not_27_out, F2);
  not not_28 (not_28_out, F3);
  not not_29 (not_29_out, F4);
  not not_30 (not_30_out, OP0);
  not not_31 (not_31_out, OP1);
  not not_32 (not_32_out, OP2);
  not not_33 (not_33_out, OP4);
  not not_34 (not_34_out, OP5);
  not not_35 (not_35_out, F1);
  not not_36 (not_36_out, F3);
  not not_37 (not_37_out, F4);
  not not_38 (not_38_out, OP0);
  not not_39 (not_39_out, OP1);
  not not_40 (not_40_out, OP2);
  not not_41 (not_41_out, OP4);
  not not_42 (not_42_out, OP5);
  not not_43 (not_43_out, F2);
  not not_44 (not_44_out, F4);
  not not_45 (not_45_out, OP0);
  not not_46 (not_46_out, OP1);
  not not_47 (not_47_out, OP2);
  not not_48 (not_48_out, OP4);
  not not_49 (not_49_out, OP5);
  not not_50 (not_50_out, F3);
  not not_51 (not_51_out, F4);
  not not_52 (not_52_out, OP0);
  not not_53 (not_53_out, OP2);
  not not_54 (not_54_out, OP4);
  not not_55 (not_55_out, OP5);
  not not_56 (not_56_out, OP1);
  not not_57 (not_57_out, OP4);
  not not_58 (not_58_out, OP5);
  not not_59 (not_59_out, OP1);
  not not_60 (not_60_out, OP3);
  not not_61 (not_61_out, OP4);
  not not_62 (not_62_out, OP2);
  not not_63 (not_63_out, OP3);
  not not_64 (not_64_out, OP4);
  not not_65 (not_65_out, OP0);
  not not_66 (not_66_out, OP1);
  not not_67 (not_67_out, OP2);
  not not_68 (not_68_out, OP3);
  not not_69 (not_69_out, OP4);
  not not_70 (not_70_out, OP5);
  not not_71 (not_71_out, F0);
  not not_72 (not_72_out, F1);
  not not_73 (not_73_out, F4);
  not not_74 (not_74_out, F5);
  not not_75 (not_75_out, OP0);
  not not_76 (not_76_out, OP2);
  not not_77 (not_77_out, OP4);
  not not_78 (not_78_out, OP5);
  not not_79 (not_79_out, OP1);
  not not_80 (not_80_out, OP2);
  not not_81 (not_81_out, OP4);
  not not_82 (not_82_out, OP5);
  not not_83 (not_83_out, OP1);
  not not_84 (not_84_out, OP3);
  not not_85 (not_85_out, OP4);
  not not_86 (not_86_out, OP5);
  not not_87 (not_87_out, OP3);
  not not_88 (not_88_out, OP4);
  not not_89 (not_89_out, OP5);
  not not_90 (not_90_out, OP0);
  not not_91 (not_91_out, OP1);
  not not_92 (not_92_out, OP2);
  not not_93 (not_93_out, OP3);
  not not_94 (not_94_out, OP4);
  not not_95 (not_95_out, OP5);
  not not_96 (not_96_out, F0);
  not not_97 (not_97_out, F2);
  not not_98 (not_98_out, F3);
  not not_99 (not_99_out, F4);
  not not_100 (not_100_out, OP0);
  not not_101 (not_101_out, OP1);
  not not_102 (not_102_out, OP2);
  not not_103 (not_103_out, OP3);
  not not_104 (not_104_out, OP4);
  not not_105 (not_105_out, OP5);
  not not_106 (not_106_out, F1);
  not not_107 (not_107_out, F3);
  not not_108 (not_108_out, F4);
  not not_109 (not_109_out, OP0);
  not not_110 (not_110_out, OP1);
  not not_111 (not_111_out, OP2);
  not not_112 (not_112_out, OP3);
  not not_113 (not_113_out, OP4);
  not not_114 (not_114_out, OP5);
  not not_115 (not_115_out, F2);
  not not_116 (not_116_out, F4);
  not not_117 (not_117_out, OP0);
  not not_118 (not_118_out, OP1);
  not not_119 (not_119_out, OP2);
  not not_120 (not_120_out, OP3);
  not not_121 (not_121_out, OP4);
  not not_122 (not_122_out, OP5);
  not not_123 (not_123_out, F3);
  not not_124 (not_124_out, F4);
  not not_125 (not_125_out, OP0);
  not not_126 (not_126_out, OP1);
  not not_127 (not_127_out, OP3);
  not not_128 (not_128_out, OP4);
  not not_129 (not_129_out, OP5);
  not not_130 (not_130_out, OP1);
  not not_131 (not_131_out, OP3);
  not not_132 (not_132_out, OP4);
  not not_133 (not_133_out, OP5);
  not not_134 (not_134_out, OP0);
  not not_135 (not_135_out, OP1);
  not not_136 (not_136_out, OP2);
  not not_137 (not_137_out, OP3);
  not not_138 (not_138_out, OP4);
  not not_139 (not_139_out, OP5);
  not not_140 (not_140_out, F0);
  not not_141 (not_141_out, F1);
  not not_142 (not_142_out, F2);
  not not_143 (not_143_out, F4);
  not not_144 (not_144_out, F5);
  not not_145 (not_145_out, OP2);
  not not_146 (not_146_out, OP3);
  not not_147 (not_147_out, OP4);
  not not_148 (not_148_out, OP5);
  not not_149 (not_149_out, OP2);
  not not_150 (not_150_out, OP3);
  not not_151 (not_151_out, OP4);
  not not_152 (not_152_out, OP5);
  not not_153 (not_153_out, OP0);
  not not_154 (not_154_out, OP1);
  not not_155 (not_155_out, OP2);
  not not_156 (not_156_out, OP3);
  not not_157 (not_157_out, OP4);
  not not_158 (not_158_out, OP5);
  not not_159 (not_159_out, F3);
  not not_160 (not_160_out, F4);
  not not_161 (not_161_out, F5);
  not not_162 (not_162_out, OP0);
  not not_163 (not_163_out, OP1);
  not not_164 (not_164_out, OP2);
  not not_165 (not_165_out, OP3);
  not not_166 (not_166_out, OP4);
  not not_167 (not_167_out, OP5);
  not not_168 (not_168_out, F2);
  not not_169 (not_169_out, F3);
  not not_170 (not_170_out, F4);
  not not_171 (not_171_out, OP1);
  not not_172 (not_172_out, OP3);
  not not_173 (not_173_out, OP4);
  not not_174 (not_174_out, OP3);
  not not_175 (not_175_out, OP4);
  not not_176 (not_176_out, OP5);
  and and_1 (and_1_out, OP0, not_1_out, OP2, not_2_out, not_3_out, OP5);
  and and_2 (and_2_out, OP0, OP1, not_4_out, not_5_out, not_6_out, OP5);
  and and_3 (MemWrite, OP0, OP1, not_7_out, OP3, not_8_out, OP5);
  and and_4 (and_4_out, not_9_out, not_10_out, OP3, not_11_out, not_12_out);
  and and_5 (and_5_out, not_13_out, OP3, not_14_out, not_15_out);
  and and_6 (and_6_out, OP0, not_16_out, OP2, not_17_out, not_18_out, OP5);
  and and_7 (and_7_out, OP0, OP1, not_19_out, not_20_out, OP5);
  and and_8 (and_8_out, not_21_out, not_22_out, not_23_out, not_24_out, not_25_out, not_26_out, not_27_out, not_28_out, not_29_out);
  and and_9 (and_9_out, not_30_out, not_31_out, not_32_out, not_33_out, not_34_out, not_35_out, not_36_out, not_37_out, F5);
  and and_10 (and_10_out, not_38_out, not_39_out, not_40_out, not_41_out, not_42_out, F1, not_43_out, not_44_out, F5);
  and and_11 (and_11_out, not_45_out, not_46_out, not_47_out, not_48_out, not_49_out, F0, F1, not_50_out, not_51_out);
  and and_12 (and_12_out, not_52_out, not_53_out, OP3, not_54_out, not_55_out);
  and and_13 (and_13_out, not_56_out, OP3, not_57_out, not_58_out);
  and and_14 (and_14_out, OP0, not_59_out, OP2, not_60_out, not_61_out, OP5);
  and and_15 (and_15_out, OP0, OP1, not_62_out, not_63_out, not_64_out);
  and and_16 (SysCALL, not_65_out, not_66_out, not_67_out, not_68_out, not_69_out, not_70_out, not_71_out, not_72_out, F2, F3, not_73_out, not_74_out);
  and and_17 (and_17_out, not_75_out, not_76_out, OP3, not_77_out, not_78_out);
  and and_18 (and_18_out, not_79_out, not_80_out, OP3, not_81_out, not_82_out);
  and and_19 (and_19_out, not_83_out, OP2, not_84_out, not_85_out, not_86_out);
  and and_20 (and_20_out, OP0, OP2, not_87_out, not_88_out, not_89_out);
  and and_21 (and_21_out, not_90_out, not_91_out, not_92_out, not_93_out, not_94_out, not_95_out, not_96_out, not_97_out, not_98_out, not_99_out);
  and and_22 (and_22_out, not_100_out, not_101_out, not_102_out, not_103_out, not_104_out, not_105_out, not_106_out, not_107_out, not_108_out, F5);
  and and_23 (and_23_out, not_109_out, not_110_out, not_111_out, not_112_out, not_113_out, not_114_out, F1, not_115_out, not_116_out, F5);
  and and_24 (and_24_out, not_117_out, not_118_out, not_119_out, not_120_out, not_121_out, not_122_out, F0, F1, not_123_out, not_124_out);
  and and_25 (BEQ, not_125_out, not_126_out, OP2, not_127_out, not_128_out, not_129_out);
  and and_26 (BNE, OP0, not_130_out, OP2, not_131_out, not_132_out, not_133_out);
  and and_27 (JR, not_134_out, not_135_out, not_136_out, not_137_out, not_138_out, not_139_out, not_140_out, not_141_out, not_142_out, F3, not_143_out, not_144_out);
  and and_28 (JUMP, OP1, not_145_out, not_146_out, not_147_out, not_148_out);
  and and_29 (JAL, OP0, OP1, not_149_out, not_150_out, not_151_out, not_152_out);
  and and_30 (SRAV, not_153_out, not_154_out, not_155_out, not_156_out, not_157_out, not_158_out, F0, F1, F2, not_159_out, not_160_out, not_161_out);
  and and_31 (SUBU, not_162_out, not_163_out, not_164_out, not_165_out, not_166_out, not_167_out, F0, F1, not_168_out, not_169_out, not_170_out, F5);
  and and_32 (LHU, OP0, not_171_out, OP2, not_172_out, not_173_out, OP5);
  and and_33 (BGTZ, OP0, OP1, OP2, not_174_out, not_175_out, not_176_out);
  or or_1 (MemToReg, and_1_out, and_2_out);
  or or_2 (ALU_SRC, and_4_out, and_5_out, and_6_out, and_7_out);
  or or_3 (RegWrite, and_8_out, and_9_out, and_10_out, and_11_out, and_12_out, and_13_out, and_14_out, and_15_out);
  or or_4 (SignedExt, and_17_out, and_18_out, and_19_out, and_20_out);
  or or_5 (RegDst, and_21_out, and_22_out, and_23_out, and_24_out);
endmodule

// ALU
module MIPS_ALU (
  input  [4:0] shamt,
  input  [31:0] X,
  input  [31:0] Y,
  input  [3:0] AluOP,
  output Equal,
  output [31:0] Result,
  output [31:0] Result_2
);

  wire [0:0] comparator_1_lt, comparator_2_lt;
  wire [31:0] adder_1_out, AND_out, divider_1_out, divider_1_rem, multiplier_1_cout, multiplier_1_out,
       NOR_out, OR_out, shifter_1_out, shifter_2_out, shifter_3_out, subtractor_1_out, XOR_out;

  assign AND_out = X & Y;  // AND_Gate AND, 32 bits wide
  assign OR_out = X | Y;  // OR_Gate OR, 32 bits wide
  Shifter #(.width(32), .shift("ll")) shifter_1 (.in(Y), .\dist (shamt), .out(shifter_1_out));
  Shifter #(.width(32), .shift("ar")) shifter_2 (.in(Y), .\dist (shamt), .out(shifter_2_out));
  Shifter #(.width(32), .shift("lr")) shifter_3 (.in(Y), .\dist (shamt), .out(shifter_3_out));
  Multiplier #(.width(32)) multiplier_1 (.a(X), .b(Y), .out(multiplier_1_out), .cout(multiplier_1_cout));  // open: cin
  Divider #(.width(32)) divider_1 (.a(X), .b(Y), .out(divider_1_out), .rem(divider_1_rem));  // open: upper
  Adder #(.width(32)) adder_1 (.a(X), .b(Y), .out(adder_1_out));  // open: cin, cout
  Subtractor #(.width(32)) subtractor_1 (.a(X), .b(Y), .out(subtractor_1_out));  // open: bin, bout
  assign XOR_out = X ^ Y;  // XOR_Gate XOR, 32 bits wide
  assign NOR_out = ~(X | Y);  // NOR_Gate NOR, 32 bits wide
  Comparator #(.width(32), .mode("twosComplement")) comparator_1 (
    .a(X), .b(Y), .eq(Equal), .lt(comparator_1_lt[0]));  // open: gt
  Comparator #(.width(32), .mode("unsigned")) comparator_2 (.a(X), .b(Y), .lt(comparator_2_lt[0]));  // open: gt, eq
  Multiplexer #(.select(4), .width(32), .disabled("Z"), .enable("false")) multiplexer_1 (
    .in0(shifter_1_out), .in1(shifter_2_out), .in2(shifter_3_out), .in3(multiplier_1_out),
    .in4(divider_1_out), .in5(adder_1_out), .in6(subtractor_1_out), .in7(AND_out), .in8(OR_out),
    .in9(XOR_out), .in10(NOR_out), .in11({{31{1'b0}}, comparator_1_lt[0]}),
    .in12({{31{1'b0}}, comparator_2_lt[0]}), .in13({32{1'b0}}), .in14({32{1'b0}}), .in15({32{1'b0}}),
    .out(Result), .sel(AluOP));
  Multiplexer #(.select(4), .width(32), .disabled("Z"), .enable("false")) multiplexer_2 (
    .in0({32{1'b0}}), .in1({32{1'b0}}), .in2({32{1'b0}}), .in3(multiplier_1_cout), .in4(divider_1_rem),
    .in5({32{1'b0}}), .in6({32{1'b0}}), .in7({32{1'b0}}), .in8({32{1'b0}}), .in9({32{1'b0}}),
    .in10({32{1'b0}}), .in11({32{1'b0}}), .in12({32{1'b0}}), .in13({32{1'b0}}), .in14({32{1'b0}}),
    .in15({32{1'b0}}), .out(Result_2), .sel(AluOP));

  // Other names for the same wires on the sheet: Result2[31:0] = Result_2; S[3:0] = AluOP

  // Notes on the sheet:
  //   不要改变此引脚区域内容，也不要改变ALU封装形式
  //   输入引脚
  //   输出引脚
endmodule

module MIPS_Regifile (
  input  [31:0] Din,
  input  Clk,
  input  WE,
  input  [4:0] R1Adr,
  input  [4:0] WAdr,
  input  [4:0] R2Adr,
  output [31:0] R1,
  output [3:0] out_8,
  output [31:0] R2
);

  // RegisterFile registerfile_1: pin names not known; wires that end beside it: Din, Clk, WE, WAdr, R1Adr, R2Adr, R1, R2
endmodule

module rename_the_circuit (
  input  [31:0] BranchAddr_in,
  input  [31:0] PC,
  input  AddrReady,
  input  CLK,
  input  BranchTaken,
  input  [31:0] EX_PC,
  output Miss,
  output [31:0] BranchAddr_out,
  output Jump
);

  wire and_1_out, and_2_out, and_3_out, and_4_out, and_5_out, and_6_out, and_7_out, and_8_out, and_9_out,
       and_10_out, and_11_out, and_12_out, and_13_out, and_14_out, and_15_out, and_16_out, and_17_out,
       comparator_1_eq, comparator_2_eq, comparator_3_eq, comparator_4_eq, comparator_5_eq, comparator_6_eq,
       comparator_7_eq, comparator_8_eq, comparator_9_eq, comparator_10_eq, comparator_11_eq,
       comparator_12_eq, comparator_13_eq, comparator_14_eq, comparator_15_eq, comparator_16_eq,
       decoder_1_out0, decoder_1_out1, decoder_1_out2, decoder_1_out3, decoder_1_out4, decoder_1_out5,
       decoder_1_out6, decoder_1_out7, Miss_t, rename_the_circuit_1_p11, rename_the_circuit_1_p12,
       rename_the_circuit_2_p14, rename_the_circuit_3_p14, rename_the_circuit_4_p13,
       rename_the_circuit_4_p16, rename_the_circuit_5_p15, rename_the_circuit_5_p17,
       rename_the_circuit_6_p14, rename_the_circuit_6_p16, rename_the_circuit_7_p14,
       rename_the_circuit_7_p16, rename_the_circuit_8_p5, rename_the_circuit_8_p11, rename_the_circuit_9_p2,
       rename_the_circuit_9_p3, rename_the_circuit_9_p5, rename_the_circuit_10_p4, rename_the_circuit_10_p6,
       rename_the_circuit_11_p4, rename_the_circuit_11_p6, rename_the_circuit_11_p9,
       rename_the_circuit_12_p4, rename_the_circuit_12_p6, rename_the_circuit_12_p11,
       rename_the_circuit_13_p4, rename_the_circuit_13_p6, rename_the_circuit_13_p11,
       rename_the_circuit_14_p4, rename_the_circuit_14_p6, rename_the_circuit_14_p11,
       rename_the_circuit_15_p4, rename_the_circuit_15_p6, rename_the_circuit_15_p11,
       rename_the_circuit_16_p5, undriven_2, undriven_4, undriven_6, undriven_8, undriven_10, undriven_12,
       undriven_14, undriven_16;
  wire [2:0] max_1_max_num, max_2_max_num, max_3_max_num, max_4_max_num, max_5_max_num, max_6_max_num,
       max_7_max_num;
  wire [15:0] Count0, Count1, Count2, Count3, Count4, Count5, Count6, Count7, max_1_max, max_2_max,
       max_3_max, max_4_max, max_5_max, max_6_max;
  wire [31:0] rename_the_circuit_9_p1, rename_the_circuit_9_p4, rename_the_circuit_10_p5,
       rename_the_circuit_11_p5, rename_the_circuit_12_p5, rename_the_circuit_13_p5,
       rename_the_circuit_14_p5, rename_the_circuit_15_p5, undriven, undriven_3, undriven_5, undriven_7,
       undriven_9, undriven_11, undriven_13, undriven_15;

  Max max_1 (.Y(Count0), .X(Count1), .Y_num(3'b000), .X_num(3'b001), .MAX(max_1_max), .Max_num(max_1_max_num));
  Max max_2 (.Y(Count2), .X(Count3), .Y_num(3'b010), .X_num(3'b011), .MAX(max_2_max), .Max_num(max_2_max_num));
  Max max_3 (.Y(Count4), .X(Count5), .Y_num(3'b100), .X_num(3'b101), .MAX(max_3_max), .Max_num(max_3_max_num));
  Max max_4 (.Y(Count6), .X(Count7), .Y_num(3'b110), .X_num(3'b111), .MAX(max_4_max), .Max_num(max_4_max_num));
  Max max_5 (
    .Y(max_1_max), .X(max_2_max), .Y_num(max_1_max_num), .X_num(max_2_max_num), .MAX(max_5_max),
    .Max_num(max_5_max_num));
  Max max_6 (
    .Y(max_3_max), .X(max_4_max), .Y_num(max_3_max_num), .X_num(max_4_max_num), .MAX(max_6_max),
    .Max_num(max_6_max_num));
  Decoder #(.select(3), .tristate("false"), .disabled("Z"), .enable("false")) decoder_1 (
    .out0(decoder_1_out0), .out1(decoder_1_out1), .out2(decoder_1_out2), .out3(decoder_1_out3),
    .out4(decoder_1_out4), .out5(decoder_1_out5), .out6(decoder_1_out6), .out7(decoder_1_out7),
    .sel(max_7_max_num));
  Max max_7 (
    .Y(max_5_max), .X(max_6_max), .Y_num(max_5_max_num), .X_num(max_6_max_num), .Max_num(max_7_max_num));  // open: MAX
  and and_1 (and_1_out, AddrReady, Miss_t);
  and and_2 (and_2_out, and_1_out, decoder_1_out0);
  and and_3 (and_3_out, and_1_out, decoder_1_out1);
  and and_4 (and_4_out, and_1_out, decoder_1_out2);
  and and_5 (and_5_out, and_1_out, decoder_1_out3);
  and and_6 (and_6_out, and_1_out, decoder_1_out4);
  and and_7 (and_7_out, and_1_out, decoder_1_out5);
  and and_8 (and_8_out, and_1_out, decoder_1_out6);
  and and_9 (and_9_out, and_1_out, decoder_1_out7);
  // rename_the_circuit rename_the_circuit_1: pin names not known; wires that end beside it: EX_PC, BranchAddr_in, and_2_out, EX_PC, BranchAddr_in, AddrReady, BranchTaken, CLK, CLK, CLK, rename_the_circuit_1_p11, rename_the_circuit_1_p12
  // rename_the_circuit rename_the_circuit_2: pin names not known; wires that end beside it: BranchTaken, and_2_out, EX_PC, BranchAddr_in, and_3_out, EX_PC, BranchAddr_in, AddrReady, AddrReady, CLK, CLK, CLK, rename_the_circuit_1_p12, rename_the_circuit_2_p14
  // rename_the_circuit rename_the_circuit_3: pin names not known; wires that end beside it: BranchTaken, and_3_out, EX_PC, BranchAddr_in, and_4_out, EX_PC, BranchAddr_in, AddrReady, AddrReady, CLK, CLK, CLK, rename_the_circuit_2_p14, rename_the_circuit_3_p14
  // rename_the_circuit rename_the_circuit_4: pin names not known; wires that end beside it: BranchTaken, and_4_out, EX_PC, BranchAddr_in, and_5_out, EX_PC, BranchAddr_in, AddrReady, AddrReady, CLK, CLK, CLK, rename_the_circuit_4_p13, rename_the_circuit_4_p13, rename_the_circuit_3_p14, rename_the_circuit_4_p16
  // rename_the_circuit rename_the_circuit_5: pin names not known; wires that end beside it: BranchTaken, and_5_out, EX_PC, BranchAddr_in, and_6_out, EX_PC, BranchAddr_in, AddrReady, AddrReady, CLK, CLK, CLK, rename_the_circuit_4_p13, rename_the_circuit_4_p13, rename_the_circuit_5_p15, rename_the_circuit_4_p16, rename_the_circuit_5_p17
  // rename_the_circuit rename_the_circuit_6: pin names not known; wires that end beside it: BranchTaken, and_6_out, EX_PC, BranchAddr_in, and_7_out, EX_PC, BranchAddr_in, AddrReady, AddrReady, CLK, CLK, CLK, rename_the_circuit_5_p15, rename_the_circuit_6_p14, rename_the_circuit_5_p17, rename_the_circuit_6_p16
  // rename_the_circuit rename_the_circuit_7: pin names not known; wires that end beside it: BranchTaken, and_7_out, EX_PC, BranchAddr_in, and_8_out, EX_PC, BranchAddr_in, AddrReady, AddrReady, CLK, CLK, CLK, rename_the_circuit_6_p14, rename_the_circuit_7_p14, rename_the_circuit_6_p16, rename_the_circuit_7_p16
  // rename_the_circuit rename_the_circuit_8: pin names not known; wires that end beside it: BranchTaken, and_8_out, EX_PC, BranchAddr_in, rename_the_circuit_8_p5, and_9_out, AddrReady, AddrReady, CLK, rename_the_circuit_7_p14, rename_the_circuit_8_p11, rename_the_circuit_7_p16
  Comparator #(.width(32), .mode("twosComplement")) comparator_1 (
    .a(rename_the_circuit_9_p1), .b(EX_PC), .eq(comparator_1_eq));  // open: gt, lt
  Comparator #(.width(32), .mode("twosComplement")) comparator_2 (
    .a(rename_the_circuit_9_p4), .b(EX_PC), .eq(comparator_2_eq));  // open: gt, lt
  Comparator #(.width(32), .mode("twosComplement")) comparator_3 (
    .a(rename_the_circuit_10_p5), .b(EX_PC), .eq(comparator_3_eq));  // open: gt, lt
  Comparator #(.width(32), .mode("twosComplement")) comparator_4 (
    .a(rename_the_circuit_11_p5), .b(EX_PC), .eq(comparator_4_eq));  // open: gt, lt
  Comparator #(.width(32), .mode("twosComplement")) comparator_5 (
    .a(rename_the_circuit_12_p5), .b(EX_PC), .eq(comparator_5_eq));  // open: gt, lt
  Comparator #(.width(32), .mode("twosComplement")) comparator_6 (
    .a(rename_the_circuit_13_p5), .b(EX_PC), .eq(comparator_6_eq));  // open: gt, lt
  Comparator #(.width(32), .mode("twosComplement")) comparator_7 (
    .a(rename_the_circuit_14_p5), .b(EX_PC), .eq(comparator_7_eq));  // open: gt, lt
  Comparator #(.width(32), .mode("twosComplement")) comparator_8 (
    .a(rename_the_circuit_15_p5), .b(EX_PC), .eq(comparator_8_eq));  // open: gt, lt
  and and_10 (and_10_out, comparator_1_eq, rename_the_circuit_9_p3);
  and and_11 (and_11_out, comparator_2_eq, rename_the_circuit_10_p4);
  and and_12 (and_12_out, comparator_3_eq, rename_the_circuit_11_p4);
  and and_13 (and_13_out, comparator_4_eq, rename_the_circuit_12_p4);
  and and_14 (and_14_out, comparator_5_eq, rename_the_circuit_13_p4);
  and and_15 (and_15_out, comparator_6_eq, rename_the_circuit_14_p4);
  and and_16 (and_16_out, comparator_7_eq, rename_the_circuit_15_p4);
  and and_17 (and_17_out, comparator_8_eq, rename_the_circuit_16_p5);
  nor nor_1 (Miss_t, and_10_out, and_11_out, and_12_out, and_13_out, and_14_out, and_15_out, and_16_out, and_17_out);
  // rename_the_circuit rename_the_circuit_9: pin names not known; wires that end beside it: rename_the_circuit_9_p1, rename_the_circuit_9_p2, rename_the_circuit_9_p3, rename_the_circuit_9_p4, rename_the_circuit_9_p5, rename_the_circuit_1_p11, rename_the_circuit_1_p12, CLK, CLK, CLK, Jump
  // rename_the_circuit rename_the_circuit_10: pin names not known; wires that end beside it: rename_the_circuit_9_p3, rename_the_circuit_9_p4, rename_the_circuit_9_p5, rename_the_circuit_10_p4, rename_the_circuit_10_p5, rename_the_circuit_10_p6, rename_the_circuit_1_p12, rename_the_circuit_2_p14, CLK, CLK, CLK, Jump, Jump
  // rename_the_circuit rename_the_circuit_11: pin names not known; wires that end beside it: rename_the_circuit_10_p4, rename_the_circuit_10_p5, rename_the_circuit_10_p6, rename_the_circuit_11_p4, rename_the_circuit_11_p5, rename_the_circuit_11_p6, rename_the_circuit_2_p14, rename_the_circuit_3_p14, rename_the_circuit_11_p9, rename_the_circuit_11_p9, CLK, CLK, CLK, Jump, Jump
  // rename_the_circuit rename_the_circuit_12: pin names not known; wires that end beside it: rename_the_circuit_11_p4, rename_the_circuit_11_p5, rename_the_circuit_11_p6, rename_the_circuit_12_p4, rename_the_circuit_12_p5, rename_the_circuit_12_p6, rename_the_circuit_3_p14, rename_the_circuit_4_p16, rename_the_circuit_11_p9, rename_the_circuit_11_p9, rename_the_circuit_12_p11, rename_the_circuit_12_p11, CLK, CLK, CLK, Jump, Jump
  // rename_the_circuit rename_the_circuit_13: pin names not known; wires that end beside it: rename_the_circuit_12_p4, rename_the_circuit_12_p5, rename_the_circuit_12_p6, rename_the_circuit_13_p4, rename_the_circuit_13_p5, rename_the_circuit_13_p6, rename_the_circuit_4_p16, rename_the_circuit_5_p17, rename_the_circuit_12_p11, rename_the_circuit_12_p11, rename_the_circuit_13_p11, rename_the_circuit_13_p11, CLK, CLK, CLK, Jump, Jump
  // rename_the_circuit rename_the_circuit_14: pin names not known; wires that end beside it: rename_the_circuit_13_p4, rename_the_circuit_13_p5, rename_the_circuit_13_p6, rename_the_circuit_14_p4, rename_the_circuit_14_p5, rename_the_circuit_14_p6, rename_the_circuit_5_p17, rename_the_circuit_6_p16, rename_the_circuit_13_p11, rename_the_circuit_13_p11, rename_the_circuit_14_p11, rename_the_circuit_14_p11, CLK, CLK, CLK, Jump, Jump
  // rename_the_circuit rename_the_circuit_15: pin names not known; wires that end beside it: rename_the_circuit_14_p4, rename_the_circuit_14_p5, rename_the_circuit_14_p6, rename_the_circuit_15_p4, rename_the_circuit_15_p5, rename_the_circuit_15_p6, rename_the_circuit_6_p16, rename_the_circuit_7_p16, rename_the_circuit_14_p11, rename_the_circuit_14_p11, rename_the_circuit_15_p11, rename_the_circuit_15_p11, CLK, CLK, CLK, Jump, Jump
  // rename_the_circuit rename_the_circuit_16: pin names not known; wires that end beside it: rename_the_circuit_15_p4, rename_the_circuit_15_p5, rename_the_circuit_15_p6, rename_the_circuit_8_p5, rename_the_circuit_16_p5, rename_the_circuit_7_p16, rename_the_circuit_15_p11, rename_the_circuit_15_p11, CLK, Jump, Jump
  Comparator #(.width(32), .mode("twosComplement")) comparator_9 (
    .a(undriven), .b(PC), .eq(comparator_9_eq));  // open: gt, lt
  and and_18 (CLK, comparator_9_eq, undriven_2);
  Comparator #(.width(32), .mode("twosComplement")) comparator_10 (
    .a(undriven_3), .b(PC), .eq(comparator_10_eq));  // open: gt, lt
  and and_19 (CLK, comparator_10_eq, undriven_4);
  Comparator #(.width(32), .mode("twosComplement")) comparator_11 (
    .a(undriven_5), .b(PC), .eq(comparator_11_eq));  // open: gt, lt
  and and_20 (CLK, comparator_11_eq, undriven_6);
  Comparator #(.width(32), .mode("twosComplement")) comparator_12 (
    .a(undriven_7), .b(PC), .eq(comparator_12_eq));  // open: gt, lt
  and and_21 (CLK, comparator_12_eq, undriven_8);
  Comparator #(.width(32), .mode("twosComplement")) comparator_13 (
    .a(undriven_9), .b(PC), .eq(comparator_13_eq));  // open: gt, lt
  and and_22 (CLK, comparator_13_eq, undriven_10);
  Comparator #(.width(32), .mode("twosComplement")) comparator_14 (
    .a(undriven_11), .b(PC), .eq(comparator_14_eq));  // open: gt, lt
  and and_23 (CLK, comparator_14_eq, undriven_12);
  Comparator #(.width(32), .mode("twosComplement")) comparator_15 (
    .a(undriven_13), .b(PC), .eq(comparator_15_eq));  // open: gt, lt
  and and_24 (CLK, comparator_15_eq, undriven_14);
  Comparator #(.width(32), .mode("twosComplement")) comparator_16 (
    .a(undriven_15), .b(PC), .eq(comparator_16_eq));  // open: gt, lt
  and and_25 (rename_the_circuit_8_p5, comparator_16_eq, undriven_16);
  nor nor_2 (Miss, CLK, CLK, CLK, CLK, CLK, CLK, CLK, rename_the_circuit_8_p5);

  // Other names for the same wires on the sheet: BraAddr[31:0] = BranchAddr_in; EX_PC_in[31:0] = EX_PC;
  //   PC_in[31:0] = PC

  // Notes on the sheet:
  //   输入引脚区
  //   请勿增改引脚，请勿修改子电路封装
  //   电路功能：利用上面给定的隧道构建8行的Cache，cache映射方式自选
  //   请在下方利用上方输入输出引脚的隧道信号构建电路，ctrl+d复制选择部件
  //   输出引脚区
endmodule

module IF_ID (
  input  PreditJump,
  input  [31:0] IR_in,
  input  [31:0] PC_in,
  input  CLK,
  input  CLR,
  input  Stall,
  output PreditJump_2,
  output [31:0] IR_out,
  output [31:0] PC_out
);

  wire multiplexer_1_out, not_1_out;
  wire [31:0] multiplexer_2_out, multiplexer_3_out;

  Multiplexer #(.select(1), .width(1), .disabled("Z"), .enable("false")) multiplexer_1 (
    .in0(PreditJump), .in1(1'b0), .out(multiplexer_1_out), .sel(CLR));
  Multiplexer #(.select(1), .width(32), .disabled("Z"), .enable("false")) multiplexer_2 (
    .in0(IR_in), .in1({32{1'b0}}), .out(multiplexer_2_out), .sel(CLR));
  Multiplexer #(.select(1), .width(32), .disabled("Z"), .enable("false")) multiplexer_3 (
    .in0(PC_in), .in1({32{1'b0}}), .out(multiplexer_3_out), .sel(CLR));
  Pull_Resistor #(.pull(0)) pull_resistor_1 (.node(CLR));
  not not_1 (not_1_out, Stall);
  Register #(.width(1), .trigger("rising"), .Select("low")) register_1 (
    .D(multiplexer_1_out), .en(not_1_out), .Q(PreditJump_2), .clk(CLK));  // open: clr
  Register #(.width(32), .trigger("rising"), .Select("low")) register_2 (
    .D(multiplexer_2_out), .en(not_1_out), .Q(IR_out), .clk(CLK));  // open: clr
  Register #(.width(32), .trigger("rising"), .Select("low")) register_3 (
    .D(multiplexer_3_out), .en(not_1_out), .Q(PC_out), .clk(CLK));  // open: clr
  Pull_Resistor #(.pull(0)) pull_resistor_2 (.node(not_1_out));
endmodule

module ID_EX (
  input  RegWrite_in,
  input  [31:0] IR_in,
  input  RegDst_in,
  input  MemToReg_in,
  input  [31:0] PC_in,
  input  Syscall_in,
  input  [3:0] AluOP_in,
  input  JMP_in,
  input  [31:0] A_in,
  input  AluSrc_in,
  input  JR_in,
  input  MemWrite,
  input  [31:0] B_in,
  input  JAL_in,
  input  BGTZ,
  input  [31:0] Imm_in,
  input  SignedExt_in,
  input  SUBU,
  input  [4:0] Shamt,
  input  Beq_in,
  input  LHU,
  input  [31:0] MD_in,
  input  SRAV,
  input  Bne_in,
  input  [31:0] ALU_in,
  input  PreditJump,
  input  CLK,
  input  CLR,
  input  Stall,
  output RegWrite_out,
  output [31:0] IR_out,
  output RegDst_out,
  output MemToReg_out,
  output [31:0] PC_out,
  output Syscall_out,
  output [3:0] AluOP_out,
  output JMP_out,
  output [31:0] A_out,
  output AluSrc_out,
  output JR_out,
  output MemWrite_2,
  output [31:0] B_out,
  output JAL_out,
  output BGTZ_2,
  output [31:0] Imm_out,
  output SignedExt_out,
  output SUBU_2,
  output [4:0] Shamt_2,
  output Beq_out,
  output LHU_2,
  output [31:0] MD_out,
  output SRAV_2,
  output Bne_out,
  output [31:0] ALU_out,
  output PreditJump_2
);

  wire multiplexer_1_out, multiplexer_2_out, multiplexer_3_out, multiplexer_4_out, multiplexer_5_out,
       multiplexer_6_out, multiplexer_7_out, multiplexer_8_out, multiplexer_9_out, multiplexer_10_out,
       multiplexer_11_out, multiplexer_13_out, multiplexer_14_out, multiplexer_15_out, multiplexer_16_out,
       multiplexer_17_out, multiplexer_18_out, not_1_out;
  wire [3:0] multiplexer_12_out;
  wire [4:0] multiplexer_24_out;
  wire [31:0] multiplexer_19_out, multiplexer_20_out, multiplexer_21_out, multiplexer_22_out,
       multiplexer_23_out, multiplexer_25_out, multiplexer_26_out;

  Multiplexer #(.select(1), .width(1), .disabled("Z"), .enable("false")) multiplexer_1 (
    .in0(RegDst_in), .in1(1'b0), .out(multiplexer_1_out), .sel(CLR));
  Multiplexer #(.select(1), .width(1), .disabled("Z"), .enable("false")) multiplexer_2 (
    .in0(Syscall_in), .in1(1'b0), .out(multiplexer_2_out), .sel(CLR));
  Multiplexer #(.select(1), .width(1), .disabled("Z"), .enable("false")) multiplexer_3 (
    .in0(JMP_in), .in1(1'b0), .out(multiplexer_3_out), .sel(CLR));
  Multiplexer #(.select(1), .width(1), .disabled("Z"), .enable("false")) multiplexer_4 (
    .in0(JR_in), .in1(1'b0), .out(multiplexer_4_out), .sel(CLR));
  Multiplexer #(.select(1), .width(1), .disabled("Z"), .enable("false")) multiplexer_5 (
    .in0(JAL_in), .in1(1'b0), .out(multiplexer_5_out), .sel(CLR));
  Multiplexer #(.select(1), .width(1), .disabled("Z"), .enable("false")) multiplexer_6 (
    .in0(SignedExt_in), .in1(1'b0), .out(multiplexer_6_out), .sel(CLR));
  Multiplexer #(.select(1), .width(1), .disabled("Z"), .enable("false")) multiplexer_7 (
    .in0(Beq_in), .in1(1'b0), .out(multiplexer_7_out), .sel(CLR));
  Multiplexer #(.select(1), .width(1), .disabled("Z"), .enable("false")) multiplexer_8 (
    .in0(Bne_in), .in1(1'b0), .out(multiplexer_8_out), .sel(CLR));
  Multiplexer #(.select(1), .width(1), .disabled("Z"), .enable("false")) multiplexer_9 (
    .in0(PreditJump), .in1(1'b0), .out(multiplexer_9_out), .sel(CLR));
  Pull_Resistor #(.pull(0)) pull_resistor_1 (.node(CLR));
  not not_1 (not_1_out, Stall);
  Register #(.width(1), .trigger("rising"), .Select("low")) register_1 (
    .D(multiplexer_1_out), .en(not_1_out), .Q(RegDst_out), .clk(CLK));  // open: clr
  Register #(.width(1), .trigger("rising"), .Select("low")) register_2 (
    .D(multiplexer_2_out), .en(not_1_out), .Q(Syscall_out), .clk(CLK));  // open: clr
  Register #(.width(1), .trigger("rising"), .Select("low")) register_3 (
    .D(multiplexer_3_out), .en(not_1_out), .Q(JMP_out), .clk(CLK));  // open: clr
  Register #(.width(1), .trigger("rising"), .Select("low")) register_4 (
    .D(multiplexer_4_out), .en(not_1_out), .Q(JR_out), .clk(CLK));  // open: clr
  Register #(.width(1), .trigger("rising"), .Select("low")) register_5 (
    .D(multiplexer_5_out), .en(not_1_out), .Q(JAL_out), .clk(CLK));  // open: clr
  Register #(.width(1), .trigger("rising"), .Select("low")) register_6 (
    .D(multiplexer_6_out), .en(not_1_out), .Q(SignedExt_out), .clk(CLK));  // open: clr
  Register #(.width(1), .trigger("rising"), .Select("low")) register_7 (
    .D(multiplexer_7_out), .en(not_1_out), .Q(Beq_out), .clk(CLK));  // open: clr
  Register #(.width(1), .trigger("rising"), .Select("low")) register_8 (
    .D(multiplexer_8_out), .en(not_1_out), .Q(Bne_out), .clk(CLK));  // open: clr
  Register #(.width(1), .trigger("rising"), .Select("low")) register_9 (
    .D(multiplexer_9_out), .en(not_1_out), .Q(PreditJump_2), .clk(CLK));  // open: clr
  Pull_Resistor #(.pull(0)) pull_resistor_2 (.node(not_1_out));
  Multiplexer #(.select(1), .width(1), .disabled("Z"), .enable("false")) multiplexer_10 (
    .in0(RegWrite_in), .in1(1'b0), .out(multiplexer_10_out), .sel(CLR));
  Multiplexer #(.select(1), .width(1), .disabled("Z"), .enable("false")) multiplexer_11 (
    .in0(MemToReg_in), .in1(1'b0), .out(multiplexer_11_out), .sel(CLR));
  Multiplexer #(.select(1), .width(4), .disabled("Z"), .enable("false")) multiplexer_12 (
    .in0(AluOP_in), .in1(4'b0000), .out(multiplexer_12_out), .sel(CLR));
  Multiplexer #(.select(1), .width(1), .disabled("Z"), .enable("false")) multiplexer_13 (
    .in0(AluSrc_in), .in1(1'b0), .out(multiplexer_13_out), .sel(CLR));
  Multiplexer #(.select(1), .width(1), .disabled("Z"), .enable("false")) multiplexer_14 (
    .in0(MemWrite), .in1(1'b0), .out(multiplexer_14_out), .sel(CLR));
  Multiplexer #(.select(1), .width(1), .disabled("Z"), .enable("false")) multiplexer_15 (
    .in0(BGTZ), .in1(1'b0), .out(multiplexer_15_out), .sel(CLR));
  Multiplexer #(.select(1), .width(1), .disabled("Z"), .enable("false")) multiplexer_16 (
    .in0(SUBU), .in1(1'b0), .out(multiplexer_16_out), .sel(CLR));
  Multiplexer #(.select(1), .width(1), .disabled("Z"), .enable("false")) multiplexer_17 (
    .in0(LHU), .in1(1'b0), .out(multiplexer_17_out), .sel(CLR));
  Multiplexer #(.select(1), .width(1), .disabled("Z"), .enable("false")) multiplexer_18 (
    .in0(SRAV), .in1(1'b0), .out(multiplexer_18_out), .sel(CLR));
  Register #(.width(1), .trigger("rising"), .Select("low")) register_10 (
    .D(multiplexer_10_out), .en(not_1_out), .Q(RegWrite_out), .clk(CLK));  // open: clr
  Register #(.width(1), .trigger("rising"), .Select("low")) register_11 (
    .D(multiplexer_11_out), .en(not_1_out), .Q(MemToReg_out), .clk(CLK));  // open: clr
  Register #(.width(4), .trigger("rising"), .Select("low")) register_12 (
    .D(multiplexer_12_out), .en(not_1_out), .Q(AluOP_out), .clk(CLK));  // open: clr
  Register #(.width(1), .trigger("rising"), .Select("low")) register_13 (
    .D(multiplexer_13_out), .en(not_1_out), .Q(AluSrc_out), .clk(CLK));  // open: clr
  Register #(.width(1), .trigger("rising"), .Select("low")) register_14 (
    .D(multiplexer_14_out), .en(not_1_out), .Q(MemWrite_2), .clk(CLK));  // open: clr
  Register #(.width(1), .trigger("rising"), .Select("low")) register_15 (
    .D(multiplexer_15_out), .en(not_1_out), .Q(BGTZ_2), .clk(CLK));  // open: clr
  Register #(.width(1), .trigger("rising"), .Select("low")) register_16 (
    .D(multiplexer_16_out), .en(not_1_out), .Q(SUBU_2), .clk(CLK));  // open: clr
  Register #(.width(1), .trigger("rising"), .Select("low")) register_17 (
    .D(multiplexer_17_out), .en(not_1_out), .Q(LHU_2), .clk(CLK));  // open: clr
  Register #(.width(1), .trigger("rising"), .Select("low")) register_18 (
    .D(multiplexer_18_out), .en(not_1_out), .Q(SRAV_2), .clk(CLK));  // open: clr
  Multiplexer #(.select(1), .width(32), .disabled("Z"), .enable("false")) multiplexer_19 (
    .in0(IR_in), .in1({32{1'b0}}), .out(multiplexer_19_out), .sel(CLR));
  Multiplexer #(.select(1), .width(32), .disabled("Z"), .enable("false")) multiplexer_20 (
    .in0(PC_in), .in1({32{1'b0}}), .out(multiplexer_20_out), .sel(CLR));
  Multiplexer #(.select(1), .width(32), .disabled("Z"), .enable("false")) multiplexer_21 (
    .in0(A_in), .in1({32{1'b0}}), .out(multiplexer_21_out), .sel(CLR));
  Multiplexer #(.select(1), .width(32), .disabled("Z"), .enable("false")) multiplexer_22 (
    .in0(B_in), .in1({32{1'b0}}), .out(multiplexer_22_out), .sel(CLR));
  Multiplexer #(.select(1), .width(32), .disabled("Z"), .enable("false")) multiplexer_23 (
    .in0(Imm_in), .in1({32{1'b0}}), .out(multiplexer_23_out), .sel(CLR));
  Multiplexer #(.select(1), .width(5), .disabled("Z"), .enable("false")) multiplexer_24 (
    .in0(Shamt), .in1({5{1'b0}}), .out(multiplexer_24_out), .sel(CLR));
  Multiplexer #(.select(1), .width(32), .disabled("Z"), .enable("false")) multiplexer_25 (
    .in0(MD_in), .in1({32{1'b0}}), .out(multiplexer_25_out), .sel(CLR));
  Multiplexer #(.select(1), .width(32), .disabled("Z"), .enable("false")) multiplexer_26 (
    .in0(ALU_in), .in1({32{1'b0}}), .out(multiplexer_26_out), .sel(CLR));
  Register #(.width(32), .trigger("rising"), .Select("low")) register_19 (
    .D(multiplexer_19_out), .en(not_1_out), .Q(IR_out), .clk(CLK));  // open: clr
  Register #(.width(32), .trigger("rising"), .Select("low")) register_20 (
    .D(multiplexer_20_out), .en(not_1_out), .Q(PC_out), .clk(CLK));  // open: clr
  Register #(.width(32), .trigger("rising"), .Select("low")) register_21 (
    .D(multiplexer_21_out), .en(not_1_out), .Q(A_out), .clk(CLK));  // open: clr
  Register #(.width(32), .trigger("rising"), .Select("low")) register_22 (
    .D(multiplexer_22_out), .en(not_1_out), .Q(B_out), .clk(CLK));  // open: clr
  Register #(.width(32), .trigger("rising"), .Select("low")) register_23 (
    .D(multiplexer_23_out), .en(not_1_out), .Q(Imm_out), .clk(CLK));  // open: clr
  Register #(.width(5), .trigger("rising"), .Select("low")) register_24 (
    .D(multiplexer_24_out), .en(not_1_out), .Q(Shamt_2), .clk(CLK));  // open: clr
  Register #(.width(32), .trigger("rising"), .Select("low")) register_25 (
    .D(multiplexer_25_out), .en(not_1_out), .Q(MD_out), .clk(CLK));  // open: clr
  Register #(.width(32), .trigger("rising"), .Select("low")) register_26 (
    .D(multiplexer_26_out), .en(not_1_out), .Q(ALU_out), .clk(CLK));  // open: clr
endmodule

module FSM (
  input  RST,
  input  CLK,
  input  X,
  input  EN,
  output D2,
  output Z,
  output D1
);

  wire and_1_out, and_2_out, and_3_out, and_4_out, D1_qn, D2_qn, or_2_out;

  D_Flip_Flop #(.trigger("rising"), .Pre_Clr_Positions("ABOVE_BELOW"), .NegatePresetClear("false"), .enable("true"), .NewFFLayout("true")) u_D2 (
    .clk(CLK), .D(Z), .Q(D2), .Qn(D2_qn), .preset(RST), .en(EN));  // open: reset
  D_Flip_Flop #(.trigger("rising"), .Pre_Clr_Positions("ABOVE_BELOW"), .NegatePresetClear("false"), .enable("true"), .NewFFLayout("true")) u_D1 (
    .clk(CLK), .D(or_2_out), .Q(D1), .Qn(D1_qn), .preset(RST), .en(EN));  // open: reset
  and and_1 (and_1_out, D2, D1_qn);
  or or_1 (Z, and_1_out, and_2_out);
  and and_2 (and_2_out, X, D1);
  and and_3 (and_3_out, D2_qn, D1_qn, X);
  and and_4 (and_4_out, ~X, D2, D1);  // AND_Gate
  or or_2 (or_2_out, and_3_out, and_4_out);
endmodule

// MAX
module Max (
  input  [15:0] Y,
  input  [15:0] X,
  input  [2:0] Y_num,
  input  [2:0] X_num,
  output [15:0] MAX,
  output [2:0] Max_num
);

  wire comparator_1_eq, comparator_1_gt, or_1_out;

  Multiplexer #(.select(1), .width(16), .disabled("Z"), .enable("false")) multiplexer_1 (
    .in0(Y), .in1(X), .out(MAX), .sel(or_1_out));
  Comparator #(.width(16), .mode("unsigned")) comparator_1 (
    .a(X), .b(Y), .gt(comparator_1_gt), .eq(comparator_1_eq));  // open: lt
  or or_1 (or_1_out, comparator_1_gt, comparator_1_eq);
  Multiplexer #(.select(1), .width(3), .disabled("Z"), .enable("false")) multiplexer_2 (
    .in0(Y_num), .in1(X_num), .out(Max_num), .sel(or_1_out));

  // Notes on the sheet:
  //   输出两个输入中的较大值，并输出较大值的3位编号
endmodule

module BTB (
  input  [31:0] PC,
  input  [31:0] EX_PC,
  input  [31:0] EX_BranchAddr,
  input  EX_Branch,
  input  EX_BranchTaken,
  input  CLK,
  output [31:0] JumpAddr,
  output PreditJump
);

  wire rename_the_circuit_1_p7, rename_the_circuit_1_p8;

  // rename_the_circuit rename_the_circuit_1: pin names not known; wires that end beside it: EX_PC, PC, EX_BranchTaken, JumpAddr, CLK, EX_Branch, rename_the_circuit_1_p7, rename_the_circuit_1_p8, EX_BranchAddr
  and and_1 (PreditJump, ~rename_the_circuit_1_p7, rename_the_circuit_1_p8);  // AND_Gate

  // Other names for the same wires on the sheet: EX_Addr[31:0] = EX_BranchAddr
endmodule
