// Logisim project cpu24-动态分支预测.circ as structural Verilog: 24 circuits, main circuit ◇单周期MIPS
module \单周期MIPS  (
  input  IR1,
  input  IR2,
  input  IR3,
  output RegWrite,
  output MemWrite,
  output [31:0] PC,
  output [31:0] IR,
  output [31:0] RDin,
  output [31:0] MDin,
  output [31:0] LedData
);

  wire AluSrc, and_1_out, and_2_out, and_3_out, and_4_out, and_5_out, BEQ, BGTZ, BNE, Branch, CLK,
       clock_2_out, comparator_1_eq, comparator_2_lt, comparator_3_eq, comparator_3_lt, d_ff_1_q, Go, IR1_t,
       IR2_t, IR3_t, IRA, IRB, IRC, JAL, JMP, JR, LHU, MemToReg, mips_alu_1_equal, nand_1_out, not_1_out,
       not_2_out, not_3_out, not_4_out, or_1_out, Pause, RegDst, SignedExt, SRAV, SUBU, Syscall, W1, W2, W3;
  wire [3:0] AluOP;
  wire [4:0] multiplexer_2_out, multiplexer_3_out, multiplexer_4_out, multiplexer_5_out, multiplexer_9_out;
  wire [12:0] CNT_num;
  wire [15:0] \总周期数 ;
  wire [31:0] adder_1_out, adder_2_out, bit_extender_1_out, bit_extender_2_out, bit_extender_3_out,
       bit_extender_4_out, controlled_buffer_1_out, mips_alu_1_result, multiplexer_1_out, multiplexer_7_out,
       multiplexer_8_out, multiplexer_10_out, multiplexer_11_out, multiplexer_12_out, ram_1_data,
       target_offset, v0;

  Clock #(.highDuration(1), .lowDuration(1)) clock_1 ();  // open: out
  Button _1 (.out(IRA));
  Button _2 (.out(IRB));
  Button _3 (.out(IRC));
  Button \u_继续运行  (.out(Go));
  LED #(.active("true")) led_1 (.in(W1));
  LED #(.active("true")) led_2 (.in(W2));
  LED #(.active("true")) led_3 (.in(W3));
  Hex_Digit_Display hex_digit_display_1 (.value(LedData[31:28]));  // open: dp
  assign controlled_buffer_1_out = JR ? v0 : 32'bz;  // Controlled_Buffer controlled_buffer_1
  assign controlled_buffer_1_out = JMP ? {PC[31:28], IR[25:0], 2'b00} : 32'bz;  // Controlled_Buffer controlled_buffer_2
  assign controlled_buffer_1_out = Branch ? adder_1_out : 32'bz;  // Controlled_Buffer controlled_buffer_3
  Adder #(.width(32)) adder_1 (.a(adder_2_out), .b(target_offset), .out(adder_1_out));  // open: cin, cout
  Hex_Digit_Display hex_digit_display_2 (.value(LedData[27:24]));  // open: dp
  Hex_Digit_Display hex_digit_display_3 (.value(LedData[23:20]));  // open: dp
  or or_1 (or_1_out, JMP, JR, Branch);
  not not_1 (not_1_out, Pause);
  Counter #(.width(16), .max('hffff), .ongoal("wrap"), .trigger("rising"), .behavior("new")) counter_1 (
    .count(not_1_out), .Q(\总周期数 ), .clk(CLK));  // open: load, D, carry, clr, preset, down
  Hex_Digit_Display hex_digit_display_4 (.value(LedData[19:16]));  // open: dp
  Hex_Digit_Display hex_digit_display_5 (.value(LedData[15:12]));  // open: dp
  not not_2 (not_2_out, Pause);
  Multiplexer #(.select(1), .width(32), .disabled("Z"), .enable("false")) multiplexer_1 (
    .in0(adder_2_out), .in1(controlled_buffer_1_out), .out(multiplexer_1_out), .sel(or_1_out));
  Hex_Digit_Display hex_digit_display_6 (.value(LedData[7:4]));  // open: dp
  Hex_Digit_Display hex_digit_display_7 (.value(LedData[11:8]));  // open: dp
  // Probe on \总周期数 
  Register #(.width(32), .trigger("rising"), .Select("low")) u_PC (
    .D(multiplexer_1_out), .en(not_2_out), .Q(PC), .clk(CLK));  // open: clr
  Hex_Digit_Display hex_digit_display_8 (.value(LedData[3:0]));  // open: dp
  Adder #(.width(32)) adder_2 (.a(PC), .b(32'h4), .out(adder_2_out));  // open: cin, cout
  \单周期硬布线控制器  \u_单周期硬布线控制器_1  (
    .Func(IR[5:0]), .OP(IR[31:26]), .ALU_OP(AluOP), .MemToReg(MemToReg), .MemWrite(MemWrite),
    .ALU_SRC(AluSrc), .RegWrite(RegWrite), .SysCALL(Syscall), .SignedExt(SignedExt), .RegDst(RegDst),
    .JR(JR), .JMP(JMP), .Beq(BEQ), .JAL(JAL), .Bne(BNE), .SRAV(SRAV), .SUBU(SUBU), .LHU(LHU), .BGTZ(BGTZ));  // open: ERET, MFC0, MTC0, MF
  ROM #(.addrWidth(10), .dataWidth(32), .Select("high")) rom_1 (.addr(PC[11:2]), .data(IR));
  Keyboard #(.Char_bit_width(7), .buflen(32), .trigger("rising")) keyboard_1 ();  // open: clk, re, clr, avail, data
  or or_2 (IR1_t, IR1, IRA);
  // Mips_Probe mips_probe_1: pin names not known; wires that end beside it: IR
  or or_3 (IR2_t, IR2, IRB);
  Multiplexer #(.select(1), .width(5), .disabled("Z"), .enable("false")) multiplexer_2 (
    .in0(IR[20:16]), .in1(IR[15:11]), .out(multiplexer_2_out), .sel(RegDst));
  not not_3 (not_3_out, JAL);
  TTY #(.Char_bit_width(7), .rows(8), .cols(32), .trigger("rising")) tty_1 ();  // open: data, clk, we, clr
  not not_4 (not_4_out, Syscall);
  Multiplexer #(.select(1), .width(5), .disabled("Z"), .enable("false")) multiplexer_3 (
    .in0(5'b00010), .in1(IR[25:21]), .out(multiplexer_3_out), .sel(not_4_out));
  Multiplexer #(.select(1), .width(5), .disabled("Z"), .enable("false")) multiplexer_4 (
    .in0(5'b00100), .in1(IR[20:16]), .out(multiplexer_4_out), .sel(not_4_out));
  Multiplexer #(.select(1), .width(5), .disabled("Z"), .enable("false")) multiplexer_5 (
    .in0({5{1'b1}}), .in1(multiplexer_2_out), .out(multiplexer_5_out), .sel(not_3_out));
  Multiplexer #(.select(1), .width(32), .disabled("Z"), .enable("false")) multiplexer_6 (
    .in0(multiplexer_12_out), .in1(adder_2_out), .out(RDin), .sel(JAL));
  assign bit_extender_1_out = {{16{1'b0}}, IR[15:0]};  // Bit_Extender bit_extender_1
  assign bit_extender_2_out = {{16{IR[15]}}, IR[15:0]};  // Bit_Extender bit_extender_2
  or or_4 (IR3_t, IR3, IRC);
  Multiplexer #(.select(1), .width(32), .disabled("Z"), .enable("false")) multiplexer_7 (
    .in0(bit_extender_1_out), .in1(bit_extender_2_out), .out(multiplexer_7_out), .sel(SignedExt));
  MIPS_Regifile mips_regifile_1 (
    .Din(RDin), .Clk(CLK), .R1(v0), .R2(MDin), .WE(RegWrite), .W_num(multiplexer_5_out),
    .R1_num(multiplexer_3_out), .R2_num(multiplexer_4_out));
  Comparator #(.width(32), .mode("unsigned")) comparator_1 (.a(32'h22), .b(v0), .eq(comparator_1_eq));  // open: gt, lt
  Multiplexer #(.select(1), .width(32), .disabled("Z"), .enable("false")) multiplexer_8 (
    .in0(MDin), .in1(multiplexer_7_out), .out(multiplexer_8_out), .sel(AluSrc));
  Multiplexer #(.select(1), .width(5), .disabled("Z"), .enable("false")) multiplexer_9 (
    .in0(IR[10:6]), .in1(v0[4:0]), .out(multiplexer_9_out), .sel(SRAV));
  Shifter #(.width(32), .shift("ll")) shifter_1 (.in(multiplexer_7_out), .\dist (5'b00010), .out(target_offset));
  and and_1 (and_1_out, Syscall, comparator_1_eq);
  and and_2 (and_2_out, Syscall, ~comparator_1_eq);  // AND_Gate
  MIPS_ALU mips_alu_1 (
    .X(v0), .Y(multiplexer_8_out), .AluOP(AluOP), .Equal(mips_alu_1_equal), .Result(mips_alu_1_result),
    .shamt(multiplexer_9_out));  // open: Result_2
  Register #(.width(32), .trigger("falling"), .Select("low")) register_1 (
    .D(MDin), .Q(LedData), .clk(and_1_out));  // open: en, clr
  Register #(.width(1), .trigger("rising"), .Select("low")) register_2 (
    .D(and_2_out), .en(and_2_out), .Q(Pause), .clk(CLK), .clr(Go));
  Comparator #(.width(32), .mode("twosComplement")) comparator_2 (
    .a({32{1'b0}}), .b(v0), .lt(comparator_2_lt));  // open: gt, eq
  and and_3 (and_3_out, BEQ, mips_alu_1_equal);
  and and_4 (and_4_out, BNE, ~mips_alu_1_equal);  // AND_Gate
  and and_5 (and_5_out, BGTZ, comparator_2_lt);
  RAM #(.addrWidth(10), .dataWidth(32), .bus("separate"), .Select("high")) ram_1 (
    .addr(mips_alu_1_result[11:2]), .din(MDin), .data(ram_1_data), .str(MemWrite), .clk(CLK));  // open: sel, ld, clr
  D_Flip_Flop #(.trigger("high"), .Pre_Clr_Positions("LEGACY"), .NegatePresetClear("false"), .enable("true"), .NewFFLayout("false")) d_ff_1 (.Q(d_ff_1_q));  // open: clk, D, Qn, preset, en, reset
  or or_5 (Branch, and_3_out, and_4_out, and_5_out);
  Multiplexer #(.select(1), .width(32), .disabled("Z"), .enable("false")) multiplexer_10 (
    .in0(mips_alu_1_result), .in1(ram_1_data), .out(multiplexer_10_out), .sel(MemToReg));
  // Probe on 13'hc
  Clock #(.highDuration(1), .lowDuration(1)) clock_2 (.out(clock_2_out));
  assign bit_extender_3_out = {{16{1'b0}}, multiplexer_10_out[15:0]};  // Bit_Extender bit_extender_3
  Multiplexer #(.select(1), .width(32), .disabled("Z"), .enable("false")) multiplexer_11 (
    .in0(bit_extender_3_out), .in1(bit_extender_4_out), .out(multiplexer_11_out), .sel(mips_alu_1_result[1]));
  assign bit_extender_4_out = {{16{1'b0}}, multiplexer_10_out[31:16]};  // Bit_Extender bit_extender_4
  Comparator #(.width(13), .mode("twosComplement")) comparator_3 (
    .a(CNT_num), .b(13'hc), .eq(comparator_3_eq), .lt(comparator_3_lt));  // open: gt
  Multiplexer #(.select(1), .width(32), .disabled("Z"), .enable("false")) multiplexer_12 (
    .in0(multiplexer_10_out), .in1(multiplexer_11_out), .out(multiplexer_12_out), .sel(LHU));
  nand nand_1 (nand_1_out, d_ff_1_q, comparator_3_eq);
  Counter #(.width(13), .max('h1fff), .ongoal("stay"), .trigger("rising"), .behavior("old")) counter_2 (
    .count(comparator_3_lt), .Q(CNT_num), .clk(clock_2_out));  // open: load, D, carry, clr, preset
  assign CLK = nand_1_out ? clock_2_out : 1'bz;  // Controlled_Buffer controlled_buffer_4
  Pull_Resistor #(.pull(1)) pull_resistor_1 (.node(CLK));

  // Other names for the same wires on the sheet: a0[31:0] = MDin; Func[5:0] = IR[5:0]; index[25:0] = IR[25:0];
  //   Shamt[4:0] = IR[10:6]; OP[5:0] = IR[31:26]; PC31_28[3:0] = PC[31:28]

  // Notes on the sheet:
  //   中断源
  //   中断等待指示
  //   总复位信号应将除ROM以外所有存储组件全部清零
  //   数码管输出
  //   数码管输出应该用寄存器锁存，否则显示数据只能一闪而过
  //   JMP
  //   JR
  //   OP
  //   Func
  //   指令存储器
  //   Beq
  //   Bne
  //   MemToReg
  //   MemWrite
  //   AluOP
  //   AluSrcB
  //   RegWrite
  //   JAL
  //   RegDst
  //   Syscall
  //   contents of rom_1 (hex, n*v repeats v):
  //   20110001 8000c05 20110001 20120002 20130003 8000c09 20110001 20120002 20130003 8000c0d 20110001
  //   20120002 20130003 8000c11 20110001 20120002 20130003 c000cb8 20100001 20110001 118fc0 112020
  //   20020022 c 118882 12200001 8000c15 112020 20020022 c 20110001 118880 112020 20020022 c 12200001
  //   8000c1f 20110001 118fc0 112020 20020022 c 1188c3 112020 20020022 c 118903 112020 20020022 c 118903
  //   112020 20020022 c 118903 112020 20020022 c 118903 112020 20020022 c 118903 112020 20020022 c 118903
  //   112020 20020022 c 118903 112020 20020022 c 20100001 109fc0 139fc3 8021 2012000c 24160003 26100001
  //   3210000f 20080008 20090001 139900 2709825 132020 20020022 c 1094022 1500fff9 22100001 2018000f
  //   2188024 108700 20080008 20090001 139902 2709825 132021 20020022 c 1094022 1500fff9 108702 2c9b022
  //   12c00001 8000c50 4020 1084027 84400 3508ffff 82021 20020022 c 2010ffff 20110000 ae300000 22100001
  //   22310004 ae300000 22100001 22310004 ae300000 22100001 22310004 ae300000 22100001 22310004 ae300000
  //   22100001 22310004 ae300000 22100001 22310004 ae300000 22100001 22310004 ae300000 22100001 22310004
  //   ae300000 22100001 22310004 ae300000 22100001 22310004 ae300000 22100001 22310004 ae300000 22100001
  //   22310004 ae300000 22100001 22310004 ae300000 22100001 22310004 ae300000 22100001 22310004 ae300000
  //   22100001 22310004 22100001 8020 2011003c 8e130000 8e340000 274402a 11000002 ae330000 ae140000
  //   2231fffc 1611fff8 102020 20020022 c 22100004 2011003c 1611fff2 20020032 c 20100000 22100001 102020
  //   20020022 c 22100002 102020 20020022 c 22100003 102020 20020022 c 22100004 102020 20020022 c 22100005
  //   102020 20020022 c 22100006 102020 20020022 c 22100007 102020 20020022 c 22100008 102020 20020022
  //   20020022 c 3e00008
  //   OP
  //   Func
  //   指令字
  //   rs
  //   rt
  //   rd
  //   sa
  //   Imm
  //   instr_index
  //   为方便自动评测，需要输出PC，IR，寄存器堆写如数据RDin
  //   RAM写使能MemWrite、RAM写入数据MDin等信号
  //   控制位
  //   暂停节拍，不能为0
  //   用这个时钟源需要去掉电路中的其他时钟源
  //   戳工具置1进入计数暂停模式，ctrl+k时钟自动运行到对应节拍暂停
  //   ctrl+k关闭时钟连续运行，将控制位置零，进入单步调试模式调试
  //   可计数暂停的时钟源
endmodule

// 单周期硬布线控制器
module \单周期硬布线控制器  (
  input  [5:0] OP,
  input  [5:0] Func,
  input  [4:0] MF,
  output [3:0] ALU_OP,
  output MemToReg,
  output MemWrite,
  output ALU_SRC,
  output RegWrite,
  output SysCALL,
  output SignedExt,
  output RegDst,
  output Beq,
  output Bne,
  output JR,
  output JMP,
  output JAL,
  output SRAV,
  output SUBU,
  output LHU,
  output BGTZ,
  output MFC0,
  output MTC0,
  output ERET
);

  \运算控制器自动生成  \u_运算控制器自动生成_1  (
    .OP0(OP[0]), .OP1(OP[1]), .OP2(OP[2]), .OP3(OP[3]), .OP4(OP[4]), .OP5(OP[5]), .F0(Func[0]), .F1(Func[1]),
    .F2(Func[2]), .F3(Func[3]), .F4(Func[4]), .F5(Func[5]), .S0(ALU_OP[0]), .S1(ALU_OP[1]), .S2(ALU_OP[2]),
    .S3(ALU_OP[3]));
  \控制信号自动生成  \u_控制信号自动生成_1  (
    .OP0(OP[0]), .OP1(OP[1]), .OP2(OP[2]), .OP3(OP[3]), .OP4(OP[4]), .OP5(OP[5]), .F0(Func[0]), .F1(Func[1]),
    .F2(Func[2]), .F3(Func[3]), .F4(Func[4]), .F5(Func[5]), .MemToReg(MemToReg), .MemWrite(MemWrite),
    .ALU_SRC(ALU_SRC), .RegWrite(RegWrite), .SysCALL(SysCALL), .SignedExt(SignedExt), .RegDst(RegDst),
    .BEQ(Beq), .BNE(Bne), .JR(JR), .JUMP(JMP), .JAL(JAL), .SRAV(SRAV), .SUBU(SUBU), .LHU(LHU), .BGTZ(BGTZ));
  and and_1 (ERET, ~OP[0], ~OP[1], ~OP[2], ~OP[3], OP[4], ~OP[5], ~Func[0], ~Func[1], ~Func[2], Func[3], Func[4], ~Func[5]);  // AND_Gate
  and and_2 (MFC0, ~OP[0], ~OP[1], ~OP[2], ~OP[3], OP[4], ~OP[5], ~MF[0], ~MF[1], ~MF[2], ~MF[3], ~MF[4]);  // AND_Gate
  and and_3 (MTC0, ~OP[0], ~OP[1], ~OP[2], ~OP[3], OP[4], ~OP[5], ~MF[0], ~MF[1], MF[2], ~MF[3], ~MF[4]);  // AND_Gate

  // Other names for the same wires on the sheet: OP_CODE[5:0] = OP

  // Notes on the sheet:
  //   运算器控制器，根据指令生成运算器功能选择信号
endmodule

// 运算器控制器
module \运算控制器自动生成  (
  input  OP0,
  input  OP1,
  input  OP2,
  input  OP3,
  input  OP4,
  input  OP5,
  input  F0,
  input  F1,
  input  F2,
  input  F3,
  input  F4,
  input  F5,
  output S0,
  output S1,
  output S2,
  output S3
);

  wire and_1_out, and_2_out, and_3_out, and_4_out, and_5_out, and_6_out, and_7_out, and_8_out, and_9_out,
       and_10_out, and_11_out, and_12_out, and_13_out, and_14_out, and_15_out, and_16_out, and_17_out,
       and_18_out, and_19_out, and_20_out, and_21_out, and_22_out, and_23_out, and_24_out, and_25_out,
       and_26_out, not_1_out, not_2_out, not_3_out, not_4_out, not_5_out, not_6_out, not_7_out, not_8_out,
       not_9_out, not_10_out, not_11_out, not_12_out, not_13_out, not_14_out, not_15_out, not_16_out,
       not_17_out, not_18_out, not_19_out, not_20_out, not_21_out, not_22_out, not_23_out, not_24_out,
       not_25_out, not_26_out, not_27_out, not_28_out, not_29_out, not_30_out, not_31_out, not_32_out,
       not_33_out, not_34_out, not_35_out, not_36_out, not_37_out, not_38_out, not_39_out, not_40_out,
       not_41_out, not_42_out, not_43_out, not_44_out, not_45_out, not_46_out, not_47_out, not_48_out,
       not_49_out, not_50_out, not_51_out, not_52_out, not_53_out, not_54_out, not_55_out, not_56_out,
       not_57_out, not_58_out, not_59_out, not_60_out, not_61_out, not_62_out, not_63_out, not_64_out,
       not_65_out, not_66_out, not_67_out, not_68_out, not_69_out, not_70_out, not_71_out, not_72_out,
       not_73_out, not_74_out, not_75_out, not_76_out, not_77_out, not_78_out, not_79_out, not_80_out,
       not_81_out, not_82_out, not_83_out, not_84_out, not_85_out, not_86_out, not_87_out, not_88_out,
       not_89_out, not_90_out, not_91_out, not_92_out, not_93_out, not_94_out, not_95_out, not_96_out,
       not_97_out, not_98_out, not_99_out, not_100_out, not_101_out, not_102_out, not_103_out, not_104_out,
       not_105_out, not_106_out, not_107_out, not_108_out, not_109_out, not_110_out, not_111_out,
       not_112_out, not_113_out, not_114_out, not_115_out, not_116_out, not_117_out, not_118_out,
       not_119_out, not_120_out, not_121_out, not_122_out, not_123_out, not_124_out, not_125_out,
       not_126_out, not_127_out, not_128_out, not_129_out, not_130_out, not_131_out, not_132_out,
       not_133_out, not_134_out, not_135_out, not_136_out, not_137_out, not_138_out, not_139_out,
       not_140_out, not_141_out, not_142_out, not_143_out, not_144_out, not_145_out, not_146_out,
       not_147_out, not_148_out, not_149_out, not_150_out, not_151_out, not_152_out, not_153_out,
       not_154_out, not_155_out, not_156_out;

  not not_1 (not_1_out, OP0);
  not not_2 (not_2_out, OP1);
  not not_3 (not_3_out, OP2);
  not not_4 (not_4_out, OP4);
  not not_5 (not_5_out, OP5);
  not not_6 (not_6_out, F0);
  not not_7 (not_7_out, F1);
  not not_8 (not_8_out, F3);
  not not_9 (not_9_out, F4);
  not not_10 (not_10_out, OP0);
  not not_11 (not_11_out, OP1);
  not not_12 (not_12_out, OP2);
  not not_13 (not_13_out, OP4);
  not not_14 (not_14_out, OP5);
  not not_15 (not_15_out, F1);
  not not_16 (not_16_out, F2);
  not not_17 (not_17_out, F3);
  not not_18 (not_18_out, F4);
  not not_19 (not_19_out, OP0);
  not not_20 (not_20_out, OP1);
  not not_21 (not_21_out, OP2);
  not not_22 (not_22_out, OP4);
  not not_23 (not_23_out, OP5);
  not not_24 (not_24_out, F0);
  not not_25 (not_25_out, F2);
  not not_26 (not_26_out, F4);
  not not_27 (not_27_out, OP0);
  not not_28 (not_28_out, OP1);
  not not_29 (not_29_out, OP2);
  not not_30 (not_30_out, OP4);
  not not_31 (not_31_out, OP5);
  not not_32 (not_32_out, F3);
  not not_33 (not_33_out, F4);
  not not_34 (not_34_out, F5);
  not not_35 (not_35_out, OP0);
  not not_36 (not_36_out, OP1);
  not not_37 (not_37_out, OP4);
  not not_38 (not_38_out, OP5);
  not not_39 (not_39_out, OP0);
  not not_40 (not_40_out, OP2);
  not not_41 (not_41_out, OP4);
  not not_42 (not_42_out, OP5);
  not not_43 (not_43_out, OP1);
  not not_44 (not_44_out, OP2);
  not not_45 (not_45_out, OP4);
  not not_46 (not_46_out, OP5);
  not not_47 (not_47_out, OP1);
  not not_48 (not_48_out, OP3);
  not not_49 (not_49_out, OP4);
  not not_50 (not_50_out, OP2);
  not not_51 (not_51_out, OP4);
  not not_52 (not_52_out, OP0);
  not not_53 (not_53_out, OP1);
  not not_54 (not_54_out, OP2);
  not not_55 (not_55_out, OP3);
  not not_56 (not_56_out, OP4);
  not not_57 (not_57_out, OP5);
  not not_58 (not_58_out, F0);
  not not_59 (not_59_out, F1);
  not not_60 (not_60_out, F3);
  not not_61 (not_61_out, F4);
  not not_62 (not_62_out, OP0);
  not not_63 (not_63_out, OP1);
  not not_64 (not_64_out, OP2);
  not not_65 (not_65_out, OP3);
  not not_66 (not_66_out, OP4);
  not not_67 (not_67_out, OP5);
  not not_68 (not_68_out, F0);
  not not_69 (not_69_out, F2);
  not not_70 (not_70_out, F3);
  not not_71 (not_71_out, F4);
  not not_72 (not_72_out, OP0);
  not not_73 (not_73_out, OP1);
  not not_74 (not_74_out, OP2);
  not not_75 (not_75_out, OP3);
  not not_76 (not_76_out, OP4);
  not not_77 (not_77_out, OP5);
  not not_78 (not_78_out, F0);
  not not_79 (not_79_out, F2);
  not not_80 (not_80_out, F4);
  not not_81 (not_81_out, OP0);
  not not_82 (not_82_out, OP1);
  not not_83 (not_83_out, OP2);
  not not_84 (not_84_out, OP3);
  not not_85 (not_85_out, OP4);
  not not_86 (not_86_out, OP5);
  not not_87 (not_87_out, F3);
  not not_88 (not_88_out, F4);
  not not_89 (not_89_out, OP0);
  not not_90 (not_90_out, OP1);
  not not_91 (not_91_out, OP4);
  not not_92 (not_92_out, OP5);
  not not_93 (not_93_out, OP0);
  not not_94 (not_94_out, OP2);
  not not_95 (not_95_out, OP4);
  not not_96 (not_96_out, OP5);
  not not_97 (not_97_out, OP0);
  not not_98 (not_98_out, OP1);
  not not_99 (not_99_out, OP2);
  not not_100 (not_100_out, OP4);
  not not_101 (not_101_out, OP5);
  not not_102 (not_102_out, F0);
  not not_103 (not_103_out, F1);
  not not_104 (not_104_out, F3);
  not not_105 (not_105_out, F4);
  not not_106 (not_106_out, OP0);
  not not_107 (not_107_out, OP1);
  not not_108 (not_108_out, OP2);
  not not_109 (not_109_out, OP4);
  not not_110 (not_110_out, OP5);
  not not_111 (not_111_out, F2);
  not not_112 (not_112_out, F3);
  not not_113 (not_113_out, F4);
  not not_114 (not_114_out, OP0);
  not not_115 (not_115_out, OP1);
  not not_116 (not_116_out, OP2);
  not not_117 (not_117_out, OP4);
  not not_118 (not_118_out, OP5);
  not not_119 (not_119_out, F2);
  not not_120 (not_120_out, F4);
  not not_121 (not_121_out, OP0);
  not not_122 (not_122_out, OP1);
  not not_123 (not_123_out, OP4);
  not not_124 (not_124_out, OP5);
  not not_125 (not_125_out, OP1);
  not not_126 (not_126_out, OP2);
  not not_127 (not_127_out, OP4);
  not not_128 (not_128_out, OP5);
  not not_129 (not_129_out, OP1);
  not not_130 (not_130_out, OP3);
  not not_131 (not_131_out, OP4);
  not not_132 (not_132_out, OP2);
  not not_133 (not_133_out, OP4);
  not not_134 (not_134_out, OP0);
  not not_135 (not_135_out, OP1);
  not not_136 (not_136_out, OP2);
  not not_137 (not_137_out, OP3);
  not not_138 (not_138_out, OP4);
  not not_139 (not_139_out, OP5);
  not not_140 (not_140_out, F2);
  not not_141 (not_141_out, F4);
  not not_142 (not_142_out, OP0);
  not not_143 (not_143_out, OP1);
  not not_144 (not_144_out, OP2);
  not not_145 (not_145_out, OP3);
  not not_146 (not_146_out, OP4);
  not not_147 (not_147_out, OP5);
  not not_148 (not_148_out, F3);
  not not_149 (not_149_out, F4);
  not not_150 (not_150_out, OP0);
  not not_151 (not_151_out, OP2);
  not not_152 (not_152_out, OP4);
  not not_153 (not_153_out, OP5);
  not not_154 (not_154_out, OP1);
  not not_155 (not_155_out, OP4);
  not not_156 (not_156_out, OP5);
  and and_1 (and_1_out, not_1_out, not_2_out, not_3_out, not_4_out, not_5_out, not_6_out, not_7_out, not_8_out, not_9_out, F5);
  and and_2 (and_2_out, not_10_out, not_11_out, not_12_out, not_13_out, not_14_out, not_15_out, not_16_out, not_17_out, not_18_out, F5);
  and and_3 (and_3_out, not_19_out, not_20_out, not_21_out, not_22_out, not_23_out, not_24_out, F1, not_25_out, F3, not_26_out, F5);
  and and_4 (and_4_out, not_27_out, not_28_out, not_29_out, not_30_out, not_31_out, F0, F1, not_32_out, not_33_out, not_34_out);
  and and_5 (and_5_out, not_35_out, not_36_out, OP3, not_37_out, not_38_out);
  and and_6 (and_6_out, not_39_out, not_40_out, OP3, not_41_out, not_42_out);
  and and_7 (and_7_out, not_43_out, not_44_out, OP3, not_45_out, not_46_out);
  and and_8 (and_8_out, OP0, not_47_out, OP2, not_48_out, not_49_out, OP5);
  and and_9 (and_9_out, OP0, OP1, not_50_out, not_51_out, OP5);
  and and_10 (and_10_out, not_52_out, not_53_out, not_54_out, not_55_out, not_56_out, not_57_out, not_58_out, not_59_out, F2, not_60_out, not_61_out, F5);
  and and_11 (and_11_out, not_62_out, not_63_out, not_64_out, not_65_out, not_66_out, not_67_out, not_68_out, F1, not_69_out, not_70_out, not_71_out);
  and and_12 (and_12_out, not_72_out, not_73_out, not_74_out, not_75_out, not_76_out, not_77_out, not_78_out, F1, not_79_out, not_80_out, F5);
  and and_13 (and_13_out, not_81_out, not_82_out, not_83_out, not_84_out, not_85_out, not_86_out, F0, F1, not_87_out, not_88_out, F5);
  and and_14 (and_14_out, not_89_out, not_90_out, OP2, OP3, not_91_out, not_92_out);
  and and_15 (and_15_out, not_93_out, OP1, not_94_out, OP3, not_95_out, not_96_out);
  and and_16 (and_16_out, not_97_out, not_98_out, not_99_out, not_100_out, not_101_out, not_102_out, not_103_out, not_104_out, not_105_out, F5);
  and and_17 (and_17_out, not_106_out, not_107_out, not_108_out, not_109_out, not_110_out, not_111_out, not_112_out, not_113_out, F5);
  and and_18 (and_18_out, not_114_out, not_115_out, not_116_out, not_117_out, not_118_out, F0, F1, not_119_out, not_120_out, F5);
  and and_19 (and_19_out, not_121_out, not_122_out, OP3, not_123_out, not_124_out);
  and and_20 (and_20_out, not_125_out, not_126_out, OP3, not_127_out, not_128_out);
  and and_21 (and_21_out, OP0, not_129_out, OP2, not_130_out, not_131_out, OP5);
  and and_22 (and_22_out, OP0, OP1, not_132_out, not_133_out, OP5);
  and and_23 (and_23_out, not_134_out, not_135_out, not_136_out, not_137_out, not_138_out, not_139_out, F1, not_140_out, F3, not_141_out, F5);
  and and_24 (and_24_out, not_142_out, not_143_out, not_144_out, not_145_out, not_146_out, not_147_out, F0, F2, not_148_out, not_149_out, F5);
  and and_25 (and_25_out, not_150_out, OP1, not_151_out, OP3, not_152_out, not_153_out);
  and and_26 (and_26_out, OP0, not_154_out, OP2, OP3, not_155_out, not_156_out);
  or or_1 (S0, and_1_out, and_2_out, and_3_out, and_4_out, and_5_out, and_6_out, and_7_out, and_8_out, and_9_out);
  or or_2 (S1, and_10_out, and_11_out, and_12_out, and_13_out, and_14_out, and_15_out);
  or or_3 (S2, and_16_out, and_17_out, and_18_out, and_19_out, and_20_out, and_21_out, and_22_out);
  or or_4 (S3, and_23_out, and_24_out, and_25_out, and_26_out);
endmodule

// 控制信号生成
module \控制信号自动生成  (
  input  OP0,
  input  OP1,
  input  OP2,
  input  OP3,
  input  OP4,
  input  OP5,
  input  F0,
  input  F1,
  input  F2,
  input  F3,
  input  F4,
  input  F5,
  output MemToReg,
  output MemWrite,
  output ALU_SRC,
  output RegWrite,
  output SysCALL,
  output SignedExt,
  output RegDst,
  output BEQ,
  output BNE,
  output JR,
  output JUMP,
  output JAL,
  output SRAV,
  output SUBU,
  output LHU,
  output BGTZ
);

  wire and_1_out, and_2_out, and_4_out, and_5_out, and_6_out, and_7_out, and_8_out, and_9_out, and_10_out,
       and_11_out, and_12_out, and_13_out, and_14_out, and_15_out, and_17_out, and_18_out, and_19_out,
       and_20_out, and_21_out, and_22_out, and_23_out, and_24_out, not_1_out, not_2_out, not_3_out,
       not_4_out, not_5_out, not_6_out, not_7_out, not_8_out, not_9_out, not_10_out, not_11_out, not_12_out,
       not_13_out, not_14_out, not_15_out, not_16_out, not_17_out, not_18_out, not_19_out, not_20_out,
       not_21_out, not_22_out, not_23_out, not_24_out, not_25_out, not_26_out, not_27_out, not_28_out,
       not_29_out, not_30_out, not_31_out, not_32_out, not_33_out, not_34_out, not_35_out, not_36_out,
       not_37_out, not_38_out, not_39_out, not_40_out, not_41_out, not_42_out, not_43_out, not_44_out,
       not_45_out, not_46_out, not_47_out, not_48_out, not_49_out, not_50_out, not_51_out, not_52_out,
       not_53_out, not_54_out, not_55_out, not_56_out, not_57_out, not_58_out, not_59_out, not_60_out,
       not_61_out, not_62_out, not_63_out, not_64_out, not_65_out, not_66_out, not_67_out, not_68_out,
       not_69_out, not_70_out, not_71_out, not_72_out, not_73_out, not_74_out, not_75_out, not_76_out,
       not_77_out, not_78_out, not_79_out, not_80_out, not_81_out, not_82_out, not_83_out, not_84_out,
       not_85_out, not_86_out, not_87_out, not_88_out, not_89_out, not_90_out, not_91_out, not_92_out,
       not_93_out, not_94_out, not_95_out, not_96_out, not_97_out, not_98_out, not_99_out, not_100_out,
       not_101_out, not_102_out, not_103_out, not_104_out, not_105_out, not_106_out, not_107_out,
       not_108_out, not_109_out, not_110_out, not_111_out, not_112_out, not_113_out, not_114_out,
       not_115_out, not_116_out, not_117_out, not_118_out, not_119_out, not_120_out, not_121_out,
       not_122_out, not_123_out, not_124_out, not_125_out, not_126_out, not_127_out, not_128_out,
       not_129_out, not_130_out, not_131_out, not_132_out, not_133_out, not_134_out, not_135_out,
       not_136_out, not_137_out, not_138_out, not_139_out, not_140_out, not_141_out, not_142_out,
       not_143_out, not_144_out, not_145_out, not_146_out, not_147_out, not_148_out, not_149_out,
       not_150_out, not_151_out, not_152_out, not_153_out, not_154_out, not_155_out, not_156_out,
       not_157_out, not_158_out, not_159_out, not_160_out, not_161_out, not_162_out, not_163_out,
       not_164_out, not_165_out, not_166_out, not_167_out, not_168_out, not_169_out, not_170_out,
       not_171_out, not_172_out, not_173_out, not_174_out, not_175_out, not_176_out;

  not not_1 (not_1_out, OP1);
  not not_2 (not_2_out, OP3);
  not not_3 (not_3_out, OP4);
  not not_4 (not_4_out, OP2);
  not not_5 (not_5_out, OP3);
  not not_6 (not_6_out, OP4);
  not not_7 (not_7_out, OP2);
  not not_8 (not_8_out, OP4);
  not not_9 (not_9_out, OP0);
  not not_10 (not_10_out, OP2);
  not not_11 (not_11_out, OP4);
  not not_12 (not_12_out, OP5);
  not not_13 (not_13_out, OP1);
  not not_14 (not_14_out, OP4);
  not not_15 (not_15_out, OP5);
  not not_16 (not_16_out, OP1);
  not not_17 (not_17_out, OP3);
  not not_18 (not_18_out, OP4);
  not not_19 (not_19_out, OP2);
  not not_20 (not_20_out, OP4);
  not not_21 (not_21_out, OP0);
  not not_22 (not_22_out, OP1);
  not not_23 (not_23_out, OP2);
  not not_24 (not_24_out, OP4);
  not not_25 (not_25_out, OP5);
  not not_26 (not_26_out, F0);
  not not_27 (not_27_out, F2);
  not not_28 (not_28_out, F3);
  not not_29 (not_29_out, F4);
  not not_30 (not_30_out, OP0);
  not not_31 (not_31_out, OP1);
  not not_32 (not_32_out, OP2);
  not not_33 (not_33_out, OP4);
  not not_34 (not_34_out, OP5);
  not not_35 (not_35_out, F1);
  not not_36 (not_36_out, F3);
  not not_37 (not_37_out, F4);
  not not_38 (not_38_out, OP0);
  not not_39 (not_39_out, OP1);
  not not_40 (not_40_out, OP2);
  not not_41 (not_41_out, OP4);
  not not_42 (not_42_out, OP5);
  not not_43 (not_43_out, F2);
  not not_44 (not_44_out, F4);
  not not_45 (not_45_out, OP0);
  not not_46 (not_46_out, OP1);
  not not_47 (not_47_out, OP2);
  not not_48 (not_48_out, OP4);
  not not_49 (not_49_out, OP5);
  not not_50 (not_50_out, F3);
  not not_51 (not_51_out, F4);
  not not_52 (not_52_out, OP0);
  not not_53 (not_53_out, OP2);
  not not_54 (not_54_out, OP4);
  not not_55 (not_55_out, OP5);
  not not_56 (not_56_out, OP1);
  not not_57 (not_57_out, OP4);
  not not_58 (not_58_out, OP5);
  not not_59 (not_59_out, OP1);
  not not_60 (not_60_out, OP3);
  not not_61 (not_61_out, OP4);
  not not_62 (not_62_out, OP2);
  not not_63 (not_63_out, OP3);
  not not_64 (not_64_out, OP4);
  not not_65 (not_65_out, OP0);
  not not_66 (not_66_out, OP1);
  not not_67 (not_67_out, OP2);
  not not_68 (not_68_out, OP3);
  not not_69 (not_69_out, OP4);
  not not_70 (not_70_out, OP5);
  not not_71 (not_71_out, F0);
  not not_72 (not_72_out, F1);
  not not_73 (not_73_out, F4);
  not not_74 (not_74_out, F5);
  not not_75 (not_75_out, OP0);
  not not_76 (not_76_out, OP2);
  not not_77 (not_77_out, OP4);
  not not_78 (not_78_out, OP5);
  not not_79 (not_79_out, OP1);
  not not_80 (not_80_out, OP2);
  not not_81 (not_81_out, OP4);
  not not_82 (not_82_out, OP5);
  not not_83 (not_83_out, OP1);
  not not_84 (not_84_out, OP3);
  not not_85 (not_85_out, OP4);
  not not_86 (not_86_out, OP5);
  not not_87 (not_87_out, OP3);
  not not_88 (not_88_out, OP4);
  not not_89 (not_89_out, OP5);
  not not_90 (not_90_out, OP0);
  not not_91 (not_91_out, OP1);
  not not_92 (not_92_out, OP2);
  not not_93 (not_93_out, OP3);
  not not_94 (not_94_out, OP4);
  not not_95 (not_95_out, OP5);
  not not_96 (not_96_out, F0);
  not not_97 (not_97_out, F2);
  not not_98 (not_98_out, F3);
  not not_99 (not_99_out, F4);
  not not_100 (not_100_out, OP0);
  not not_101 (not_101_out, OP1);
  not not_102 (not_102_out, OP2);
  not not_103 (not_103_out, OP3);
  not not_104 (not_104_out, OP4);
  not not_105 (not_105_out, OP5);
  not not_106 (not_106_out, F1);
  not not_107 (not_107_out, F3);
  not not_108 (not_108_out, F4);
  not not_109 (not_109_out, OP0);
  not not_110 (not_110_out, OP1);
  not not_111 (not_111_out, OP2);
  not not_112 (not_112_out, OP3);
  not not_113 (not_113_out, OP4);
  not not_114 (not_114_out, OP5);
  not not_115 (not_115_out, F2);
  not not_116 (not_116_out, F4);
  not not_117 (not_117_out, OP0);
  not not_118 (not_118_out, OP1);
  not not_119 (not_119_out, OP2);
  not not_120 (not_120_out, OP3);
  not not_121 (not_121_out, OP4);
  not not_122 (not_122_out, OP5);
  not not_123 (not_123_out, F3);
  not not_124 (not_124_out, F4);
  not not_125 (not_125_out, OP0);
  not not_126 (not_126_out, OP1);
  not not_127 (not_127_out, OP3);
  not not_128 (not_128_out, OP4);
  not not_129 (not_129_out, OP5);
  not not_130 (not_130_out, OP1);
  not not_131 (not_131_out, OP3);
  not not_132 (not_132_out, OP4);
  not not_133 (not_133_out, OP5);
  not not_134 (not_134_out, OP0);
  not not_135 (not_135_out, OP1);
  not not_136 (not_136_out, OP2);
  not not_137 (not_137_out, OP3);
  not not_138 (not_138_out, OP4);
  not not_139 (not_139_out, OP5);
  not not_140 (not_140_out, F0);
  not not_141 (not_141_out, F1);
  not not_142 (not_142_out, F2);
  not not_143 (not_143_out, F4);
  not not_144 (not_144_out, F5);
  not not_145 (not_145_out, OP2);
  not not_146 (not_146_out, OP3);
  not not_147 (not_147_out, OP4);
  not not_148 (not_148_out, OP5);
  not not_149 (not_149_out, OP2);
  not not_150 (not_150_out, OP3);
  not not_151 (not_151_out, OP4);
  not not_152 (not_152_out, OP5);
  not not_153 (not_153_out, OP0);
  not not_154 (not_154_out, OP1);
  not not_155 (not_155_out, OP2);
  not not_156 (not_156_out, OP3);
  not not_157 (not_157_out, OP4);
  not not_158 (not_158_out, OP5);
  not not_159 (not_159_out, F3);
  not not_160 (not_160_out, F4);
  not not_161 (not_161_out, F5);
  not not_162 (not_162_out, OP0);
  not not_163 (not_163_out, OP1);
  not not_164 (not_164_out, OP2);
  not not_165 (not_165_out, OP3);
  not not_166 (not_166_out, OP4);
  not not_167 (not_167_out, OP5);
  not not_168 (not_168_out, F2);
  not not_169 (not_169_out, F3);
  not not_170 (not_170_out, F4);
  not not_171 (not_171_out, OP1);
  not not_172 (not_172_out, OP3);
  not not_173 (not_173_out, OP4);
  not not_174 (not_174_out, OP3);
  not not_175 (not_175_out, OP4);
  not not_176 (not_176_out, OP5);
  and and_1 (and_1_out, OP0, not_1_out, OP2, not_2_out, not_3_out, OP5);
  and and_2 (and_2_out, OP0, OP1, not_4_out, not_5_out, not_6_out, OP5);
  and and_3 (MemWrite, OP0, OP1, not_7_out, OP3, not_8_out, OP5);
  and and_4 (and_4_out, not_9_out, not_10_out, OP3, not_11_out, not_12_out);
  and and_5 (and_5_out, not_13_out, OP3, not_14_out, not_15_out);
  and and_6 (and_6_out, OP0, not_16_out, OP2, not_17_out, not_18_out, OP5);
  and and_7 (and_7_out, OP0, OP1, not_19_out, not_20_out, OP5);
  and and_8 (and_8_out, not_21_out, not_22_out, not_23_out, not_24_out, not_25_out, not_26_out, not_27_out, not_28_out, not_29_out);
  and and_9 (and_9_out, not_30_out, not_31_out, not_32_out, not_33_out, not_34_out, not_35_out, not_36_out, not_37_out, F5);
  and and_10 (and_10_out, not_38_out, not_39_out, not_40_out, not_41_out, not_42_out, F1, not_43_out, not_44_out, F5);
  and and_11 (and_11_out, not_45_out, not_46_out, not_47_out, not_48_out, not_49_out, F0, F1, not_50_out, not_51_out);
  and and_12 (and_12_out, not_52_out, not_53_out, OP3, not_54_out, not_55_out);
  and and_13 (and_13_out, not_56_out, OP3, not_57_out, not_58_out);
  and and_14 (and_14_out, OP0, not_59_out, OP2, not_60_out, not_61_out, OP5);
  and and_15 (and_15_out, OP0, OP1, not_62_out, not_63_out, not_64_out);
  and and_16 (SysCALL, not_65_out, not_66_out, not_67_out, not_68_out, not_69_out, not_70_out, not_71_out, not_72_out, F2, F3, not_73_out, not_74_out);
  and and_17 (and_17_out, not_75_out, not_76_out, OP3, not_77_out, not_78_out);
  and and_18 (and_18_out, not_79_out, not_80_out, OP3, not_81_out, not_82_out);
  and and_19 (and_19_out, not_83_out, OP2, not_84_out, not_85_out, not_86_out);
  and and_20 (and_20_out, OP0, OP2, not_87_out, not_88_out, not_89_out);
  and and_21 (and_21_out, not_90_out, not_91_out, not_92_out, not_93_out, not_94_out, not_95_out, not_96_out, not_97_out, not_98_out, not_99_out);
  and and_22 (and_22_out, not_100_out, not_101_out, not_102_out, not_103_out, not_104_out, not_105_out, not_106_out, not_107_out, not_108_out, F5);
  and and_23 (and_23_out, not_109_out, not_110_out, not_111_out, not_112_out, not_113_out, not_114_out, F1, not_115_out, not_116_out, F5);
  and and_24 (and_24_out, not_117_out, not_118_out, not_119_out, not_120_out, not_121_out, not_122_out, F0, F1, not_123_out, not_124_out);
  and and_25 (BEQ, not_125_out, not_126_out, OP2, not_127_out, not_128_out, not_129_out);
  and and_26 (BNE, OP0, not_130_out, OP2, not_131_out, not_132_out, not_133_out);
  and and_27 (JR, not_134_out, not_135_out, not_136_out, not_137_out, not_138_out, not_139_out, not_140_out, not_141_out, not_142_out, F3, not_143_out, not_144_out);
  and and_28 (JUMP, OP1, not_145_out, not_146_out, not_147_out, not_148_out);
  and and_29 (JAL, OP0, OP1, not_149_out, not_150_out, not_151_out, not_152_out);
  and and_30 (SRAV, not_153_out, not_154_out, not_155_out, not_156_out, not_157_out, not_158_out, F0, F1, F2, not_159_out, not_160_out, not_161_out);
  and and_31 (SUBU, not_162_out, not_163_out, not_164_out, not_165_out, not_166_out, not_167_out, F0, F1, not_168_out, not_169_out, not_170_out, F5);
  and and_32 (LHU, OP0, not_171_out, OP2, not_172_out, not_173_out, OP5);
  and and_33 (BGTZ, OP0, OP1, OP2, not_174_out, not_175_out, not_176_out);
  or or_1 (MemToReg, and_1_out, and_2_out);
  or or_2 (ALU_SRC, and_4_out, and_5_out, and_6_out, and_7_out);
  or or_3 (RegWrite, and_8_out, and_9_out, and_10_out, and_11_out, and_12_out, and_13_out, and_14_out, and_15_out);
  or or_4 (SignedExt, and_17_out, and_18_out, and_19_out, and_20_out);
  or or_5 (RegDst, and_21_out, and_22_out, and_23_out, and_24_out);
endmodule

// ALU
module MIPS_ALU (
  input  [4:0] shamt,
  input  [31:0] X,
  input  [31:0] Y,
  input  [3:0] AluOP,
  output Equal,
  output [31:0] Result,
  output [31:0] Result_2
);

  wire [0:0] comparator_1_lt, comparator_2_lt;
  wire [31:0] adder_1_out, AND_out, divider_1_out, divider_1_rem, multiplier_1_cout, multiplier_1_out,
       NOR_out, OR_out, shifter_1_out, shifter_2_out, shifter_3_out, subtractor_1_out, XOR_out;

  assign AND_out = X & Y;  // AND_Gate AND, 32 bits wide
  assign OR_out = X | Y;  // OR_Gate OR, 32 bits wide
  Shifter #(.width(32), .shift("ll")) shifter_1 (.in(Y), .\dist (shamt), .out(shifter_1_out));
  Shifter #(.width(32), .shift("ar")) shifter_2 (.in(Y), .\dist (shamt), .out(shifter_2_out));
  Shifter #(.width(32), .shift("lr")) shifter_3 (.in(Y), .\dist (shamt), .out(shifter_3_out));
  Multiplier #(.width(32)) multiplier_1 (.a(X), .b(Y), .out(multiplier_1_out), .cout(multiplier_1_cout));  // open: cin
  Divider #(.width(32)) divider_1 (.a(X), .b(Y), .out(divider_1_out), .rem(divider_1_rem));  // open: upper
  Adder #(.width(32)) adder_1 (.a(X), .b(Y), .out(adder_1_out));  // open: cin, cout
  Subtractor #(.width(32)) subtractor_1 (.a(X), .b(Y), .out(subtractor_1_out));  // open: bin, bout
  assign XOR_out = X ^ Y;  // XOR_Gate XOR, 32 bits wide
  assign NOR_out = ~(X | Y);  // NOR_Gate NOR, 32 bits wide
  Comparator #(.width(32), .mode("twosComplement")) comparator_1 (
    .a(X), .b(Y), .eq(Equal), .lt(comparator_1_lt[0]));  // open: gt
  Comparator #(.width(32), .mode("unsigned")) comparator_2 (.a(X), .b(Y), .lt(comparator_2_lt[0]));  // open: gt, eq
  Multiplexer #(.select(4), .width(32), .disabled("Z"), .enable("false")) multiplexer_1 (
    .in0(shifter_1_out), .in1(shifter_2_out), .in2(shifter_3_out), .in3(multiplier_1_out),
    .in4(divider_1_out), .in5(adder_1_out), .in6(subtractor_1_out), .in7(AND_out), .in8(OR_out),
    .in9(XOR_out), .in10(NOR_out), .in11({{31{1'b0}}, comparator_1_lt[0]}),
    .in12({{31{1'b0}}, comparator_2_lt[0]}), .in13({32{1'b0}}), .in14({32{1'b0}}), .in15({32{1'b0}}),
    .out(Result), .sel(AluOP));
  Multiplexer #(.select(4), .width(32), .disabled("Z"), .enable("false")) multiplexer_2 (
    .in0({32{1'b0}}), .in1({32{1'b0}}), .in2({32{1'b0}}), .in3(multiplier_1_cout), .in4(divider_1_rem),
    .in5({32{1'b0}}), .in6({32{1'b0}}), .in7({32{1'b0}}), .in8({32{1'b0}}), .in9({32{1'b0}}),
    .in10({32{1'b0}}), .in11({32{1'b0}}), .in12({32{1'b0}}), .in13({32{1'b0}}), .in14({32{1'b0}}),
    .in15({32{1'b0}}), .out(Result_2), .sel(AluOP));

  // Other names for the same wires on the sheet: Result2[31:0] = Result_2; S[3:0] = AluOP

  // Notes on the sheet:
  //   不要改变此引脚区域内容，也不要改变ALU封装形式
  //   输入引脚
  //   输出引脚
endmodule

module MIPS_Regifile (
  input  [31:0] Din,
  input  Clk,
  input  WE,
  input  [4:0] R1_num,
  input  [4:0] W_num,
  input  [4:0] R2_num,
  output [31:0] R1,
  output [31:0] R2
);

  // RegisterFile registerfile_1: pin names not known; wires that end beside it: Din, Clk, WE, W_num, R1_num, R2_num, R1, R2
endmodule

module \理想流水线  (
  output RegWrite,
  output MemWrite,
  output [31:0] IF_PC,
  output [31:0] ID_PC,
  output [31:0] EX_PC,
  output [31:0] M_PC,
  output [31:0] WB_PC,
  output [31:0] RDin,
  output [31:0] MDin,
  output [31:0] LedData
);

  wire AluSrc, and_1_out, and_2_out, BEQ, BGTZ, BNE, CLK, clock_1_out, clock_2_out, comparator_1_eq,
       comparator_1_lt, comparator_2_eq, d_ff_1_q, EX_AluSrc, EX_SRAV, Go, id_ex_1_lhu_2,
       id_ex_1_memtoreg_out, id_ex_1_memwrite_2, id_ex_1_regdst_out, id_ex_1_regwrite_out,
       id_ex_1_syscall_out, id_ex_2_lhu_2, id_ex_2_memtoreg_out, id_ex_2_regdst_out, id_ex_2_regwrite_out,
       id_ex_2_syscall_out, IR1, IR2, IR3, JAL, JMP, JR, LHU, MemToReg, MemWrite_t, nand_1_out, not_1_out,
       not_2_out, not_3_out, Pause, RegDst, RegW, RST, SignedExt, SRAV, SUBU, Syscall, W1, W2, W3, WB_LHU,
       WB_MemtoReg, WB_RegDst, WB_Syscall;
  wire [3:0] AluOP, EX_AluOP;
  wire [4:0] id_ex_1_a_out, id_ex_1_shamt_2, multiplexer_1_out, multiplexer_2_out, multiplexer_5_out,
       multiplexer_6_out;
  wire [12:0] CNT_num;
  wire [15:0] \LoadUse次数 , \总周期数 , \插入气泡数 , \无条件分支数 , \条件分支成功数 ;
  wire [31:0] adder_1_out, bit_extender_1_out, bit_extender_2_out, bit_extender_3_out, bit_extender_4_out,
       EX_IR, id_ex_1_b_out, id_ex_1_imm_out, id_ex_2_a_out, id_ex_2_alu_out, id_ex_3_a_out, id_ex_3_alu_out,
       id_ex_3_b_out, id_ex_3_md_out, ID_IR, IF_IR, MEM_IR, mips_alu_1_result, mips_regifile_1_r1,
       mips_regifile_1_r2, multiplexer_3_out, multiplexer_4_out, multiplexer_7_out, multiplexer_8_out,
       ram_1_data, WB_IR;
  wire [31:5] id_ex_1_a_out_2;

  Button \u_总复位  (.out(RST));
  Button _1 (.out(IR1));
  Button _2 (.out(IR2));
  Button _3 (.out(IR3));
  // Probe on \总周期数 
  // Probe on \总周期数 
  not not_1 (not_1_out, Pause);
  Button \u_继续运行  (.out(Go));
  LED #(.active("true")) led_1 (.in(W1));
  LED #(.active("true")) led_2 (.in(W2));
  LED #(.active("true")) led_3 (.in(W3));
  not not_2 (not_2_out, Pause);
  Counter #(.width(16), .max('hffff), .ongoal("wrap"), .trigger("rising"), .behavior("new")) counter_1 (
    .count(not_2_out), .Q(\总周期数 ), .clk(CLK));  // open: load, D, carry, clr, preset, down
  Register #(.width(32), .trigger("rising"), .Select("low")) PC (
    .D(adder_1_out), .en(not_1_out), .Q(IF_PC), .clk(CLK));  // open: clr
  Hex_Digit_Display hex_digit_display_1 (.value(LedData[31:28]));  // open: dp
  // Probe on IF_PC[19:0]
  // Mips_Probe mips_probe_1: pin names not known; wires that end beside it: IF_IR
  Hex_Digit_Display hex_digit_display_2 (.value(LedData[23:20]));  // open: dp
  Hex_Digit_Display hex_digit_display_3 (.value(LedData[27:24]));  // open: dp
  // Probe on ID_PC[19:0]
  // Mips_Probe mips_probe_2: pin names not known; wires that end beside it: ID_IR
  Adder #(.width(32)) adder_1 (.a(32'h4), .b(IF_PC), .out(adder_1_out));  // open: cin, cout
  ROM #(.addrWidth(10), .dataWidth(32), .Select("high")) rom_1 (.addr(IF_PC[11:2]), .data(IF_IR));
  Hex_Digit_Display hex_digit_display_4 (.value(LedData[19:16]));  // open: dp
  Hex_Digit_Display hex_digit_display_5 (.value(LedData[15:12]));  // open: dp
  IF_ID if_id_1 (
    .CLK(CLK), .CLR(RST), .IR_in(IF_IR), .IR_out(ID_IR), .PC_in(IF_PC), .PC_out(ID_PC));  // open: Stall, PreditJump, PreditJump_2
  Hex_Digit_Display hex_digit_display_6 (.value(LedData[11:8]));  // open: dp
  Hex_Digit_Display hex_digit_display_7 (.value(LedData[7:4]));  // open: dp
  Clock #(.highDuration(1), .lowDuration(1)) clock_1 (.out(clock_1_out));
  // Probe on EX_PC[19:0]
  // Mips_Probe mips_probe_3: pin names not known; wires that end beside it: clock_1_out, EX_IR, CLK
  Hex_Digit_Display hex_digit_display_8 (.value(LedData[3:0]));  // open: dp
  not not_3 (not_3_out, Syscall);
  assign bit_extender_1_out = {{16{1'b0}}, ID_IR[15:0]};  // Bit_Extender bit_extender_1
  assign bit_extender_2_out = {{16{ID_IR[15]}}, ID_IR[15:0]};  // Bit_Extender bit_extender_2
  // Probe on \总周期数 
  // Probe on M_PC[19:0]
  // Mips_Probe mips_probe_4: pin names not known; wires that end beside it: MEM_IR
  \单周期硬布线控制器  \u_单周期硬布线控制器_1  (
    .Func(ID_IR[5:0]), .OP(ID_IR[31:26]), .ALU_OP(AluOP), .MemToReg(MemToReg), .MemWrite(MemWrite_t),
    .ALU_SRC(AluSrc), .RegWrite(RegW), .SysCALL(Syscall), .SignedExt(SignedExt), .RegDst(RegDst), .JR(JR),
    .JMP(JMP), .Beq(BEQ), .JAL(JAL), .Bne(BNE), .SRAV(SRAV), .SUBU(SUBU), .LHU(LHU), .BGTZ(BGTZ));  // open: ERET, MFC0, MTC0, MF
  Multiplexer #(.select(1), .width(5), .disabled("Z"), .enable("false")) multiplexer_1 (
    .in0(5'b00010), .in1(ID_IR[25:21]), .out(multiplexer_1_out), .sel(not_3_out));
  Multiplexer #(.select(1), .width(5), .disabled("Z"), .enable("false")) multiplexer_2 (
    .in0(5'b00100), .in1(ID_IR[20:16]), .out(multiplexer_2_out), .sel(not_3_out));
  Multiplexer #(.select(1), .width(32), .disabled("Z"), .enable("false")) multiplexer_3 (
    .in0(bit_extender_1_out), .in1(bit_extender_2_out), .out(multiplexer_3_out), .sel(SignedExt));
  // Probe on \总周期数 
  // Probe on \无条件分支数 
  // Probe on \条件分支成功数 
  // Probe on \插入气泡数 
  // Probe on \LoadUse次数 
  MIPS_Regifile mips_regifile_1 (
    .Din(RDin), .Clk(CLK), .R1(mips_regifile_1_r1), .R2(mips_regifile_1_r2), .WE(RegWrite),
    .W_num(multiplexer_6_out), .R1_num(multiplexer_1_out), .R2_num(multiplexer_2_out));
  // Probe on IF_PC[11:0]
  // Probe on WB_PC[19:0]
  // Mips_Probe mips_probe_5: pin names not known; wires that end beside it: WB_IR
  // Probe on ID_PC[11:0]
  // Probe on EX_PC[11:0]
  ID_EX id_ex_1 (
    .RegDst_in(RegDst), .IR_in(ID_IR), .Syscall_in(Syscall), .RegWrite_in(RegW), .PC_in(ID_PC), .JMP_in(JMP),
    .MemToReg_in(MemToReg), .A_in(mips_regifile_1_r1), .JR_in(JR), .AluOP_in(AluOP), .JAL_in(JAL),
    .AluSrc_in(AluSrc), .B_in(mips_regifile_1_r2), .SignedExt_in(SignedExt), .MemWrite(MemWrite_t),
    .Imm_in(multiplexer_3_out), .Beq_in(BEQ), .Shamt(ID_IR[10:6]), .Bne_in(BNE), .CLK(CLK),
    .RegDst_out(id_ex_1_regdst_out), .IR_out(EX_IR), .Syscall_out(id_ex_1_syscall_out),
    .RegWrite_out(id_ex_1_regwrite_out), .PC_out(EX_PC), .MemToReg_out(id_ex_1_memtoreg_out),
    .A_out({id_ex_1_a_out_2, id_ex_1_a_out}), .AluOP_out(EX_AluOP), .AluSrc_out(EX_AluSrc),
    .B_out(id_ex_1_b_out), .MemWrite_2(id_ex_1_memwrite_2), .Imm_out(id_ex_1_imm_out),
    .Shamt_2(id_ex_1_shamt_2), .CLR(RST), .BGTZ(BGTZ), .SUBU(SUBU), .LHU(LHU), .LHU_2(id_ex_1_lhu_2),
    .SRAV(SRAV), .SRAV_2(EX_SRAV));  // open: JMP_out, JR_out, JAL_out, SignedExt_out, Beq_out, Bne_out, Stall, BGTZ_2, SUBU_2, MD_in, MD_out, ALU_in, ALU_out, PreditJump, PreditJump_2
  // Probe on M_PC[11:0]
  D_Flip_Flop #(.trigger("high"), .Pre_Clr_Positions("LEGACY"), .NegatePresetClear("false"), .enable("true"), .NewFFLayout("false")) d_ff_1 (.Q(d_ff_1_q));  // open: clk, D, Qn, preset, en, reset
  // Probe on 13'hc
  // Probe on WB_PC[11:0]
  Comparator #(.width(13), .mode("twosComplement")) comparator_1 (
    .a(CNT_num), .b(13'hc), .eq(comparator_1_eq), .lt(comparator_1_lt));  // open: gt
  Clock #(.highDuration(1), .lowDuration(1)) clock_2 (.out(clock_2_out));
  Multiplexer #(.select(1), .width(32), .disabled("Z"), .enable("false")) multiplexer_4 (
    .in0(id_ex_1_b_out), .in1(id_ex_1_imm_out), .out(multiplexer_4_out), .sel(EX_AluSrc));
  nand nand_1 (nand_1_out, d_ff_1_q, comparator_1_eq);
  Counter #(.width(13), .max('h1fff), .ongoal("stay"), .trigger("rising"), .behavior("old")) counter_2 (
    .count(comparator_1_lt), .Q(CNT_num), .clk(clock_2_out));  // open: load, D, carry, clr, preset
  MIPS_ALU mips_alu_1 (
    .X({id_ex_1_a_out_2, id_ex_1_a_out}), .Y(multiplexer_4_out), .AluOP(EX_AluOP),
    .Result(mips_alu_1_result), .shamt(multiplexer_5_out));  // open: Equal, Result_2
  Multiplexer #(.select(1), .width(5), .disabled("Z"), .enable("false")) multiplexer_5 (
    .in0(id_ex_1_shamt_2), .in1(id_ex_1_a_out), .out(multiplexer_5_out), .sel(EX_SRAV));
  assign CLK = nand_1_out ? clock_2_out : 1'bz;  // Controlled_Buffer controlled_buffer_1
  Pull_Resistor #(.pull(1)) pull_resistor_1 (.node(CLK));
  ID_EX id_ex_2 (
    .RegDst_in(id_ex_1_regdst_out), .IR_in(EX_IR), .Syscall_in(id_ex_1_syscall_out),
    .RegWrite_in(id_ex_1_regwrite_out), .PC_in(EX_PC), .MemToReg_in(id_ex_1_memtoreg_out),
    .A_in({id_ex_1_a_out_2, id_ex_1_a_out}), .B_in(id_ex_1_b_out), .MemWrite(id_ex_1_memwrite_2), .CLK(CLK),
    .RegDst_out(id_ex_2_regdst_out), .IR_out(MEM_IR), .Syscall_out(id_ex_2_syscall_out),
    .RegWrite_out(id_ex_2_regwrite_out), .PC_out(M_PC), .MemToReg_out(id_ex_2_memtoreg_out),
    .A_out(id_ex_2_a_out), .B_out(MDin), .MemWrite_2(MemWrite), .CLR(RST), .LHU(id_ex_1_lhu_2),
    .LHU_2(id_ex_2_lhu_2), .ALU_in(mips_alu_1_result), .ALU_out(id_ex_2_alu_out));  // open: JMP_in, JR_in, AluOP_in, JAL_in, AluSrc_in, SignedExt_in, Imm_in, Beq_in, Shamt, Bne_in, JMP_out, JR_out, AluOP_out, JAL_out, AluSrc_out, SignedExt_out, Imm_out, Beq_out, Shamt_2, Bne_out, Stall, BGTZ, BGTZ_2, SUBU, SUBU_2, SRAV, SRAV_2, MD_in, MD_out, PreditJump, PreditJump_2
  RAM #(.addrWidth(10), .dataWidth(32), .bus("separate"), .Select("high")) ram_1 (
    .addr(id_ex_2_alu_out[11:2]), .din(MDin), .data(ram_1_data), .str(MemWrite), .clk(CLK));  // open: sel, ld, clr
  ID_EX id_ex_3 (
    .RegDst_in(id_ex_2_regdst_out), .IR_in(MEM_IR), .Syscall_in(id_ex_2_syscall_out),
    .RegWrite_in(id_ex_2_regwrite_out), .PC_in(M_PC), .MemToReg_in(id_ex_2_memtoreg_out),
    .A_in(id_ex_2_a_out), .B_in(MDin), .CLK(CLK), .RegDst_out(WB_RegDst), .IR_out(WB_IR),
    .Syscall_out(WB_Syscall), .RegWrite_out(RegWrite), .PC_out(WB_PC), .MemToReg_out(WB_MemtoReg),
    .A_out(id_ex_3_a_out), .B_out(id_ex_3_b_out), .CLR(RST), .LHU(id_ex_2_lhu_2), .LHU_2(WB_LHU),
    .MD_in(ram_1_data), .MD_out(id_ex_3_md_out), .ALU_in(id_ex_2_alu_out), .ALU_out(id_ex_3_alu_out));  // open: JMP_in, JR_in, AluOP_in, JAL_in, AluSrc_in, SignedExt_in, MemWrite, Imm_in, Beq_in, Shamt, Bne_in, JMP_out, JR_out, AluOP_out, JAL_out, AluSrc_out, SignedExt_out, MemWrite_2, Imm_out, Beq_out, Shamt_2, Bne_out, Stall, BGTZ, BGTZ_2, SUBU, SUBU_2, SRAV, SRAV_2, PreditJump, PreditJump_2
  Comparator #(.width(32), .mode("unsigned")) comparator_2 (
    .a(32'h22), .b(id_ex_3_a_out), .eq(comparator_2_eq));  // open: gt, lt
  Multiplexer #(.select(1), .width(5), .disabled("Z"), .enable("false")) multiplexer_6 (
    .in0(WB_IR[20:16]), .in1(WB_IR[15:11]), .out(multiplexer_6_out), .sel(WB_RegDst));
  Register #(.width(32), .trigger("falling"), .Select("low")) register_1 (
    .D(id_ex_3_b_out), .Q(LedData), .clk(and_1_out));  // open: en, clr
  and and_1 (and_1_out, WB_Syscall, comparator_2_eq);
  Register #(.width(1), .trigger("rising"), .Select("low")) register_2 (
    .D(and_2_out), .en(and_2_out), .Q(Pause), .clk(CLK), .clr(Go));
  and and_2 (and_2_out, WB_Syscall, ~comparator_2_eq);  // AND_Gate
  Multiplexer #(.select(1), .width(32), .disabled("Z"), .enable("false")) multiplexer_7 (
    .in0(id_ex_3_alu_out), .in1(id_ex_3_md_out), .out(multiplexer_7_out), .sel(WB_MemtoReg));
  assign bit_extender_3_out = {{16{1'b0}}, multiplexer_7_out[15:0]};  // Bit_Extender bit_extender_3
  Multiplexer #(.select(1), .width(32), .disabled("Z"), .enable("false")) multiplexer_8 (
    .in0(bit_extender_3_out), .in1(bit_extender_4_out), .out(multiplexer_8_out), .sel(id_ex_3_alu_out[1]));
  assign bit_extender_4_out = {{16{1'b0}}, multiplexer_7_out[31:16]};  // Bit_Extender bit_extender_4
  Multiplexer #(.select(1), .width(32), .disabled("Z"), .enable("false")) multiplexer_9 (
    .in0(multiplexer_7_out), .in1(multiplexer_8_out), .out(RDin), .sel(WB_LHU));

  // Other names for the same wires on the sheet: MEM_PC[31:0] = M_PC; MemW = MemWrite

  // Notes on the sheet:
  //   中断源
  //   时空图监测，可删除
  //   中断等待指示
  //   指令存储器
  //   contents of rom_1 (hex, n*v repeats v):
  //   20100000 20110000 20120000 20130000 36100000 36310001 36520002 36730003 ae100000 ae110004 ae120008
  //   ae13000c 2002000a 20110000 20120000 20130000 c
  //   数码管输出
  //   OP
  //   Func
  //   rs
  //   rt
  //   Imm
  //   sa
  //   JMP
  //   JR
  //   OP
  //   Func
  //   Bne
  //   MemToReg
  //   MemWrite
  //   AluOP
  //   AluSrcB
  //   RegWrite
  //   JAL
  //   RegDst
  //   Syscall
  //   控制位
  //   流水调试日志用
  //   暂停节拍，不能为0
  //   戳工具置1进入计数暂停模式，ctrl+k时钟自动运行到对应节拍暂停
  //   ctrl+k关闭时钟连续运行，将控制位置零，进入单步调试模式调试
  //   用这个时钟源需要去掉电路中的其他时钟源
  //   可计数暂停的时钟源
  //   为方便自动评测，需要输出流水线各段保存的PC值，注意是PC不是PC+4，另外ID段寄存器写入信息，Mem段内存写入信息也要输出
  //   rt
  //   rd
endmodule

module IF_ID (
  input  PreditJump,
  input  [31:0] IR_in,
  input  [31:0] PC_in,
  input  CLK,
  input  CLR,
  input  Stall,
  output PreditJump_2,
  output [31:0] IR_out,
  output [31:0] PC_out
);

  wire multiplexer_1_out, not_1_out;
  wire [31:0] multiplexer_2_out, multiplexer_3_out;

  Multiplexer #(.select(1), .width(1), .disabled("Z"), .enable("false")) multiplexer_1 (
    .in0(PreditJump), .in1(1'b0), .out(multiplexer_1_out), .sel(CLR));
  Multiplexer #(.select(1), .width(32), .disabled("Z"), .enable("false")) multiplexer_2 (
    .in0(IR_in), .in1({32{1'b0}}), .out(multiplexer_2_out), .sel(CLR));
  Multiplexer #(.select(1), .width(32), .disabled("Z"), .enable("false")) multiplexer_3 (
    .in0(PC_in), .in1({32{1'b0}}), .out(multiplexer_3_out), .sel(CLR));
  Pull_Resistor #(.pull(0)) pull_resistor_1 (.node(CLR));
  not not_1 (not_1_out, Stall);
  Register #(.width(1), .trigger("rising"), .Select("low")) register_1 (
    .D(multiplexer_1_out), .en(not_1_out), .Q(PreditJump_2), .clk(CLK));  // open: clr
  Register #(.width(32), .trigger("rising"), .Select("low")) register_2 (
    .D(multiplexer_2_out), .en(not_1_out), .Q(IR_out), .clk(CLK));  // open: clr
  Register #(.width(32), .trigger("rising"), .Select("low")) register_3 (
    .D(multiplexer_3_out), .en(not_1_out), .Q(PC_out), .clk(CLK));  // open: clr
  Pull_Resistor #(.pull(0)) pull_resistor_2 (.node(not_1_out));
endmodule

module ID_EX (
  input  RegWrite_in,
  input  [31:0] IR_in,
  input  RegDst_in,
  input  MemToReg_in,
  input  [31:0] PC_in,
  input  Syscall_in,
  input  [3:0] AluOP_in,
  input  JMP_in,
  input  [31:0] A_in,
  input  AluSrc_in,
  input  JR_in,
  input  MemWrite,
  input  [31:0] B_in,
  input  JAL_in,
  input  BGTZ,
  input  [31:0] Imm_in,
  input  SignedExt_in,
  input  SUBU,
  input  [4:0] Shamt,
  input  Beq_in,
  input  LHU,
  input  [31:0] MD_in,
  input  SRAV,
  input  Bne_in,
  input  [31:0] ALU_in,
  input  PreditJump,
  input  CLK,
  input  CLR,
  input  Stall,
  output RegWrite_out,
  output [31:0] IR_out,
  output RegDst_out,
  output MemToReg_out,
  output [31:0] PC_out,
  output Syscall_out,
  output [3:0] AluOP_out,
  output JMP_out,
  output [31:0] A_out,
  output AluSrc_out,
  output JR_out,
  output MemWrite_2,
  output [31:0] B_out,
  output JAL_out,
  output BGTZ_2,
  output [31:0] Imm_out,
  output SignedExt_out,
  output SUBU_2,
  output [4:0] Shamt_2,
  output Beq_out,
  output LHU_2,
  output [31:0] MD_out,
  output SRAV_2,
  output Bne_out,
  output [31:0] ALU_out,
  output PreditJump_2
);

  wire multiplexer_1_out, multiplexer_2_out, multiplexer_3_out, multiplexer_4_out, multiplexer_5_out,
       multiplexer_6_out, multiplexer_7_out, multiplexer_8_out, multiplexer_9_out, multiplexer_10_out,
       multiplexer_11_out, multiplexer_13_out, multiplexer_14_out, multiplexer_15_out, multiplexer_16_out,
       multiplexer_17_out, multiplexer_18_out, not_1_out;
  wire [3:0] multiplexer_12_out;
  wire [4:0] multiplexer_24_out;
  wire [31:0] multiplexer_19_out, multiplexer_20_out, multiplexer_21_out, multiplexer_22_out,
       multiplexer_23_out, multiplexer_25_out, multiplexer_26_out;

  Multiplexer #(.select(1), .width(1), .disabled("Z"), .enable("false")) multiplexer_1 (
    .in0(RegDst_in), .in1(1'b0), .out(multiplexer_1_out), .sel(CLR));
  Multiplexer #(.select(1), .width(1), .disabled("Z"), .enable("false")) multiplexer_2 (
    .in0(Syscall_in), .in1(1'b0), .out(multiplexer_2_out), .sel(CLR));
  Multiplexer #(.select(1), .width(1), .disabled("Z"), .enable("false")) multiplexer_3 (
    .in0(JMP_in), .in1(1'b0), .out(multiplexer_3_out), .sel(CLR));
  Multiplexer #(.select(1), .width(1), .disabled("Z"), .enable("false")) multiplexer_4 (
    .in0(JR_in), .in1(1'b0), .out(multiplexer_4_out), .sel(CLR));
  Multiplexer #(.select(1), .width(1), .disabled("Z"), .enable("false")) multiplexer_5 (
    .in0(JAL_in), .in1(1'b0), .out(multiplexer_5_out), .sel(CLR));
  Multiplexer #(.select(1), .width(1), .disabled("Z"), .enable("false")) multiplexer_6 (
    .in0(SignedExt_in), .in1(1'b0), .out(multiplexer_6_out), .sel(CLR));
  Multiplexer #(.select(1), .width(1), .disabled("Z"), .enable("false")) multiplexer_7 (
    .in0(Beq_in), .in1(1'b0), .out(multiplexer_7_out), .sel(CLR));
  Multiplexer #(.select(1), .width(1), .disabled("Z"), .enable("false")) multiplexer_8 (
    .in0(Bne_in), .in1(1'b0), .out(multiplexer_8_out), .sel(CLR));
  Multiplexer #(.select(1), .width(1), .disabled("Z"), .enable("false")) multiplexer_9 (
    .in0(PreditJump), .in1(1'b0), .out(multiplexer_9_out), .sel(CLR));
  Pull_Resistor #(.pull(0)) pull_resistor_1 (.node(CLR));
  not not_1 (not_1_out, Stall);
  Register #(.width(1), .trigger("rising"), .Select("low")) register_1 (
    .D(multiplexer_1_out), .en(not_1_out), .Q(RegDst_out), .clk(CLK));  // open: clr
  Register #(.width(1), .trigger("rising"), .Select("low")) register_2 (
    .D(multiplexer_2_out), .en(not_1_out), .Q(Syscall_out), .clk(CLK));  // open: clr
  Register #(.width(1), .trigger("rising"), .Select("low")) register_3 (
    .D(multiplexer_3_out), .en(not_1_out), .Q(JMP_out), .clk(CLK));  // open: clr
  Register #(.width(1), .trigger("rising"), .Select("low")) register_4 (
    .D(multiplexer_4_out), .en(not_1_out), .Q(JR_out), .clk(CLK));  // open: clr
  Register #(.width(1), .trigger("rising"), .Select("low")) register_5 (
    .D(multiplexer_5_out), .en(not_1_out), .Q(JAL_out), .clk(CLK));  // open: clr
  Register #(.width(1), .trigger("rising"), .Select("low")) register_6 (
    .D(multiplexer_6_out), .en(not_1_out), .Q(SignedExt_out), .clk(CLK));  // open: clr
  Register #(.width(1), .trigger("rising"), .Select("low")) register_7 (
    .D(multiplexer_7_out), .en(not_1_out), .Q(Beq_out), .clk(CLK));  // open: clr
  Register #(.width(1), .trigger("rising"), .Select("low")) register_8 (
    .D(multiplexer_8_out), .en(not_1_out), .Q(Bne_out), .clk(CLK));  // open: clr
  Register #(.width(1), .trigger("rising"), .Select("low")) register_9 (
    .D(multiplexer_9_out), .en(not_1_out), .Q(PreditJump_2), .clk(CLK));  // open: clr
  Pull_Resistor #(.pull(0)) pull_resistor_2 (.node(not_1_out));
  Multiplexer #(.select(1), .width(1), .disabled("Z"), .enable("false")) multiplexer_10 (
    .in0(RegWrite_in), .in1(1'b0), .out(multiplexer_10_out), .sel(CLR));
  Multiplexer #(.select(1), .width(1), .disabled("Z"), .enable("false")) multiplexer_11 (
    .in0(MemToReg_in), .in1(1'b0), .out(multiplexer_11_out), .sel(CLR));
  Multiplexer #(.select(1), .width(4), .disabled("Z"), .enable("false")) multiplexer_12 (
    .in0(AluOP_in), .in1(4'b0000), .out(multiplexer_12_out), .sel(CLR));
  Multiplexer #(.select(1), .width(1), .disabled("Z"), .enable("false")) multiplexer_13 (
    .in0(AluSrc_in), .in1(1'b0), .out(multiplexer_13_out), .sel(CLR));
  Multiplexer #(.select(1), .width(1), .disabled("Z"), .enable("false")) multiplexer_14 (
    .in0(MemWrite), .in1(1'b0), .out(multiplexer_14_out), .sel(CLR));
  Multiplexer #(.select(1), .width(1), .disabled("Z"), .enable("false")) multiplexer_15 (
    .in0(BGTZ), .in1(1'b0), .out(multiplexer_15_out), .sel(CLR));
  Multiplexer #(.select(1), .width(1), .disabled("Z"), .enable("false")) multiplexer_16 (
    .in0(SUBU), .in1(1'b0), .out(multiplexer_16_out), .sel(CLR));
  Multiplexer #(.select(1), .width(1), .disabled("Z"), .enable("false")) multiplexer_17 (
    .in0(LHU), .in1(1'b0), .out(multiplexer_17_out), .sel(CLR));
  Multiplexer #(.select(1), .width(1), .disabled("Z"), .enable("false")) multiplexer_18 (
    .in0(SRAV), .in1(1'b0), .out(multiplexer_18_out), .sel(CLR));
  Register #(.width(1), .trigger("rising"), .Select("low")) register_10 (
    .D(multiplexer_10_out), .en(not_1_out), .Q(RegWrite_out), .clk(CLK));  // open: clr
  Register #(.width(1), .trigger("rising"), .Select("low")) register_11 (
    .D(multiplexer_11_out), .en(not_1_out), .Q(MemToReg_out), .clk(CLK));  // open: clr
  Register #(.width(4), .trigger("rising"), .Select("low")) register_12 (
    .D(multiplexer_12_out), .en(not_1_out), .Q(AluOP_out), .clk(CLK));  // open: clr
  Register #(.width(1), .trigger("rising"), .Select("low")) register_13 (
    .D(multiplexer_13_out), .en(not_1_out), .Q(AluSrc_out), .clk(CLK));  // open: clr
  Register #(.width(1), .trigger("rising"), .Select("low")) register_14 (
    .D(multiplexer_14_out), .en(not_1_out), .Q(MemWrite_2), .clk(CLK));  // open: clr
  Register #(.width(1), .trigger("rising"), .Select("low")) register_15 (
    .D(multiplexer_15_out), .en(not_1_out), .Q(BGTZ_2), .clk(CLK));  // open: clr
  Register #(.width(1), .trigger("rising"), .Select("low")) register_16 (
    .D(multiplexer_16_out), .en(not_1_out), .Q(SUBU_2), .clk(CLK));  // open: clr
  Register #(.width(1), .trigger("rising"), .Select("low")) register_17 (
    .D(multiplexer_17_out), .en(not_1_out), .Q(LHU_2), .clk(CLK));  // open: clr
  Register #(.width(1), .trigger("rising"), .Select("low")) register_18 (
    .D(multiplexer_18_out), .en(not_1_out), .Q(SRAV_2), .clk(CLK));  // open: clr
  Multiplexer #(.select(1), .width(32), .disabled("Z"), .enable("false")) multiplexer_19 (
    .in0(IR_in), .in1({32{1'b0}}), .out(multiplexer_19_out), .sel(CLR));
  Multiplexer #(.select(1), .width(32), .disabled("Z"), .enable("false")) multiplexer_20 (
    .in0(PC_in), .in1({32{1'b0}}), .out(multiplexer_20_out), .sel(CLR));
  Multiplexer #(.select(1), .width(32), .disabled("Z"), .enable("false")) multiplexer_21 (
    .in0(A_in), .in1({32{1'b0}}), .out(multiplexer_21_out), .sel(CLR));
  Multiplexer #(.select(1), .width(32), .disabled("Z"), .enable("false")) multiplexer_22 (
    .in0(B_in), .in1({32{1'b0}}), .out(multiplexer_22_out), .sel(CLR));
  Multiplexer #(.select(1), .width(32), .disabled("Z"), .enable("false")) multiplexer_23 (
    .in0(Imm_in), .in1({32{1'b0}}), .out(multiplexer_23_out), .sel(CLR));
  Multiplexer #(.select(1), .width(5), .disabled("Z"), .enable("false")) multiplexer_24 (
    .in0(Shamt), .in1({5{1'b0}}), .out(multiplexer_24_out), .sel(CLR));
  Multiplexer #(.select(1), .width(32), .disabled("Z"), .enable("false")) multiplexer_25 (
    .in0(MD_in), .in1({32{1'b0}}), .out(multiplexer_25_out), .sel(CLR));
  Multiplexer #(.select(1), .width(32), .disabled("Z"), .enable("false")) multiplexer_26 (
    .in0(ALU_in), .in1({32{1'b0}}), .out(multiplexer_26_out), .sel(CLR));
  Register #(.width(32), .trigger("rising"), .Select("low")) register_19 (
    .D(multiplexer_19_out), .en(not_1_out), .Q(IR_out), .clk(CLK));  // open: clr
  Register #(.width(32), .trigger("rising"), .Select("low")) register_20 (
    .D(multiplexer_20_out), .en(not_1_out), .Q(PC_out), .clk(CLK));  // open: clr
  Register #(.width(32), .trigger("rising"), .Select("low")) register_21 (
    .D(multiplexer_21_out), .en(not_1_out), .Q(A_out), .clk(CLK));  // open: clr
  Register #(.width(32), .trigger("rising"), .Select("low")) register_22 (
    .D(multiplexer_22_out), .en(not_1_out), .Q(B_out), .clk(CLK));  // open: clr
  Register #(.width(32), .trigger("rising"), .Select("low")) register_23 (
    .D(multiplexer_23_out), .en(not_1_out), .Q(Imm_out), .clk(CLK));  // open: clr
  Register #(.width(5), .trigger("rising"), .Select("low")) register_24 (
    .D(multiplexer_24_out), .en(not_1_out), .Q(Shamt_2), .clk(CLK));  // open: clr
  Register #(.width(32), .trigger("rising"), .Select("low")) register_25 (
    .D(multiplexer_25_out), .en(not_1_out), .Q(MD_out), .clk(CLK));  // open: clr
  Register #(.width(32), .trigger("rising"), .Select("low")) register_26 (
    .D(multiplexer_26_out), .en(not_1_out), .Q(ALU_out), .clk(CLK));  // open: clr
endmodule

module \气泡流水线  (
  output RegWrite,
  output MemWrite,
  output [31:0] IF_PC,
  output [31:0] ID_PC,
  output [31:0] EX_PC,
  output [31:0] M_PC,
  output [31:0] WB_PC,
  output [31:0] RDin,
  output [31:0] MDin,
  output [31:0] LedData
);

  wire AluSrc, and_1_out, and_2_out, and_3_out, and_4_out, and_5_out, and_6_out, BEQ, BGTZ, BNE, BraCLR,
       Branch, CLK, clock_1_out, clock_2_out, comparator_1_eq, comparator_1_lt, comparator_2_lt,
       comparator_3_eq, conflict, d_ff_1_q, EX_AluSrc, EX_BEQ, EX_BGTZ, EX_BNE, EX_JAL, EX_JMP, EX_JR,
       EX_RegDst, EX_RegW, EX_SRAV, Go, id_ex_1_lhu_2, id_ex_1_memtoreg_out, id_ex_1_memwrite_2,
       id_ex_1_syscall_out, id_ex_2_lhu_2, id_ex_2_memtoreg_out, id_ex_2_syscall_out, IR1, IR2, IR3, JAL,
       JMP, JR, LHU, MEM_JAL, MEM_RegDst, MEM_RegW, MemToReg, MemWrite_t, mips_alu_1_equal, nand_1_out,
       not_1_out, not_2_out, not_3_out, not_4_out, not_5_out, not_6_out, or_2_out, or_3_out, or_4_out,
       or_6_out, or_7_out, Pause, RegDst, RegW, RST, SignedExt, SRAV, SUBU, Syscall, W1, W2, W3, WB_JAL,
       WB_LHU, WB_MemtoReg, WB_RegDst, WB_Syscall, \源寄存器使用情况_1_r1_used , \源寄存器使用情况_1_r2_used ;
  wire [3:0] AluOP, EX_AluOP;
  wire [4:0] id_ex_1_a_out, id_ex_1_shamt_2, multiplexer_2_out, multiplexer_3_out, multiplexer_4_out,
       multiplexer_5_out, multiplexer_6_out, multiplexer_12_out, multiplexer_13_out, R1_num, R2_num;
  wire [5:0] Func;
  wire [12:0] CNT_num;
  wire [15:0] counter_4_q, counter_5_q, \LoadUse次数 , \总周期数 , \插入气泡数 , \无条件分支数 , \条件分支成功数 ;
  wire [31:0] adder_1_out, adder_2_out, adder_3_out, adder_4_out, bit_extender_1_out, bit_extender_2_out,
       bit_extender_3_out, bit_extender_4_out, controlled_buffer_1_out, EX_IR, id_ex_1_b_out,
       id_ex_1_imm_out, id_ex_2_a_out, id_ex_2_alu_out, id_ex_3_a_out, id_ex_3_alu_out, id_ex_3_b_out,
       id_ex_3_md_out, IF_IR, MEM_IR, mips_alu_1_result, mips_regifile_1_r1, mips_regifile_1_r2,
       multiplexer_1_out, multiplexer_10_out, multiplexer_11_out, multiplexer_14_out, multiplexer_15_out,
       multiplexer_16_out, ram_1_data, target_offset, WB_IR;
  wire [31:5] id_ex_1_a_out_2;
  wire [31:6] ID_IR;

  Button \u_总复位  (.out(RST));
  Button _1 (.out(IR1));
  Button _2 (.out(IR2));
  Button _3 (.out(IR3));
  // Probe on \总周期数 
  // Probe on \总周期数 
  Button \u_继续运行  (.out(Go));
  LED #(.active("true")) led_1 (.in(W1));
  LED #(.active("true")) led_2 (.in(W2));
  LED #(.active("true")) led_3 (.in(W3));
  Adder #(.width(32)) adder_1 (.a(32'h4), .b(EX_PC), .out(adder_1_out));  // open: cin, cout
  Hex_Digit_Display hex_digit_display_1 (.value(LedData[31:28]));  // open: dp
  // Probe on IF_PC[19:0]
  // Mips_Probe mips_probe_1: pin names not known; wires that end beside it: IF_IR
  Adder #(.width(32)) adder_2 (.a(adder_1_out), .b(target_offset), .out(adder_2_out));  // open: cin, cout
  Hex_Digit_Display hex_digit_display_2 (.value(LedData[27:24]));  // open: dp
  Hex_Digit_Display hex_digit_display_3 (.value(LedData[23:20]));  // open: dp
  // Probe on ID_PC[19:0]
  // Mips_Probe mips_probe_2: pin names not known; wires that end beside it: {ID_IR, Func}
  assign controlled_buffer_1_out = EX_JR ? {id_ex_1_a_out_2, id_ex_1_a_out} : 32'bz;  // Controlled_Buffer controlled_buffer_1
  assign controlled_buffer_1_out = EX_JMP ? {EX_PC[31:28], EX_IR[25:0], 2'b00} : 32'bz;  // Controlled_Buffer controlled_buffer_2
  assign controlled_buffer_1_out = Branch ? adder_2_out : 32'bz;  // Controlled_Buffer controlled_buffer_3
  Hex_Digit_Display hex_digit_display_4 (.value(LedData[15:12]));  // open: dp
  Hex_Digit_Display hex_digit_display_5 (.value(LedData[19:16]));  // open: dp
  Multiplexer #(.select(1), .width(32), .disabled("Z"), .enable("false")) multiplexer_1 (
    .in0(adder_3_out), .in1(controlled_buffer_1_out), .out(multiplexer_1_out), .sel(BraCLR));
  or or_1 (BraCLR, EX_JMP, EX_JR, Branch);
  Multiplexer #(.select(1), .width(5), .disabled("Z"), .enable("false")) multiplexer_2 (
    .in0(EX_IR[20:16]), .in1(EX_IR[15:11]), .out(multiplexer_2_out), .sel(EX_RegDst));
  Multiplexer #(.select(1), .width(5), .disabled("Z"), .enable("false")) multiplexer_3 (
    .in0(multiplexer_2_out), .in1({5{1'b1}}), .out(multiplexer_3_out), .sel(MEM_JAL));
  Multiplexer #(.select(1), .width(5), .disabled("Z"), .enable("false")) multiplexer_4 (
    .in0(MEM_IR[20:16]), .in1(MEM_IR[15:11]), .out(multiplexer_4_out), .sel(MEM_RegDst));
  Multiplexer #(.select(1), .width(5), .disabled("Z"), .enable("false")) multiplexer_5 (
    .in0(multiplexer_4_out), .in1({5{1'b1}}), .out(multiplexer_5_out), .sel(EX_JAL));
  Hex_Digit_Display hex_digit_display_6 (.value(LedData[7:4]));  // open: dp
  Hex_Digit_Display hex_digit_display_7 (.value(LedData[11:8]));  // open: dp
  Clock #(.highDuration(1), .lowDuration(1)) clock_1 (.out(clock_1_out));
  // Probe on EX_PC[19:0]
  // Mips_Probe mips_probe_3: pin names not known; wires that end beside it: clock_1_out, EX_IR, CLK
  \源寄存器使用情况  \u_源寄存器使用情况_1  (
    .OP0(ID_IR[26]), .OP1(ID_IR[27]), .OP2(ID_IR[28]), .OP3(ID_IR[29]), .OP4(ID_IR[30]), .OP5(ID_IR[31]),
    .F0(Func[0]), .F1(Func[1]), .F2(Func[2]), .F3(Func[3]), .F4(Func[4]), .F5(Func[5]),
    .R1_USED(\源寄存器使用情况_1_r1_used ), .R2_USED(\源寄存器使用情况_1_r2_used ));
  Hex_Digit_Display hex_digit_display_8 (.value(LedData[3:0]));  // open: dp
  or or_2 (or_2_out, conflict, Pause);
  not not_1 (not_1_out, or_2_out);
  Register #(.width(32), .trigger("rising"), .Select("low")) PC (
    .D(multiplexer_1_out), .en(not_1_out), .Q(IF_PC), .clk(CLK));  // open: clr
  // Probe on \总周期数 
  // Probe on M_PC[19:0]
  // Mips_Probe mips_probe_4: pin names not known; wires that end beside it: MEM_IR
  \数据相关处理逻辑  \u_数据相关处理逻辑_1  (
    .R1_Used(\源寄存器使用情况_1_r1_used ), .R2_Used(\源寄存器使用情况_1_r2_used ), .R1_num(R1_num), .EX_RegWrite(EX_RegW),
    .EX_WriteReg_num(multiplexer_3_out), .R2_num(R2_num), .MEM_WriteReg_num(multiplexer_5_out),
    .MEM_RegWrite(MEM_RegW), .conflict(conflict));
  // Probe on \总周期数 
  // Probe on \无条件分支数 
  // Probe on \条件分支成功数 
  // Probe on \插入气泡数 
  // Probe on \LoadUse次数 
  Adder #(.width(32)) adder_3 (.a(32'h4), .b(IF_PC), .out(adder_3_out));  // open: cin, cout
  // Probe on IF_PC[11:0]
  // Probe on WB_PC[19:0]
  // Mips_Probe mips_probe_5: pin names not known; wires that end beside it: WB_IR
  ROM #(.addrWidth(10), .dataWidth(32), .Select("high")) rom_1 (.addr(IF_PC[11:2]), .data(IF_IR));
  or or_3 (or_3_out, BraCLR, RST);
  // Probe on EX_PC[11:0]
  // Probe on ID_PC[11:0]
  IF_ID if_id_1 (
    .CLK(CLK), .CLR(or_3_out), .Stall(conflict), .IR_in(IF_IR), .IR_out({ID_IR, Func}), .PC_in(IF_PC),
    .PC_out(ID_PC));  // open: PreditJump, PreditJump_2
  // Probe on M_PC[11:0]
  D_Flip_Flop #(.trigger("high"), .Pre_Clr_Positions("LEGACY"), .NegatePresetClear("false"), .enable("true"), .NewFFLayout("false")) d_ff_1 (.Q(d_ff_1_q));  // open: clk, D, Qn, preset, en, reset
  // Probe on 13'hc
  Multiplexer #(.select(1), .width(5), .disabled("Z"), .enable("false")) multiplexer_6 (
    .in0({5{1'b1}}), .in1(multiplexer_13_out), .out(multiplexer_6_out), .sel(not_2_out));
  not not_2 (not_2_out, WB_JAL);
  Adder #(.width(32)) adder_4 (.a(32'h4), .b(WB_PC), .out(adder_4_out));  // open: cin, cout
  // Probe on WB_PC[11:0]
  Comparator #(.width(13), .mode("twosComplement")) comparator_1 (
    .a(CNT_num), .b(13'hc), .eq(comparator_1_eq), .lt(comparator_1_lt));  // open: gt
  Clock #(.highDuration(1), .lowDuration(1)) clock_2 (.out(clock_2_out));
  \单周期硬布线控制器  \u_单周期硬布线控制器_1  (
    .Func(Func), .OP(ID_IR[31:26]), .ALU_OP(AluOP), .MemToReg(MemToReg), .MemWrite(MemWrite_t),
    .ALU_SRC(AluSrc), .RegWrite(RegW), .SysCALL(Syscall), .SignedExt(SignedExt), .RegDst(RegDst), .JR(JR),
    .JMP(JMP), .Beq(BEQ), .JAL(JAL), .Bne(BNE), .SRAV(SRAV), .SUBU(SUBU), .LHU(LHU), .BGTZ(BGTZ));  // open: ERET, MFC0, MTC0, MF
  Multiplexer #(.select(1), .width(5), .disabled("Z"), .enable("false")) multiplexer_7 (
    .in0(ID_IR[25:21]), .in1(5'b00010), .out(R1_num), .sel(Syscall));
  Multiplexer #(.select(1), .width(5), .disabled("Z"), .enable("false")) multiplexer_8 (
    .in0(ID_IR[20:16]), .in1(5'b00100), .out(R2_num), .sel(Syscall));
  Multiplexer #(.select(1), .width(32), .disabled("Z"), .enable("false")) multiplexer_9 (
    .in0(multiplexer_16_out), .in1(adder_4_out), .out(RDin), .sel(WB_JAL));
  nand nand_1 (nand_1_out, d_ff_1_q, comparator_1_eq);
  Counter #(.width(13), .max('h1fff), .ongoal("stay"), .trigger("rising"), .behavior("old")) counter_1 (
    .count(comparator_1_lt), .Q(CNT_num), .clk(clock_2_out));  // open: load, D, carry, clr, preset
  assign bit_extender_1_out = {{16{1'b0}}, {ID_IR[15:6], Func}};  // Bit_Extender bit_extender_1
  assign bit_extender_2_out = {{16{ID_IR[15]}}, {ID_IR[15:6], Func}};  // Bit_Extender bit_extender_2
  assign CLK = nand_1_out ? clock_2_out : 1'bz;  // Controlled_Buffer controlled_buffer_4
  MIPS_Regifile mips_regifile_1 (
    .Din(RDin), .Clk(CLK), .R1(mips_regifile_1_r1), .R2(mips_regifile_1_r2), .WE(RegWrite),
    .W_num(multiplexer_6_out), .R1_num(R1_num), .R2_num(R2_num));
  Multiplexer #(.select(1), .width(32), .disabled("Z"), .enable("false")) multiplexer_10 (
    .in0(bit_extender_1_out), .in1(bit_extender_2_out), .out(multiplexer_10_out), .sel(SignedExt));
  Pull_Resistor #(.pull(1)) pull_resistor_1 (.node(CLK));
  or or_4 (or_4_out, BraCLR, conflict, RST);
  ID_EX id_ex_1 (
    .RegDst_in(RegDst), .IR_in({ID_IR, Func}), .Syscall_in(Syscall), .RegWrite_in(RegW), .PC_in(ID_PC),
    .JMP_in(JMP), .MemToReg_in(MemToReg), .A_in(mips_regifile_1_r1), .JR_in(JR), .AluOP_in(AluOP),
    .JAL_in(JAL), .AluSrc_in(AluSrc), .B_in(mips_regifile_1_r2), .SignedExt_in(SignedExt),
    .MemWrite(MemWrite_t), .Imm_in(multiplexer_10_out), .Beq_in(BEQ), .Shamt(ID_IR[10:6]), .Bne_in(BNE),
    .CLK(CLK), .RegDst_out(EX_RegDst), .IR_out(EX_IR), .Syscall_out(id_ex_1_syscall_out),
    .RegWrite_out(EX_RegW), .PC_out(EX_PC), .JMP_out(EX_JMP), .MemToReg_out(id_ex_1_memtoreg_out),
    .A_out({id_ex_1_a_out_2, id_ex_1_a_out}), .JR_out(EX_JR), .AluOP_out(EX_AluOP), .JAL_out(EX_JAL),
    .AluSrc_out(EX_AluSrc), .B_out(id_ex_1_b_out), .MemWrite_2(id_ex_1_memwrite_2),
    .Imm_out(id_ex_1_imm_out), .Beq_out(EX_BEQ), .Shamt_2(id_ex_1_shamt_2), .Bne_out(EX_BNE), .CLR(or_4_out),
    .BGTZ(BGTZ), .BGTZ_2(EX_BGTZ), .SUBU(SUBU), .LHU(LHU), .LHU_2(id_ex_1_lhu_2), .SRAV(SRAV),
    .SRAV_2(EX_SRAV));  // open: SignedExt_out, Stall, SUBU_2, MD_in, MD_out, ALU_in, ALU_out, PreditJump, PreditJump_2
  Shifter #(.width(32), .shift("ll")) shifter_1 (.in(id_ex_1_imm_out), .\dist (5'b00010), .out(target_offset));
  Multiplexer #(.select(1), .width(32), .disabled("Z"), .enable("false")) multiplexer_11 (
    .in0(id_ex_1_b_out), .in1(id_ex_1_imm_out), .out(multiplexer_11_out), .sel(EX_AluSrc));
  and and_1 (and_1_out, EX_BEQ, mips_alu_1_equal);
  and and_2 (and_2_out, EX_BNE, ~mips_alu_1_equal);  // AND_Gate
  and and_3 (and_3_out, EX_BGTZ, comparator_2_lt);
  Comparator #(.width(32), .mode("twosComplement")) comparator_2 (
    .a({32{1'b0}}), .b({id_ex_1_a_out_2, id_ex_1_a_out}), .lt(comparator_2_lt));  // open: gt, eq
  MIPS_ALU mips_alu_1 (
    .X({id_ex_1_a_out_2, id_ex_1_a_out}), .Y(multiplexer_11_out), .AluOP(EX_AluOP), .Equal(mips_alu_1_equal),
    .Result(mips_alu_1_result), .shamt(multiplexer_12_out));  // open: Result_2
  Multiplexer #(.select(1), .width(5), .disabled("Z"), .enable("false")) multiplexer_12 (
    .in0(id_ex_1_shamt_2), .in1(id_ex_1_a_out), .out(multiplexer_12_out), .sel(EX_SRAV));
  or or_5 (Branch, and_1_out, and_2_out, and_3_out);
  ID_EX id_ex_2 (
    .RegDst_in(EX_RegDst), .IR_in(EX_IR), .Syscall_in(id_ex_1_syscall_out), .RegWrite_in(EX_RegW),
    .PC_in(EX_PC), .MemToReg_in(id_ex_1_memtoreg_out), .A_in({id_ex_1_a_out_2, id_ex_1_a_out}),
    .JAL_in(EX_JAL), .B_in(id_ex_1_b_out), .MemWrite(id_ex_1_memwrite_2), .CLK(CLK), .RegDst_out(MEM_RegDst),
    .IR_out(MEM_IR), .Syscall_out(id_ex_2_syscall_out), .RegWrite_out(MEM_RegW), .PC_out(M_PC),
    .MemToReg_out(id_ex_2_memtoreg_out), .A_out(id_ex_2_a_out), .JAL_out(MEM_JAL), .B_out(MDin),
    .MemWrite_2(MemWrite), .CLR(RST), .LHU(id_ex_1_lhu_2), .LHU_2(id_ex_2_lhu_2), .ALU_in(mips_alu_1_result),
    .ALU_out(id_ex_2_alu_out));  // open: JMP_in, JR_in, AluOP_in, AluSrc_in, SignedExt_in, Imm_in, Beq_in, Shamt, Bne_in, JMP_out, JR_out, AluOP_out, AluSrc_out, SignedExt_out, Imm_out, Beq_out, Shamt_2, Bne_out, Stall, BGTZ, BGTZ_2, SUBU, SUBU_2, SRAV, SRAV_2, MD_in, MD_out, PreditJump, PreditJump_2
  RAM #(.addrWidth(10), .dataWidth(32), .bus("separate"), .Select("high")) ram_1 (
    .addr(id_ex_2_alu_out[11:2]), .din(MDin), .data(ram_1_data), .str(MemWrite), .clk(CLK));  // open: sel, ld, clr
  ID_EX id_ex_3 (
    .RegDst_in(MEM_RegDst), .IR_in(MEM_IR), .Syscall_in(id_ex_2_syscall_out), .RegWrite_in(MEM_RegW),
    .PC_in(M_PC), .MemToReg_in(id_ex_2_memtoreg_out), .A_in(id_ex_2_a_out), .JAL_in(MEM_JAL), .B_in(MDin),
    .CLK(CLK), .RegDst_out(WB_RegDst), .IR_out(WB_IR), .Syscall_out(WB_Syscall), .RegWrite_out(RegWrite),
    .PC_out(WB_PC), .MemToReg_out(WB_MemtoReg), .A_out(id_ex_3_a_out), .JAL_out(WB_JAL),
    .B_out(id_ex_3_b_out), .CLR(RST), .LHU(id_ex_2_lhu_2), .LHU_2(WB_LHU), .MD_in(ram_1_data),
    .MD_out(id_ex_3_md_out), .ALU_in(id_ex_2_alu_out), .ALU_out(id_ex_3_alu_out));  // open: JMP_in, JR_in, AluOP_in, AluSrc_in, SignedExt_in, MemWrite, Imm_in, Beq_in, Shamt, Bne_in, JMP_out, JR_out, AluOP_out, AluSrc_out, SignedExt_out, MemWrite_2, Imm_out, Beq_out, Shamt_2, Bne_out, Stall, BGTZ, BGTZ_2, SUBU, SUBU_2, SRAV, SRAV_2, PreditJump, PreditJump_2
  Comparator #(.width(32), .mode("unsigned")) comparator_3 (
    .a(32'h22), .b(id_ex_3_a_out), .eq(comparator_3_eq));  // open: gt, lt
  and and_4 (and_4_out, WB_Syscall, comparator_3_eq);
  and and_5 (and_5_out, WB_Syscall, ~comparator_3_eq);  // AND_Gate
  Multiplexer #(.select(1), .width(5), .disabled("Z"), .enable("false")) multiplexer_13 (
    .in0(WB_IR[20:16]), .in1(WB_IR[15:11]), .out(multiplexer_13_out), .sel(WB_RegDst));
  Register #(.width(32), .trigger("rising"), .Select("low")) register_1 (
    .D(id_ex_3_b_out), .Q(LedData), .clk(and_4_out));  // open: en, clr
  Register #(.width(1), .trigger("rising"), .Select("low")) register_2 (
    .D(and_5_out), .en(and_5_out), .Q(Pause), .clk(CLK), .clr(Go));
  Multiplexer #(.select(1), .width(32), .disabled("Z"), .enable("false")) multiplexer_14 (
    .in0(id_ex_3_alu_out), .in1(id_ex_3_md_out), .out(multiplexer_14_out), .sel(WB_MemtoReg));
  assign bit_extender_3_out = {{16{1'b0}}, multiplexer_14_out[15:0]};  // Bit_Extender bit_extender_3
  assign bit_extender_4_out = {{16{1'b0}}, multiplexer_14_out[31:16]};  // Bit_Extender bit_extender_4
  not not_3 (not_3_out, Pause);
  Counter #(.width(16), .max('hffff), .ongoal("wrap"), .trigger("rising"), .behavior("new")) counter_2 (
    .count(not_3_out), .Q(\总周期数 ), .clk(CLK));  // open: load, D, carry, clr, preset, down
  not not_4 (not_4_out, Pause);
  Counter #(.width(16), .max('hffff), .ongoal("wrap"), .trigger("rising"), .behavior("new")) counter_3 (
    .count(not_4_out), .Q(\无条件分支数 ), .clk(or_6_out));  // open: load, D, carry, clr, preset, down
  or or_6 (or_6_out, EX_JR, EX_JMP);
  Multiplexer #(.select(1), .width(32), .disabled("Z"), .enable("false")) multiplexer_15 (
    .in0(bit_extender_3_out), .in1(bit_extender_4_out), .out(multiplexer_15_out), .sel(id_ex_3_alu_out[1]));
  Multiplexer #(.select(1), .width(32), .disabled("Z"), .enable("false")) multiplexer_16 (
    .in0(multiplexer_14_out), .in1(multiplexer_15_out), .out(multiplexer_16_out), .sel(WB_LHU));
  not not_5 (not_5_out, Pause);
  Counter #(.width(16), .max('hffff), .ongoal("wrap"), .trigger("falling"), .behavior("new")) counter_4 (
    .count(not_5_out), .Q(counter_4_q), .clk(and_6_out));  // open: load, D, carry, clr, preset, down
  and and_6 (and_6_out, BraCLR, ~conflict);  // AND_Gate
  Counter #(.width(16), .max('hffff), .ongoal("wrap"), .trigger("falling"), .behavior("new")) counter_5 (
    .Q(counter_5_q), .clk(conflict));  // open: load, D, count, carry, clr, preset, down
  Adder #(.width(16)) adder_5 (.a(counter_4_q), .b(counter_5_q), .out(\插入气泡数 ));  // open: cin, cout
  not not_6 (not_6_out, or_7_out);
  or or_7 (or_7_out, Pause, conflict);
  Counter #(.width(16), .max('hffff), .ongoal("wrap"), .trigger("falling"), .behavior("new")) counter_6 (
    .count(not_6_out), .Q(\条件分支成功数 ), .clk(Branch));  // open: load, D, carry, clr, preset, down

  // Other names for the same wires on the sheet: index[25:0] = EX_IR[25:0]; PC31_28[3:0] = EX_PC[31:28];
  //   ID_IR[5:0] = Func; OP[5:0] = ID_IR[31:26]; MEM_PC[31:0] = M_PC; MemW = MemWrite

  // Notes on the sheet:
  //   中断源
  //   时空图监测，可删除
  //   中断等待指示
  //   rd
  //   rd
  //   数码管输出
  //   指令存储器
  //   contents of rom_1 (hex, n*v repeats v):
  //   20110001 8000c05 20110001 20120002 20130003 8000c09 20110001 20120002 20130003 8000c0d 20110001
  //   20120002 20130003 8000c11 20110001 20120002 20130003 c000cb8 20100001 20110001 118fc0 112020
  //   20020022 c 118882 12200001 8000c15 112020 20020022 c 20110001 118880 112020 20020022 c 12200001
  //   8000c1f 20110001 118fc0 112020 20020022 c 1188c3 112020 20020022 c 118903 112020 20020022 c 118903
  //   112020 20020022 c 118903 112020 20020022 c 118903 112020 20020022 c 118903 112020 20020022 c 118903
  //   112020 20020022 c 118903 112020 20020022 c 20100001 109fc0 139fc3 8021 2012000c 24160003 26100001
  //   3210000f 20080008 20090001 139900 2709825 132020 20020022 c 1094022 1500fff9 22100001 2018000f
  //   2188024 108700 20080008 20090001 139902 2709825 132021 20020022 c 1094022 1500fff9 108702 2c9b022
  //   12c00001 8000c50 4020 1084027 84400 3508ffff 82021 20020022 c 2010ffff 20110000 ae300000 22100001
  //   22310004 ae300000 22100001 22310004 ae300000 22100001 22310004 ae300000 22100001 22310004 ae300000
  //   22100001 22310004 ae300000 22100001 22310004 ae300000 22100001 22310004 ae300000 22100001 22310004
  //   ae300000 22100001 22310004 ae300000 22100001 22310004 ae300000 22100001 22310004 ae300000 22100001
  //   22310004 ae300000 22100001 22310004 ae300000 22100001 22310004 ae300000 22100001 22310004 ae300000
  //   22100001 22310004 22100001 8020 2011003c 8e130000 8e340000 274402a 11000002 ae330000 ae140000
  //   2231fffc 1611fff8 102020 20020022 c 22100004 2011003c 1611fff2 20020032 c 20100000 22100001 102020
  //   20020022 c 22100002 102020 20020022 c 22100003 102020 20020022 c 22100004 102020 20020022 c 22100005
  //   102020 20020022 c 22100006 102020 20020022 c 22100007 102020 20020022 c 22100008 102020 20020022
  //   20020022 c 3e00008
  //   控制位
  //   rs
  //   rt
  //   sa
  //   流水调试日志用
  //   暂停节拍，不能为0
  //   JMP
  //   JR
  //   OP
  //   Func
  //   Imm
  //   戳工具置1进入计数暂停模式，ctrl+k时钟自动运行到对应节拍暂停
  //   ctrl+k关闭时钟连续运行，将控制位置零，进入单步调试模式调试
  //   可计数暂停的时钟源
  //   为方便自动评测，需要输出流水线各段保存的PC值，注意是PC不是PC+4，另外ID段寄存器写入信息，Mem段内存写入信息也要输出
  //   rt
  //   rd
endmodule

module \源寄存器使用情况  (
  input  OP0,
  input  OP1,
  input  OP2,
  input  OP3,
  input  OP4,
  input  OP5,
  input  F0,
  input  F1,
  input  F2,
  input  F3,
  input  F4,
  input  F5,
  output R1_USED,
  output R2_USED
);

  wire and_1_out, and_2_out, and_3_out, and_4_out, and_5_out, and_6_out, and_7_out, and_8_out, and_9_out,
       and_10_out, and_11_out, and_12_out, and_13_out, and_14_out, and_15_out, and_16_out, and_17_out,
       not_1_out, not_2_out, not_3_out, not_4_out, not_5_out, not_6_out, not_7_out, not_8_out, not_9_out,
       not_10_out, not_11_out, not_12_out, not_13_out, not_14_out, not_15_out, not_16_out, not_17_out,
       not_18_out, not_19_out, not_20_out, not_21_out, not_22_out, not_23_out, not_24_out, not_25_out,
       not_26_out, not_27_out, not_28_out, not_29_out, not_30_out, not_31_out, not_32_out, not_33_out,
       not_34_out, not_35_out, not_36_out, not_37_out, not_38_out, not_39_out, not_40_out, not_41_out,
       not_42_out, not_43_out, not_44_out, not_45_out, not_46_out, not_47_out, not_48_out, not_49_out,
       not_50_out, not_51_out, not_52_out, not_53_out, not_54_out, not_55_out, not_56_out, not_57_out,
       not_58_out, not_59_out, not_60_out, not_61_out, not_62_out, not_63_out, not_64_out, not_65_out,
       not_66_out, not_67_out, not_68_out, not_69_out, not_70_out, not_71_out, not_72_out, not_73_out,
       not_74_out, not_75_out, not_76_out, not_77_out, not_78_out, not_79_out, not_80_out, not_81_out,
       not_82_out, not_83_out, not_84_out, not_85_out, not_86_out, not_87_out, not_88_out, not_89_out,
       not_90_out, not_91_out;

  not not_1 (not_1_out, OP0);
  not not_2 (not_2_out, OP1);
  not not_3 (not_3_out, OP4);
  not not_4 (not_4_out, OP5);
  not not_5 (not_5_out, F1);
  not not_6 (not_6_out, F3);
  not not_7 (not_7_out, F4);
  not not_8 (not_8_out, OP0);
  not not_9 (not_9_out, OP1);
  not not_10 (not_10_out, OP4);
  not not_11 (not_11_out, OP5);
  not not_12 (not_12_out, F0);
  not not_13 (not_13_out, F1);
  not not_14 (not_14_out, F4);
  not not_15 (not_15_out, F5);
  not not_16 (not_16_out, OP0);
  not not_17 (not_17_out, OP1);
  not not_18 (not_18_out, OP4);
  not not_19 (not_19_out, OP5);
  not not_20 (not_20_out, F2);
  not not_21 (not_21_out, F4);
  not not_22 (not_22_out, OP0);
  not not_23 (not_23_out, OP1);
  not not_24 (not_24_out, OP4);
  not not_25 (not_25_out, OP5);
  not not_26 (not_26_out, F3);
  not not_27 (not_27_out, F4);
  not not_28 (not_28_out, OP0);
  not not_29 (not_29_out, OP2);
  not not_30 (not_30_out, OP4);
  not not_31 (not_31_out, OP5);
  not not_32 (not_32_out, OP1);
  not not_33 (not_33_out, OP4);
  not not_34 (not_34_out, OP5);
  not not_35 (not_35_out, OP1);
  not not_36 (not_36_out, OP4);
  not not_37 (not_37_out, OP5);
  not not_38 (not_38_out, OP1);
  not not_39 (not_39_out, OP3);
  not not_40 (not_40_out, OP4);
  not not_41 (not_41_out, OP3);
  not not_42 (not_42_out, OP4);
  not not_43 (not_43_out, OP5);
  not not_44 (not_44_out, OP2);
  not not_45 (not_45_out, OP4);
  not not_46 (not_46_out, OP0);
  not not_47 (not_47_out, OP1);
  not not_48 (not_48_out, OP3);
  not not_49 (not_49_out, OP4);
  not not_50 (not_50_out, OP5);
  not not_51 (not_51_out, F0);
  not not_52 (not_52_out, F2);
  not not_53 (not_53_out, F3);
  not not_54 (not_54_out, F4);
  not not_55 (not_55_out, OP0);
  not not_56 (not_56_out, OP1);
  not not_57 (not_57_out, OP3);
  not not_58 (not_58_out, OP4);
  not not_59 (not_59_out, OP5);
  not not_60 (not_60_out, F1);
  not not_61 (not_61_out, F3);
  not not_62 (not_62_out, F4);
  not not_63 (not_63_out, OP0);
  not not_64 (not_64_out, OP1);
  not not_65 (not_65_out, OP3);
  not not_66 (not_66_out, OP4);
  not not_67 (not_67_out, OP5);
  not not_68 (not_68_out, F0);
  not not_69 (not_69_out, F1);
  not not_70 (not_70_out, F4);
  not not_71 (not_71_out, F5);
  not not_72 (not_72_out, OP0);
  not not_73 (not_73_out, OP1);
  not not_74 (not_74_out, OP3);
  not not_75 (not_75_out, OP4);
  not not_76 (not_76_out, OP5);
  not not_77 (not_77_out, F2);
  not not_78 (not_78_out, F4);
  not not_79 (not_79_out, OP0);
  not not_80 (not_80_out, OP1);
  not not_81 (not_81_out, OP3);
  not not_82 (not_82_out, OP4);
  not not_83 (not_83_out, OP5);
  not not_84 (not_84_out, F3);
  not not_85 (not_85_out, F4);
  not not_86 (not_86_out, OP1);
  not not_87 (not_87_out, OP3);
  not not_88 (not_88_out, OP4);
  not not_89 (not_89_out, OP5);
  not not_90 (not_90_out, OP2);
  not not_91 (not_91_out, OP4);
  and and_1 (and_1_out, not_1_out, not_2_out, not_3_out, not_4_out, not_5_out, not_6_out, not_7_out, F5);
  and and_2 (and_2_out, not_8_out, not_9_out, not_10_out, not_11_out, not_12_out, not_13_out, F3, not_14_out, not_15_out);
  and and_3 (and_3_out, not_16_out, not_17_out, not_18_out, not_19_out, F1, not_20_out, not_21_out, F5);
  and and_4 (and_4_out, not_22_out, not_23_out, not_24_out, not_25_out, F0, F1, F2, not_26_out, not_27_out);
  and and_5 (and_5_out, not_28_out, not_29_out, OP3, not_30_out, not_31_out);
  and and_6 (and_6_out, not_32_out, OP3, not_33_out, not_34_out);
  and and_7 (and_7_out, not_35_out, OP2, not_36_out, not_37_out);
  and and_8 (and_8_out, OP0, not_38_out, OP2, not_39_out, not_40_out);
  and and_9 (and_9_out, OP0, OP2, not_41_out, not_42_out, not_43_out);
  and and_10 (and_10_out, OP0, OP1, not_44_out, not_45_out, OP5);
  and and_11 (and_11_out, not_46_out, not_47_out, not_48_out, not_49_out, not_50_out, not_51_out, not_52_out, not_53_out, not_54_out);
  and and_12 (and_12_out, not_55_out, not_56_out, not_57_out, not_58_out, not_59_out, not_60_out, not_61_out, not_62_out, F5);
  and and_13 (and_13_out, not_63_out, not_64_out, not_65_out, not_66_out, not_67_out, not_68_out, not_69_out, F2, F3, not_70_out, not_71_out);
  and and_14 (and_14_out, not_72_out, not_73_out, not_74_out, not_75_out, not_76_out, F1, not_77_out, not_78_out, F5);
  and and_15 (and_15_out, not_79_out, not_80_out, not_81_out, not_82_out, not_83_out, F0, F1, not_84_out, not_85_out);
  and and_16 (and_16_out, not_86_out, OP2, not_87_out, not_88_out, not_89_out);
  and and_17 (and_17_out, OP0, OP1, not_90_out, OP3, not_91_out, OP5);
  or or_1 (R1_USED, and_1_out, and_2_out, and_3_out, and_4_out, and_5_out, and_6_out, and_7_out, and_8_out, and_9_out, and_10_out);
  or or_2 (R2_USED, and_11_out, and_12_out, and_13_out, and_14_out, and_15_out, and_16_out, and_17_out);
endmodule

// 数字相关处理逻辑
module \数据相关处理逻辑  (
  input  R1_Used,
  input  R2_Used,
  input  [4:0] R1_num,
  input  EX_RegWrite,
  input  [4:0] EX_WriteReg_num,
  input  [4:0] R2_num,
  input  [4:0] MEM_WriteReg_num,
  input  MEM_RegWrite,
  output conflict
);

  wire and_1_out, and_2_out, and_3_out, and_4_out, comparator_1_eq, comparator_2_eq, comparator_3_eq,
       comparator_4_eq, comparator_5_eq, comparator_6_eq;

  Comparator #(.width(5), .mode("twosComplement")) comparator_1 (
    .a({5{1'b0}}), .b(R2_num), .eq(comparator_1_eq));  // open: gt, lt
  Comparator #(.width(5), .mode("twosComplement")) comparator_2 (
    .a({5{1'b0}}), .b(R1_num), .eq(comparator_2_eq));  // open: gt, lt
  Comparator #(.width(5), .mode("twosComplement")) comparator_3 (
    .a(R1_num), .b(EX_WriteReg_num), .eq(comparator_3_eq));  // open: gt, lt
  Comparator #(.width(5), .mode("twosComplement")) comparator_4 (
    .a(R2_num), .b(EX_WriteReg_num), .eq(comparator_4_eq));  // open: gt, lt
  Comparator #(.width(5), .mode("twosComplement")) comparator_5 (
    .a(R1_num), .b(MEM_WriteReg_num), .eq(comparator_5_eq));  // open: gt, lt
  Comparator #(.width(5), .mode("twosComplement")) comparator_6 (
    .a(R2_num), .b(MEM_WriteReg_num), .eq(comparator_6_eq));  // open: gt, lt
  and and_1 (and_1_out, ~comparator_2_eq, comparator_3_eq, EX_RegWrite, R1_Used);  // AND_Gate
  and and_2 (and_2_out, ~comparator_1_eq, comparator_4_eq, EX_RegWrite, R2_Used);  // AND_Gate
  or or_1 (conflict, and_1_out, and_2_out, and_3_out, and_4_out);
  and and_3 (and_3_out, ~comparator_2_eq, comparator_5_eq, MEM_RegWrite, R1_Used);  // AND_Gate
  and and_4 (and_4_out, ~comparator_1_eq, comparator_6_eq, MEM_RegWrite, R2_Used);  // AND_Gate
endmodule
module \重定向流水线  (
  output RegWrite,
  output MemWrite,
  output [31:0] IF_PC,
  output [31:0] ID_PC,
  output [31:0] EX_PC,
  output [31:0] M_PC,
  output [31:0] WB_PC,
  output [31:0] RDin,
  output [31:0] MDin,
  output [31:0] LedData
);

  wire AluSrc, and_2_out, and_3_out, and_4_out, and_5_out, and_6_out, BEQ, BGTZ, BNE, BraCLR, Branch, CLK,
       clock_1_out, clock_2_out, comparator_1_eq, comparator_1_lt, comparator_2_lt, comparator_3_eq,
       d_ff_1_q, EX_AluSrc, EX_BEQ, EX_BGTZ, EX_BNE, EX_JAL, EX_JMP, EX_JR, EX_MemToReg, EX_RegDst, EX_RegW,
       EX_SRAV, Go, id_ex_1_lhu_2, id_ex_1_memwrite_2, id_ex_1_syscall_out, id_ex_2_lhu_2,
       id_ex_2_memtoreg_out, id_ex_2_syscall_out, IR1, IR2, IR3, JAL, JMP, JR, LHU, LoadUse, MEM_JAL,
       MEM_RegDst, MEM_RegW, MemToReg, MemWrite_t, mips_alu_1_equal, nand_1_out, not_1_out, not_2_out,
       not_3_out, not_4_out, not_5_out, or_2_out, or_3_out, or_4_out, or_5_out, or_6_out, or_8_out, or_9_out,
       Pause, RegDst, RegW, RST, SignedExt, SRAV, SUBU, Syscall, W1, W2, W3, WB_JAL, WB_LHU, WB_MemtoReg,
       WB_RegDst, WB_Syscall, \源寄存器使用情况_1_r1_used , \源寄存器使用情况_1_r2_used ;
  wire [1:0] R1_OP, R2_OP, \重定向相关处理逻辑_1_r1_ex , \重定向相关处理逻辑_1_r2_ex ;
  wire [3:0] AluOP, EX_AluOP;
  wire [4:0] id_ex_1_shamt_2, multiplexer_1_out, multiplexer_2_out, multiplexer_3_out, multiplexer_4_out,
       multiplexer_6_out, multiplexer_13_out, multiplexer_15_out, R1_num, R2_num;
  wire [5:0] Func;
  wire [12:0] CNT_num;
  wire [15:0] \LoadUse次数 , \总周期数 , \无条件分支数 , \条件分支成功数 ;
  wire [31:0] adder_1_out, adder_2_out, adder_3_out, adder_4_out, bit_extender_1_out, bit_extender_2_out,
       bit_extender_3_out, bit_extender_4_out, controlled_buffer_1_out, EX_IR, id_ex_1_a_out, id_ex_1_b_out,
       id_ex_1_imm_out, id_ex_2_a_out, id_ex_3_a_out, id_ex_3_alu_out, id_ex_3_b_out, id_ex_3_md_out, IF_IR,
       MEM_Alu, MEM_IR, mips_alu_1_result, mips_regifile_1_r1, mips_regifile_1_r2, multiplexer_5_out,
       multiplexer_10_out, multiplexer_11_out, multiplexer_12_out, multiplexer_14_out, multiplexer_16_out,
       multiplexer_17_out, multiplexer_18_out, ram_1_data, target_offset, WB_IR;
  wire [31:6] ID_IR;

  Button \u_总复位  (.out(RST));
  Button _1 (.out(IR1));
  Button _2 (.out(IR2));
  Button _3 (.out(IR3));
  // Probe on \总周期数 
  // Probe on \总周期数 
  Button \u_继续运行  (.out(Go));
  LED #(.active("true")) led_1 (.in(W1));
  LED #(.active("true")) led_2 (.in(W2));
  LED #(.active("true")) led_3 (.in(W3));
  Hex_Digit_Display hex_digit_display_1 (.value(LedData[31:28]));  // open: dp
  // Probe on IF_PC[19:0]
  // Mips_Probe mips_probe_1: pin names not known; wires that end beside it: IF_IR
  Adder #(.width(32)) adder_1 (.a(32'h4), .b(EX_PC), .out(adder_1_out));  // open: cin, cout
  Multiplexer #(.select(1), .width(5), .disabled("Z"), .enable("false")) multiplexer_1 (
    .in0(EX_IR[20:16]), .in1(EX_IR[15:11]), .out(multiplexer_1_out), .sel(EX_RegDst));
  Multiplexer #(.select(1), .width(5), .disabled("Z"), .enable("false")) multiplexer_2 (
    .in0(multiplexer_1_out), .in1({5{1'b1}}), .out(multiplexer_2_out), .sel(MEM_JAL));
  Multiplexer #(.select(1), .width(5), .disabled("Z"), .enable("false")) multiplexer_3 (
    .in0(MEM_IR[20:16]), .in1(MEM_IR[15:11]), .out(multiplexer_3_out), .sel(MEM_RegDst));
  Multiplexer #(.select(1), .width(5), .disabled("Z"), .enable("false")) multiplexer_4 (
    .in0(multiplexer_3_out), .in1({5{1'b1}}), .out(multiplexer_4_out), .sel(EX_JAL));
  Hex_Digit_Display hex_digit_display_2 (.value(LedData[27:24]));  // open: dp
  Hex_Digit_Display hex_digit_display_3 (.value(LedData[23:20]));  // open: dp
  // Probe on ID_PC[19:0]
  // Mips_Probe mips_probe_2: pin names not known; wires that end beside it: {ID_IR, Func}
  assign controlled_buffer_1_out = EX_JR ? multiplexer_11_out : 32'bz;  // Controlled_Buffer controlled_buffer_1
  assign controlled_buffer_1_out = EX_JMP ? {EX_PC[31:28], EX_IR[25:0], 2'b00} : 32'bz;  // Controlled_Buffer controlled_buffer_2
  Adder #(.width(32)) adder_2 (.a(adder_1_out), .b(target_offset), .out(adder_2_out));  // open: cin, cout
  assign controlled_buffer_1_out = Branch ? adder_2_out : 32'bz;  // Controlled_Buffer controlled_buffer_3
  \源寄存器使用情况  \u_源寄存器使用情况_1  (
    .OP0(ID_IR[26]), .OP1(ID_IR[27]), .OP2(ID_IR[28]), .OP3(ID_IR[29]), .OP4(ID_IR[30]), .OP5(ID_IR[31]),
    .F0(Func[0]), .F1(Func[1]), .F2(Func[2]), .F3(Func[3]), .F4(Func[4]), .F5(Func[5]),
    .R1_USED(\源寄存器使用情况_1_r1_used ), .R2_USED(\源寄存器使用情况_1_r2_used ));
  Hex_Digit_Display hex_digit_display_4 (.value(LedData[15:12]));  // open: dp
  Hex_Digit_Display hex_digit_display_5 (.value(LedData[19:16]));  // open: dp
  Hex_Digit_Display hex_digit_display_6 (.value(LedData[7:4]));  // open: dp
  Hex_Digit_Display hex_digit_display_7 (.value(LedData[11:8]));  // open: dp
  Clock #(.highDuration(1), .lowDuration(1)) clock_1 (.out(clock_1_out));
  // Probe on EX_PC[19:0]
  // Mips_Probe mips_probe_3: pin names not known; wires that end beside it: clock_1_out, EX_IR, CLK
  Multiplexer #(.select(1), .width(32), .disabled("Z"), .enable("false")) multiplexer_5 (
    .in0(adder_3_out), .in1(controlled_buffer_1_out), .out(multiplexer_5_out), .sel(BraCLR));
  or or_1 (BraCLR, EX_JMP, EX_JR, Branch);
  \重定向相关处理逻辑  \u_重定向相关处理逻辑_1  (
    .R1_Used(\源寄存器使用情况_1_r1_used ), .R2_Used(\源寄存器使用情况_1_r2_used ), .R1_num(R1_num), .EX_RegWrite(EX_RegW),
    .EX_WriteReg_num(multiplexer_2_out), .R2_num(R2_num), .MEM_WriteReg_num(multiplexer_4_out),
    .MEM_RegWrite(MEM_RegW), .R1_EX(\重定向相关处理逻辑_1_r1_ex [0]), .R2_EX(\重定向相关处理逻辑_1_r2_ex [0]),
    .R1_MEM(\重定向相关处理逻辑_1_r1_ex [1]), .R2_MEM(\重定向相关处理逻辑_1_r2_ex [1]));
  Hex_Digit_Display hex_digit_display_8 (.value(LedData[3:0]));  // open: dp
  or or_2 (or_2_out, LoadUse, Pause);
  not not_1 (not_1_out, or_2_out);
  Register #(.width(2), .trigger("rising"), .Select("low")) register_1 (
    .D(\重定向相关处理逻辑_1_r1_ex ), .Q(R1_OP), .clk(CLK));  // open: en, clr
  Register #(.width(2), .trigger("rising"), .Select("low")) register_2 (
    .D(\重定向相关处理逻辑_1_r2_ex ), .Q(R2_OP), .clk(CLK));  // open: en, clr
  // Probe on \总周期数 
  // Probe on M_PC[19:0]
  // Mips_Probe mips_probe_4: pin names not known; wires that end beside it: MEM_IR
  Register #(.width(32), .trigger("rising"), .Select("low")) PC (
    .D(multiplexer_5_out), .en(not_1_out), .Q(IF_PC), .clk(CLK));  // open: clr
  // Probe on \总周期数 
  // Probe on \无条件分支数 
  // Probe on \条件分支成功数 
  // Probe on \LoadUse次数 
  // Probe on \LoadUse次数 
  Adder #(.width(32)) adder_3 (.a(32'h4), .b(IF_PC), .out(adder_3_out));  // open: cin, cout
  and and_1 (LoadUse, EX_MemToReg, or_3_out);
  or or_3 (or_3_out, \重定向相关处理逻辑_1_r1_ex [0], \重定向相关处理逻辑_1_r2_ex [0]);
  // Probe on IF_PC[11:0]
  // Probe on WB_PC[19:0]
  // Mips_Probe mips_probe_5: pin names not known; wires that end beside it: WB_IR
  ROM #(.addrWidth(10), .dataWidth(32), .Select("high")) rom_1 (.addr(IF_PC[11:2]), .data(IF_IR));
  // Probe on ID_PC[11:0]
  // Probe on EX_PC[11:0]
  IF_ID if_id_1 (
    .CLK(CLK), .CLR(or_4_out), .Stall(or_5_out), .IR_in(IF_IR), .IR_out({ID_IR, Func}), .PC_in(IF_PC),
    .PC_out(ID_PC));  // open: PreditJump, PreditJump_2
  or or_4 (or_4_out, BraCLR, RST);
  // Probe on M_PC[11:0]
  D_Flip_Flop #(.trigger("high"), .Pre_Clr_Positions("LEGACY"), .NegatePresetClear("false"), .enable("true"), .NewFFLayout("false")) d_ff_1 (.Q(d_ff_1_q));  // open: clk, D, Qn, preset, en, reset
  // Probe on 13'hc
  Adder #(.width(32)) adder_4 (.a(32'h4), .b(WB_PC), .out(adder_4_out));  // open: cin, cout
  or or_5 (or_5_out, LoadUse, Pause);
  // Probe on WB_PC[11:0]
  Comparator #(.width(13), .mode("twosComplement")) comparator_1 (
    .a(CNT_num), .b(13'hc), .eq(comparator_1_eq), .lt(comparator_1_lt));  // open: gt
  Clock #(.highDuration(1), .lowDuration(1)) clock_2 (.out(clock_2_out));
  \单周期硬布线控制器  \u_单周期硬布线控制器_1  (
    .Func(Func), .OP(ID_IR[31:26]), .ALU_OP(AluOP), .MemToReg(MemToReg), .MemWrite(MemWrite_t),
    .ALU_SRC(AluSrc), .RegWrite(RegW), .SysCALL(Syscall), .SignedExt(SignedExt), .RegDst(RegDst), .JR(JR),
    .JMP(JMP), .Beq(BEQ), .JAL(JAL), .Bne(BNE), .SRAV(SRAV), .SUBU(SUBU), .LHU(LHU), .BGTZ(BGTZ));  // open: ERET, MFC0, MTC0, MF
  Multiplexer #(.select(1), .width(5), .disabled("Z"), .enable("false")) multiplexer_6 (
    .in0({5{1'b1}}), .in1(multiplexer_15_out), .out(multiplexer_6_out), .sel(not_2_out));
  not not_2 (not_2_out, WB_JAL);
  nand nand_1 (nand_1_out, d_ff_1_q, comparator_1_eq);
  Counter #(.width(13), .max('h1fff), .ongoal("stay"), .trigger("rising"), .behavior("old")) counter_1 (
    .count(comparator_1_lt), .Q(CNT_num), .clk(clock_2_out));  // open: load, D, carry, clr, preset
  Multiplexer #(.select(1), .width(5), .disabled("Z"), .enable("false")) multiplexer_7 (
    .in0(ID_IR[25:21]), .in1(5'b00010), .out(R1_num), .sel(Syscall));
  Multiplexer #(.select(1), .width(5), .disabled("Z"), .enable("false")) multiplexer_8 (
    .in0(ID_IR[20:16]), .in1(5'b00100), .out(R2_num), .sel(Syscall));
  Multiplexer #(.select(1), .width(32), .disabled("Z"), .enable("false")) multiplexer_9 (
    .in0(multiplexer_18_out), .in1(adder_4_out), .out(RDin), .sel(WB_JAL));
  assign bit_extender_1_out = {{16{1'b0}}, {ID_IR[15:6], Func}};  // Bit_Extender bit_extender_1
  assign bit_extender_2_out = {{16{ID_IR[15]}}, {ID_IR[15:6], Func}};  // Bit_Extender bit_extender_2
  assign CLK = nand_1_out ? clock_2_out : 1'bz;  // Controlled_Buffer controlled_buffer_4
  MIPS_Regifile mips_regifile_1 (
    .Din(RDin), .Clk(CLK), .R1(mips_regifile_1_r1), .R2(mips_regifile_1_r2), .WE(RegWrite),
    .W_num(multiplexer_6_out), .R1_num(R1_num), .R2_num(R2_num));
  Multiplexer #(.select(1), .width(32), .disabled("Z"), .enable("false")) multiplexer_10 (
    .in0(bit_extender_1_out), .in1(bit_extender_2_out), .out(multiplexer_10_out), .sel(SignedExt));
  Pull_Resistor #(.pull(1)) pull_resistor_1 (.node(CLK));
  ID_EX id_ex_1 (
    .RegDst_in(RegDst), .IR_in({ID_IR, Func}), .Syscall_in(Syscall), .RegWrite_in(RegW), .PC_in(ID_PC),
    .JMP_in(JMP), .MemToReg_in(MemToReg), .A_in(mips_regifile_1_r1), .JR_in(JR), .AluOP_in(AluOP),
    .JAL_in(JAL), .AluSrc_in(AluSrc), .B_in(mips_regifile_1_r2), .SignedExt_in(SignedExt),
    .MemWrite(MemWrite_t), .Imm_in(multiplexer_10_out), .Beq_in(BEQ), .Shamt(ID_IR[10:6]), .Bne_in(BNE),
    .CLK(CLK), .RegDst_out(EX_RegDst), .IR_out(EX_IR), .Syscall_out(id_ex_1_syscall_out),
    .RegWrite_out(EX_RegW), .PC_out(EX_PC), .JMP_out(EX_JMP), .MemToReg_out(EX_MemToReg),
    .A_out(id_ex_1_a_out), .JR_out(EX_JR), .AluOP_out(EX_AluOP), .JAL_out(EX_JAL), .AluSrc_out(EX_AluSrc),
    .B_out(id_ex_1_b_out), .MemWrite_2(id_ex_1_memwrite_2), .Imm_out(id_ex_1_imm_out), .Beq_out(EX_BEQ),
    .Shamt_2(id_ex_1_shamt_2), .Bne_out(EX_BNE), .CLR(or_6_out), .Stall(Pause), .BGTZ(BGTZ),
    .BGTZ_2(EX_BGTZ), .SUBU(SUBU), .LHU(LHU), .LHU_2(id_ex_1_lhu_2), .SRAV(SRAV), .SRAV_2(EX_SRAV));  // open: SignedExt_out, SUBU_2, MD_in, MD_out, ALU_in, ALU_out, PreditJump, PreditJump_2
  or or_6 (or_6_out, BraCLR, LoadUse, RST);
  Shifter #(.width(32), .shift("ll")) shifter_1 (.in(id_ex_1_imm_out), .\dist (5'b00010), .out(target_offset));
  Multiplexer #(.select(2), .width(32), .disabled("Z"), .enable("false")) multiplexer_11 (
    .in0(id_ex_1_a_out), .in1(MEM_Alu), .in2(RDin), .in3(MEM_Alu), .out(multiplexer_11_out), .sel(R1_OP));
  Multiplexer #(.select(1), .width(32), .disabled("Z"), .enable("false")) multiplexer_12 (
    .in0(multiplexer_14_out), .in1(id_ex_1_imm_out), .out(multiplexer_12_out), .sel(EX_AluSrc));
  Comparator #(.width(32), .mode("twosComplement")) comparator_2 (
    .a({32{1'b0}}), .b(multiplexer_11_out), .lt(comparator_2_lt));  // open: gt, eq
  Multiplexer #(.select(1), .width(5), .disabled("Z"), .enable("false")) multiplexer_13 (
    .in0(id_ex_1_shamt_2), .in1(multiplexer_11_out[4:0]), .out(multiplexer_13_out), .sel(EX_SRAV));
  and and_2 (and_2_out, EX_BEQ, mips_alu_1_equal);
  and and_3 (and_3_out, EX_BNE, ~mips_alu_1_equal);  // AND_Gate
  and and_4 (and_4_out, EX_BGTZ, comparator_2_lt);
  MIPS_ALU mips_alu_1 (
    .X(multiplexer_11_out), .Y(multiplexer_12_out), .AluOP(EX_AluOP), .Equal(mips_alu_1_equal),
    .Result(mips_alu_1_result), .shamt(multiplexer_13_out));  // open: Result_2
  Multiplexer #(.select(2), .width(32), .disabled("Z"), .enable("false")) multiplexer_14 (
    .in0(id_ex_1_b_out), .in1(MEM_Alu), .in2(RDin), .in3(MEM_Alu), .out(multiplexer_14_out), .sel(R2_OP));
  or or_7 (Branch, and_2_out, and_3_out, and_4_out);
  ID_EX id_ex_2 (
    .RegDst_in(EX_RegDst), .IR_in(EX_IR), .Syscall_in(id_ex_1_syscall_out), .RegWrite_in(EX_RegW),
    .PC_in(EX_PC), .MemToReg_in(EX_MemToReg), .A_in(multiplexer_11_out), .JAL_in(EX_JAL),
    .B_in(multiplexer_14_out), .MemWrite(id_ex_1_memwrite_2), .CLK(CLK), .RegDst_out(MEM_RegDst),
    .IR_out(MEM_IR), .Syscall_out(id_ex_2_syscall_out), .RegWrite_out(MEM_RegW), .PC_out(M_PC),
    .MemToReg_out(id_ex_2_memtoreg_out), .A_out(id_ex_2_a_out), .JAL_out(MEM_JAL), .B_out(MDin),
    .MemWrite_2(MemWrite), .CLR(RST), .Stall(Pause), .LHU(id_ex_1_lhu_2), .LHU_2(id_ex_2_lhu_2),
    .ALU_in(mips_alu_1_result), .ALU_out(MEM_Alu));  // open: JMP_in, JR_in, AluOP_in, AluSrc_in, SignedExt_in, Imm_in, Beq_in, Shamt, Bne_in, JMP_out, JR_out, AluOP_out, AluSrc_out, SignedExt_out, Imm_out, Beq_out, Shamt_2, Bne_out, BGTZ, BGTZ_2, SUBU, SUBU_2, SRAV, SRAV_2, MD_in, MD_out, PreditJump, PreditJump_2
  RAM #(.addrWidth(10), .dataWidth(32), .bus("separate"), .Select("high")) ram_1 (
    .addr(MEM_Alu[11:2]), .din(MDin), .data(ram_1_data), .str(MemWrite), .clk(CLK));  // open: sel, ld, clr
  ID_EX id_ex_3 (
    .RegDst_in(MEM_RegDst), .IR_in(MEM_IR), .Syscall_in(id_ex_2_syscall_out), .RegWrite_in(MEM_RegW),
    .PC_in(M_PC), .MemToReg_in(id_ex_2_memtoreg_out), .A_in(id_ex_2_a_out), .JAL_in(MEM_JAL), .B_in(MDin),
    .CLK(CLK), .RegDst_out(WB_RegDst), .IR_out(WB_IR), .Syscall_out(WB_Syscall), .RegWrite_out(RegWrite),
    .PC_out(WB_PC), .MemToReg_out(WB_MemtoReg), .A_out(id_ex_3_a_out), .JAL_out(WB_JAL),
    .B_out(id_ex_3_b_out), .CLR(RST), .Stall(Pause), .LHU(id_ex_2_lhu_2), .LHU_2(WB_LHU), .MD_in(ram_1_data),
    .MD_out(id_ex_3_md_out), .ALU_in(MEM_Alu), .ALU_out(id_ex_3_alu_out));  // open: JMP_in, JR_in, AluOP_in, AluSrc_in, SignedExt_in, MemWrite, Imm_in, Beq_in, Shamt, Bne_in, JMP_out, JR_out, AluOP_out, AluSrc_out, SignedExt_out, MemWrite_2, Imm_out, Beq_out, Shamt_2, Bne_out, BGTZ, BGTZ_2, SUBU, SUBU_2, SRAV, SRAV_2, PreditJump, PreditJump_2
  not not_3 (not_3_out, Pause);
  Counter #(.width(16), .max('hffff), .ongoal("wrap"), .trigger("rising"), .behavior("new")) counter_2 (
    .count(not_3_out), .Q(\总周期数 ), .clk(CLK));  // open: load, D, carry, clr, preset, down
  not not_4 (not_4_out, Pause);
  Counter #(.width(16), .max('hffff), .ongoal("wrap"), .trigger("rising"), .behavior("new")) counter_3 (
    .count(not_4_out), .Q(\无条件分支数 ), .clk(or_8_out));  // open: load, D, carry, clr, preset, down
  or or_8 (or_8_out, EX_JR, EX_JMP);
  Comparator #(.width(32), .mode("unsigned")) comparator_3 (
    .a(32'h22), .b(id_ex_3_a_out), .eq(comparator_3_eq));  // open: gt, lt
  Multiplexer #(.select(1), .width(5), .disabled("Z"), .enable("false")) multiplexer_15 (
    .in0(WB_IR[20:16]), .in1(WB_IR[15:11]), .out(multiplexer_15_out), .sel(WB_RegDst));
  Register #(.width(32), .trigger("rising"), .Select("low")) register_3 (
    .D(id_ex_3_b_out), .Q(LedData), .clk(and_5_out));  // open: en, clr
  and and_5 (and_5_out, WB_Syscall, comparator_3_eq);
  and and_6 (and_6_out, WB_Syscall, ~comparator_3_eq);  // AND_Gate
  Register #(.width(1), .trigger("rising"), .Select("low")) register_4 (
    .D(and_6_out), .en(and_6_out), .Q(Pause), .clk(CLK), .clr(Go));
  Multiplexer #(.select(1), .width(32), .disabled("Z"), .enable("false")) multiplexer_16 (
    .in0(id_ex_3_alu_out), .in1(id_ex_3_md_out), .out(multiplexer_16_out), .sel(WB_MemtoReg));
  Counter #(.width(16), .max('hffff), .ongoal("wrap"), .trigger("falling"), .behavior("new")) counter_4 (
    .Q(\LoadUse次数 ), .clk(LoadUse));  // open: load, D, count, carry, clr, preset, down
  assign bit_extender_3_out = {{16{1'b0}}, multiplexer_16_out[15:0]};  // Bit_Extender bit_extender_3
  Multiplexer #(.select(1), .width(32), .disabled("Z"), .enable("false")) multiplexer_17 (
    .in0(bit_extender_3_out), .in1(bit_extender_4_out), .out(multiplexer_17_out), .sel(id_ex_3_alu_out[1]));
  assign bit_extender_4_out = {{16{1'b0}}, multiplexer_16_out[31:16]};  // Bit_Extender bit_extender_4
  Multiplexer #(.select(1), .width(32), .disabled("Z"), .enable("false")) multiplexer_18 (
    .in0(multiplexer_16_out), .in1(multiplexer_17_out), .out(multiplexer_18_out), .sel(WB_LHU));
  or or_9 (or_9_out, Pause, LoadUse);
  not not_5 (not_5_out, or_9_out);
  Counter #(.width(16), .max('hffff), .ongoal("wrap"), .trigger("falling"), .behavior("new")) counter_5 (
    .count(not_5_out), .Q(\条件分支成功数 ), .clk(Branch));  // open: load, D, carry, clr, preset, down

  // Other names for the same wires on the sheet: index[25:0] = EX_IR[25:0]; PC31_28[3:0] = EX_PC[31:28];
  //   ID_IR[5:0] = Func; OP[5:0] = ID_IR[31:26]; MEM_PC[31:0] = M_PC; MemW = MemWrite; 插入气泡数[15:0] = \LoadUse次数 

  // Notes on the sheet:
  //   中断源
  //   时空图监测，可删除
  //   中断等待指示
  //   rd
  //   rd
  //   数码管输出
  //   指令存储器
  //   contents of rom_1 (hex, n*v repeats v):
  //   20090000 200b0010 34118483 20120404 118c00 129400 36318281 22520404 ad310000 2328820 21290004
  //   216bffff 1560fffb 200b0020 20090000 95310000 112020 20020022 c 21290002 216bffff 1560fff9 2002000a c
  //   控制位
  //   流水调试日志用
  //   暂停节拍，不能为0
  //   JMP
  //   JR
  //   OP
  //   Func
  //   rs
  //   rt
  //   Imm
  //   sa
  //   可计数暂停的时钟源
  //   为方便自动评测，需要输出流水线各段保存的PC值，注意是PC不是PC+4，另外ID段寄存器写入信息，Mem段内存写入信息也要输出
  //   rt
  //   rd
endmodule

// 重定向处理逻辑
module \重定向相关处理逻辑  (
  input  R1_Used,
  input  R2_Used,
  input  [4:0] R1_num,
  input  EX_RegWrite,
  input  [4:0] EX_WriteReg_num,
  input  [4:0] R2_num,
  input  [4:0] MEM_WriteReg_num,
  input  MEM_RegWrite,
  output R1_EX,
  output R2_EX,
  output R1_MEM,
  output R2_MEM
);

  wire comparator_1_eq, comparator_2_eq, comparator_3_eq, comparator_4_eq, comparator_5_eq, comparator_6_eq;

  Comparator #(.width(5), .mode("twosComplement")) comparator_1 (
    .a({5{1'b0}}), .b(R2_num), .eq(comparator_1_eq));  // open: gt, lt
  Comparator #(.width(5), .mode("twosComplement")) comparator_2 (
    .a({5{1'b0}}), .b(R1_num), .eq(comparator_2_eq));  // open: gt, lt
  Comparator #(.width(5), .mode("twosComplement")) comparator_3 (
    .a(R1_num), .b(EX_WriteReg_num), .eq(comparator_3_eq));  // open: gt, lt
  Comparator #(.width(5), .mode("twosComplement")) comparator_4 (
    .a(R2_num), .b(EX_WriteReg_num), .eq(comparator_4_eq));  // open: gt, lt
  Comparator #(.width(5), .mode("twosComplement")) comparator_5 (
    .a(R1_num), .b(MEM_WriteReg_num), .eq(comparator_5_eq));  // open: gt, lt
  Comparator #(.width(5), .mode("twosComplement")) comparator_6 (
    .a(R2_num), .b(MEM_WriteReg_num), .eq(comparator_6_eq));  // open: gt, lt
  and and_1 (R1_EX, ~comparator_2_eq, comparator_3_eq, EX_RegWrite, R1_Used);  // AND_Gate
  and and_2 (R2_EX, ~comparator_1_eq, comparator_4_eq, EX_RegWrite, R2_Used);  // AND_Gate
  and and_3 (R1_MEM, ~comparator_2_eq, comparator_5_eq, MEM_RegWrite, R1_Used);  // AND_Gate
  and and_4 (R2_MEM, ~comparator_1_eq, comparator_6_eq, MEM_RegWrite, R2_Used);  // AND_Gate
endmodule

module \中断按键参考电路  (
  input  \同步清零信号 ,
  output \与中断屏蔽位与 
);

  wire \_1号中断_out , and_1_out, clock_1_out, d_ff_1_q, or_1_out, or_2_out;

  Clock #(.highDuration(1), .lowDuration(1)) clock_1 (.out(clock_1_out));
  Button \_1号中断  (.out(\_1号中断_out ));
  LED #(.active("true")) \_1号中断等待指示灯  (.in(or_1_out));
  or or_1 (or_1_out, \与中断屏蔽位与 , d_ff_1_q);
  D_Flip_Flop #(.trigger("rising"), .Pre_Clr_Positions("LEGACY"), .NegatePresetClear("false"), .enable("true"), .NewFFLayout("false")) d_ff_1 (
    .clk(\_1号中断_out ), .D(1'b1), .Q(d_ff_1_q), .reset(\与中断屏蔽位与 ));  // open: Qn, preset, en
  or or_2 (or_2_out, d_ff_1_q, \与中断屏蔽位与 );
  and and_1 (and_1_out, or_2_out, ~\同步清零信号 );  // AND_Gate
  D_Flip_Flop #(.trigger("rising"), .Pre_Clr_Positions("LEGACY"), .NegatePresetClear("false"), .enable("true"), .NewFFLayout("false")) IR1 (
    .clk(clock_1_out), .D(and_1_out), .Q(\与中断屏蔽位与 ));  // open: Qn, preset, en, reset

  // Notes on the sheet:
  //   中断信号采样参考电路
  //   Reset 
endmodule

module \单周期MIPS_单级中断  (
  input  IR1,
  input  IR2,
  input  IR3,
  output RegWrite,
  output MemWrite,
  output [31:0] PC,
  output [31:0] IR,
  output [31:0] RDin,
  output [31:0] MDin,
  output [31:0] LedData
);

  wire AluSrc, and_1_out, and_2_out, and_3_out, and_5_out, and_6_out, and_7_out, and_8_out, BEQ, BNE, Branch,
       CLK, Clr1, Clr2, Clr3, comparator_1_eq, comparator_2_eq, comparator_3_eq, comparator_4_eq,
       comparator_5_eq, d_ff_1_q, d_ff_2_q, d_ff_3_q, ERET, Go, IR1_q, IR1_t, IR2_q, IR2_t, IR3_q, IR3_t,
       IRA, IRB, IRC, JAL, JMP, JR, MemToReg, mips_alu_1_equal, not_1_out, not_2_out, not_3_out, not_4_out,
       or_4_out, or_5_out, or_6_out, or_7_out, or_9_out, or_12_out, Pause, priority_encoder_1_gs, RegDst,
       register_1_q, register_2_q, SignedExt, Syscall, W1, W2, W3, \接收中断 ;
  wire [1:0] IntNo;
  wire [3:0] AluOP;
  wire [4:0] multiplexer_4_out, multiplexer_5_out, multiplexer_7_out, multiplexer_8_out;
  wire [15:0] \总周期数 ;
  wire [31:0] adder_1_out, adder_2_out, bit_extender_1_out, bit_extender_2_out, controlled_buffer_1_out,
       EPCin, EPCout, mips_alu_1_result, multiplexer_1_out, multiplexer_3_out, multiplexer_10_out,
       multiplexer_11_out, multiplexer_12_out, ram_1_data, target_offset, v0, \中断入口地址 ;

  Clock #(.highDuration(1), .lowDuration(1)) clock_1 (.out(CLK));
  Button _1 ();  // open: out
  Button _2 ();  // open: out
  Button _3 ();  // open: out
  Button \u_继续运行  (.out(Go));
  LED #(.active("true")) led_1 (.in(W1));
  LED #(.active("true")) led_2 (.in(W2));
  LED #(.active("true")) led_3 (.in(W3));
  Hex_Digit_Display hex_digit_display_1 (.value(LedData[31:28]));  // open: dp
  assign controlled_buffer_1_out = JR ? v0 : 32'bz;  // Controlled_Buffer controlled_buffer_1
  assign controlled_buffer_1_out = JMP ? {PC[31:28], IR[25:0], 2'b00} : 32'bz;  // Controlled_Buffer controlled_buffer_2
  assign controlled_buffer_1_out = Branch ? adder_1_out : 32'bz;  // Controlled_Buffer controlled_buffer_3
  Adder #(.width(32)) adder_1 (.a(adder_2_out), .b(target_offset), .out(adder_1_out));  // open: cin, cout
  or or_1 (W1, IR1_q, d_ff_1_q);
  or or_2 (W2, IR2_q, d_ff_2_q);
  or or_3 (W3, IR3_q, d_ff_3_q);
  Hex_Digit_Display hex_digit_display_2 (.value(LedData[27:24]));  // open: dp
  Hex_Digit_Display hex_digit_display_3 (.value(LedData[23:20]));  // open: dp
  or or_4 (or_4_out, JMP, JR, Branch);
  D_Flip_Flop #(.trigger("rising"), .Pre_Clr_Positions("LEGACY"), .NegatePresetClear("false"), .enable("true"), .NewFFLayout("false")) d_ff_1 (
    .clk(IRA), .D(1'b1), .Q(d_ff_1_q), .reset(IR1_q));  // open: Qn, preset, en
  D_Flip_Flop #(.trigger("rising"), .Pre_Clr_Positions("LEGACY"), .NegatePresetClear("false"), .enable("true"), .NewFFLayout("false")) d_ff_2 (
    .clk(IRB), .D(1'b1), .Q(d_ff_2_q), .reset(IR2_q));  // open: Qn, preset, en
  D_Flip_Flop #(.trigger("rising"), .Pre_Clr_Positions("LEGACY"), .NegatePresetClear("false"), .enable("true"), .NewFFLayout("false")) d_ff_3 (
    .clk(IRC), .D(1'b1), .Q(d_ff_3_q), .reset(IR3_q));  // open: Qn, preset, en
  Hex_Digit_Display hex_digit_display_4 (.value(LedData[15:12]));  // open: dp
  Hex_Digit_Display hex_digit_display_5 (.value(LedData[19:16]));  // open: dp
  Multiplexer #(.select(1), .width(32), .disabled("Z"), .enable("false")) multiplexer_1 (
    .in0(adder_2_out), .in1(controlled_buffer_1_out), .out(multiplexer_1_out), .sel(or_4_out));
  or or_5 (or_5_out, d_ff_1_q, IR1_q);
  or or_6 (or_6_out, d_ff_2_q, IR2_q);
  or or_7 (or_7_out, d_ff_3_q, IR3_q);
  Hex_Digit_Display hex_digit_display_6 (.value(LedData[11:8]));  // open: dp
  Hex_Digit_Display hex_digit_display_7 (.value(LedData[7:4]));  // open: dp
  // Probe on \总周期数 
  Multiplexer #(.select(1), .width(32), .disabled("Z"), .enable("false")) multiplexer_2 (
    .in0(multiplexer_1_out), .in1(EPCout), .out(EPCin), .sel(ERET));
  and and_1 (and_1_out, or_5_out, ~Clr1);  // AND_Gate
  and and_2 (and_2_out, or_6_out, ~Clr2);  // AND_Gate
  and and_3 (and_3_out, or_7_out, ~Clr3);  // AND_Gate
  Hex_Digit_Display hex_digit_display_8 (.value(LedData[3:0]));  // open: dp
  Multiplexer #(.select(1), .width(32), .disabled("Z"), .enable("false")) multiplexer_3 (
    .in0(EPCin), .in1(\中断入口地址 ), .out(multiplexer_3_out), .sel(\接收中断 ));
  D_Flip_Flop #(.trigger("rising"), .Pre_Clr_Positions("LEGACY"), .NegatePresetClear("false"), .enable("true"), .NewFFLayout("false")) u_IR1 (
    .clk(CLK), .D(and_1_out), .Q(IR1_q));  // open: Qn, preset, en, reset
  D_Flip_Flop #(.trigger("rising"), .Pre_Clr_Positions("LEGACY"), .NegatePresetClear("false"), .enable("true"), .NewFFLayout("false")) u_IR2 (
    .clk(CLK), .D(and_2_out), .Q(IR2_q));  // open: Qn, preset, en, reset
  D_Flip_Flop #(.trigger("rising"), .Pre_Clr_Positions("LEGACY"), .NegatePresetClear("false"), .enable("true"), .NewFFLayout("false")) u_IR3 (
    .clk(CLK), .D(and_3_out), .Q(IR3_q));  // open: Qn, preset, en, reset
  not not_1 (not_1_out, Pause);
  Register #(.width(32), .trigger("rising"), .Select("low")) u_PC (
    .D(multiplexer_3_out), .en(not_1_out), .Q(PC), .clk(CLK));  // open: clr
  Priority_Encoder #(.select(2), .disabled("Z")) priority_encoder_1 (
    .in0(1'b0), .in1(IR1_q), .in2(IR2_q), .in3(IR3_q), .out(IntNo), .gs(priority_encoder_1_gs));  // open: en_out, en_in
  or or_8 (IR1_t, IR1, IRA);
  or or_9 (or_9_out, \接收中断 , ERET);
  Decoder #(.select(2), .tristate("false"), .disabled(0), .enable("true")) decoder_1 (
    .out1(Clr1), .out2(Clr2), .out3(Clr3), .sel(IntNo), .en(register_1_q));  // open: out0
  Register #(.width(1), .trigger("rising"), .Select("low")) register_1 (
    .D(\接收中断 ), .Q(register_1_q), .clk(CLK));  // open: en, clr
  Register #(.width(32), .trigger("rising"), .Select("low")) EPC (
    .D(EPCin), .en(\接收中断 ), .Q(EPCout), .clk(CLK));  // open: clr
  or or_10 (IR2_t, IR2, IRB);
  Adder #(.width(32)) adder_2 (.a(PC), .b(32'h4), .out(adder_2_out));  // open: cin, cout
  and and_4 (\接收中断 , priority_encoder_1_gs, ~register_2_q);  // AND_Gate
  Register #(.width(1), .trigger("rising"), .Select("low")) register_2 (
    .D(\接收中断 ), .en(or_9_out), .Q(register_2_q), .clk(CLK));  // open: clr
  // Mips_Probe mips_probe_1: pin names not known; wires that end beside it: IR
  ROM #(.addrWidth(10), .dataWidth(32), .Select("high")) rom_1 (.addr(PC[11:2]), .data(IR));
  or or_11 (IR3_t, IR3, IRC);
  Multiplexer #(.select(1), .width(5), .disabled("Z"), .enable("false")) multiplexer_4 (
    .in0(IR[20:16]), .in1(IR[15:11]), .out(multiplexer_4_out), .sel(RegDst));
  not not_2 (not_2_out, Syscall);
  Multiplexer #(.select(1), .width(5), .disabled("Z"), .enable("false")) multiplexer_5 (
    .in0({5{1'b1}}), .in1(multiplexer_4_out), .out(multiplexer_5_out), .sel(not_3_out));
  not not_3 (not_3_out, JAL);
  assign bit_extender_1_out = {{16{1'b0}}, IR[15:0]};  // Bit_Extender bit_extender_1
  assign bit_extender_2_out = {{16{IR[15]}}, IR[15:0]};  // Bit_Extender bit_extender_2
  Multiplexer #(.select(2), .width(32), .disabled("Z"), .enable("false")) multiplexer_6 (
    .in1(32'h30ac), .in2(32'h3150), .in3(32'h31f4), .out(\中断入口地址 ), .sel(IntNo));  // open: in0
  not not_4 (not_4_out, Pause);
  Counter #(.width(16), .max('hffff), .ongoal("wrap"), .trigger("rising"), .behavior("new")) counter_1 (
    .count(not_4_out), .Q(\总周期数 ), .clk(CLK));  // open: load, D, carry, clr, preset, down
  Multiplexer #(.select(1), .width(5), .disabled("Z"), .enable("false")) multiplexer_7 (
    .in0(5'b00010), .in1(IR[25:21]), .out(multiplexer_7_out), .sel(not_2_out));
  Multiplexer #(.select(1), .width(5), .disabled("Z"), .enable("false")) multiplexer_8 (
    .in0(5'b00100), .in1(IR[20:16]), .out(multiplexer_8_out), .sel(not_2_out));
  Multiplexer #(.select(1), .width(32), .disabled("Z"), .enable("false")) multiplexer_9 (
    .in0(multiplexer_12_out), .in1(adder_2_out), .out(RDin), .sel(JAL));
  Multiplexer #(.select(1), .width(32), .disabled("Z"), .enable("false")) multiplexer_10 (
    .in0(bit_extender_1_out), .in1(bit_extender_2_out), .out(multiplexer_10_out), .sel(SignedExt));
  MIPS_Regifile mips_regifile_1 (
    .Din(RDin), .Clk(CLK), .R1(v0), .R2(MDin), .WE(RegWrite), .W_num(multiplexer_5_out),
    .R1_num(multiplexer_7_out), .R2_num(multiplexer_8_out));
  Multiplexer #(.select(1), .width(32), .disabled("Z"), .enable("false")) multiplexer_11 (
    .in0(MDin), .in1(multiplexer_10_out), .out(multiplexer_11_out), .sel(AluSrc));
  Shifter #(.width(32), .shift("ll")) shifter_1 (.in(multiplexer_10_out), .\dist (5'b00010), .out(target_offset));
  and and_5 (and_5_out, Syscall, comparator_1_eq);
  Comparator #(.width(32), .mode("unsigned")) comparator_1 (.a(32'h22), .b(v0), .eq(comparator_1_eq));  // open: gt, lt
  and and_6 (and_6_out, Syscall, ~comparator_1_eq);  // AND_Gate
  MIPS_ALU mips_alu_1 (
    .X(v0), .Y(multiplexer_11_out), .AluOP(AluOP), .Equal(mips_alu_1_equal), .Result(mips_alu_1_result),
    .shamt(IR[10:6]));  // open: Result_2
  Register #(.width(32), .trigger("falling"), .Select("low")) register_3 (
    .D(MDin), .Q(LedData), .clk(and_5_out));  // open: en, clr
  Register #(.width(1), .trigger("rising"), .Select("low")) register_4 (
    .D(and_6_out), .en(and_6_out), .Q(Pause), .clk(CLK), .clr(Go));
  \单周期硬布线控制器  \u_单周期硬布线控制器_1  (
    .Func(IR[5:0]), .OP(IR[31:26]), .ALU_OP(AluOP), .MemToReg(MemToReg), .MemWrite(MemWrite),
    .ALU_SRC(AluSrc), .RegWrite(RegWrite), .SysCALL(Syscall), .SignedExt(SignedExt), .RegDst(RegDst),
    .JR(JR), .JMP(JMP), .Beq(BEQ), .JAL(JAL), .Bne(BNE), .ERET(ERET));  // open: MFC0, MTC0, MF, SRAV, SUBU, LHU, BGTZ
  and and_7 (and_7_out, BEQ, mips_alu_1_equal);
  and and_8 (and_8_out, BNE, ~mips_alu_1_equal);  // AND_Gate
  RAM #(.addrWidth(10), .dataWidth(32), .bus("separate"), .Select("high")) ram_1 (
    .addr(mips_alu_1_result[11:2]), .din(MDin), .data(ram_1_data), .str(MemWrite), .clk(CLK));  // open: sel, ld, clr
  Comparator #(.width(16), .mode("twosComplement")) comparator_2 (
    .a(16'h23b), .b(\总周期数 ), .eq(comparator_2_eq));  // open: gt, lt
  or or_12 (or_12_out, comparator_2_eq, comparator_3_eq);
  Comparator #(.width(16), .mode("twosComplement")) comparator_3 (
    .a(\总周期数 ), .b(16'h1), .eq(comparator_3_eq));  // open: gt, lt
  Comparator #(.width(16), .mode("twosComplement")) comparator_4 (
    .a(\总周期数 ), .b(16'h4), .eq(comparator_4_eq));  // open: gt, lt
  Comparator #(.width(16), .mode("twosComplement")) comparator_5 (
    .a(\总周期数 ), .b(16'h7), .eq(comparator_5_eq));  // open: gt, lt
  or or_13 (Branch, and_7_out, and_8_out);
  Multiplexer #(.select(1), .width(32), .disabled("Z"), .enable("false")) multiplexer_12 (
    .in0(mips_alu_1_result), .in1(ram_1_data), .out(multiplexer_12_out), .sel(MemToReg));
  Pull_Resistor #(.pull(0)) pull_resistor_1 (.node(IRA));
  assign IRA = or_12_out ? ~CLK : 1'bz;  // Controlled_Inverter controlled_inverter_1
  Pull_Resistor #(.pull(0)) pull_resistor_2 (.node(IRB));
  assign IRB = comparator_4_eq ? ~CLK : 1'bz;  // Controlled_Inverter controlled_inverter_2
  Pull_Resistor #(.pull(0)) pull_resistor_3 (.node(IRC));
  assign IRC = comparator_5_eq ? ~CLK : 1'bz;  // Controlled_Inverter controlled_inverter_3

  // Other names for the same wires on the sheet: a0[31:0] = MDin; Func[5:0] = IR[5:0]; index[25:0] = IR[25:0];
  //   Shamt[4:0] = IR[10:6]; OP[5:0] = IR[31:26]; PC31_28[3:0] = PC[31:28]

  // Notes on the sheet:
  //   中断源
  //   中断等待指示
  //   总复位信号应将除ROM以外所有存储组件全部清零
  //   数码管输出
  //   数码管输出应该用寄存器锁存，否则显示数据只能一闪而过
  //   Reset 
  //   Reset 
  //   Reset 
  //   指令存储器
  //   指令字
  //   contents of rom_1 (hex, n*v repeats v):
  //   201d07d0 20100001 109fc0 139fc3 8021 2012000c 24160008 26100001 3210000f 20080008 20090001 139900
  //   2709825 132020 20020022 c 1094022 1500fff9 22100001 2018000f 2188024 108700 20080008 20090001 139902
  //   2709825 132021 20020022 c 1094022 1500fff9 108702 2c9b022 12c00001 8000c07 4020 1084027 84400
  //   3508ffff 82021 20020022 c 8000c01 afa20000 23bd0004 afa40000 23bd0004 afb00000 23bd0004 afb30000
  //   23bd0004 afb40000 23bd0004 afb50000 23bd0004 afb60000 23bd0004 20160001 20140003 20150001 168020
  //   108100 2149825 132020 20020022 c 1600fffa 295a022 1680fff7 23bdfffc 8fb60000 23bdfffc 8fb50000
  //   23bdfffc 8fb40000 23bdfffc 8fb30000 23bdfffc 8fb00000 23bdfffc 8fa40000 23bdfffc 8fa20000 42000018
  //   afa20000 23bd0004 afa40000 23bd0004 afb00000 23bd0004 afb30000 23bd0004 afb40000 23bd0004 afb50000
  //   23bd0004 afb60000 23bd0004 20160002 20140003 20150001 168020 108100 2149825 132020 20020022 c
  //   1600fffa 295a022 1680fff7 23bdfffc 8fb60000 23bdfffc 8fb50000 23bdfffc 8fb40000 23bdfffc 8fb30000
  //   23bdfffc 8fb00000 23bdfffc 8fa40000 23bdfffc 8fa20000 42000018 afa20000 23bd0004 afa40000 23bd0004
  //   afb00000 23bd0004 afb30000 23bd0004 afb40000 23bd0004 afb50000 23bd0004 afb60000 23bd0004 20160003
  //   20140003 20150001 168020 108100 2149825 132020 20020022 c 1600fffa 295a022 1680fff7 23bdfffc
  //   8fb60000 23bdfffc 8fb50000 23bdfffc 8fb40000 23bdfffc 8fb30000 23bdfffc 8fb00000 23bdfffc 8fa40000
  //   23bdfffc 8fa20000 42000018
  //   OP
  //   Func
  //   rs
  //   rt
  //   rd
  //   sa
  //   Imm
  //   instr_index
  //   为方便自动评测，需要输出PC，IR，寄存器堆写如数据RDin
  //   RAM写使能MemWrite、RAM写入数据MDin等信号
  //   Beq
  //   JMP
  //   JR
  //   Bne
  //   OP
  //   JAL
  //   Func
  //   Syscall
  //   单级中断测试信号模拟器
  //   MemToReg
  //   MemWrite
  //   AluOP
  //   AluSrcB
  //   RegWrite
  //   RegDst
endmodule

module \单周期MIPS_多级中断  (
  input  IR1,
  input  IR2,
  input  IR3,
  output RegWrite,
  output MemWrite,
  output [31:0] PC,
  output [31:0] IR,
  output [31:0] RDin,
  output [31:0] MDin,
  output [31:0] LedData
);

  wire AluSrc, and_1_out, and_2_out, and_3_out, and_5_out, and_6_out, and_7_out, and_8_out, BEQ, BNE, Branch,
       CLK, Clr1, Clr2, Clr3, comparator_1_lt, comparator_2_eq, comparator_3_eq, comparator_4_eq,
       comparator_5_eq, comparator_6_eq, comparator_7_eq, d_ff_1_q, d_ff_2_q, d_ff_3_q, ERET, Go, IE_q,
       IR1_q, IR1_t, IR2_q, IR2_t, IR3_q, IR3_t, IRA, IRB, IRC, JAL, JMP, JR, MemToReg, MFC0,
       mips_alu_1_equal, MTC0, not_1_out, not_2_out, not_3_out, not_4_out, or_4_out, or_5_out, or_6_out,
       or_7_out, or_8_out, or_10_out, or_12_out, or_14_out, or_15_out, or_16_out, Pause,
       priority_encoder_1_gs, RegDst, register_1_q, SignedExt, Syscall, W1, W2, W3, \接收中断 ;
  wire [1:0] IntNo, IntNo_2_q, IntNo_3_q, IntNo_4_q, IntNow, multiplexer_14_out, multiplexer_17_out,
       multiplexer_18_out, multiplexer_19_out;
  wire [3:0] AluOP;
  wire [4:0] multiplexer_6_out, multiplexer_8_out, multiplexer_10_out, multiplexer_11_out;
  wire [15:0] \总周期数 ;
  wire [31:0] adder_1_out, adder_2_out, bit_extender_1_out, bit_extender_2_out, controlled_buffer_1_out,
       EPC2_q, EPC3_q, EPC4_q, EPCin, EPCout, mips_alu_1_result, multiplexer_1_out, multiplexer_3_out,
       multiplexer_4_out, multiplexer_5_out, multiplexer_7_out, multiplexer_9_out, multiplexer_13_out,
       multiplexer_15_out, multiplexer_20_out, ram_1_data, target_offset, v0, \中断入口地址 ;

  Clock #(.highDuration(1), .lowDuration(1)) clock_1 (.out(CLK));
  Button _1 ();  // open: out
  Button _2 ();  // open: out
  Button _3 ();  // open: out
  Button \u_继续运行  (.out(Go));
  LED #(.active("true")) led_1 (.in(W1));
  LED #(.active("true")) led_2 (.in(W2));
  LED #(.active("true")) led_3 (.in(W3));
  or or_1 (W1, IR1_q, d_ff_1_q);
  or or_2 (W2, IR2_q, d_ff_2_q);
  or or_3 (W3, IR3_q, d_ff_3_q);
  Hex_Digit_Display hex_digit_display_1 (.value(LedData[31:28]));  // open: dp
  assign controlled_buffer_1_out = JR ? v0 : 32'bz;  // Controlled_Buffer controlled_buffer_1
  assign controlled_buffer_1_out = JMP ? {PC[31:28], IR[25:0], 2'b00} : 32'bz;  // Controlled_Buffer controlled_buffer_2
  Adder #(.width(32)) adder_1 (.a(adder_2_out), .b(target_offset), .out(adder_1_out));  // open: cin, cout
  assign controlled_buffer_1_out = Branch ? adder_1_out : 32'bz;  // Controlled_Buffer controlled_buffer_3
  D_Flip_Flop #(.trigger("rising"), .Pre_Clr_Positions("LEGACY"), .NegatePresetClear("false"), .enable("true"), .NewFFLayout("false")) d_ff_1 (
    .clk(IRA), .D(1'b1), .Q(d_ff_1_q), .reset(IR1_q));  // open: Qn, preset, en
  D_Flip_Flop #(.trigger("rising"), .Pre_Clr_Positions("LEGACY"), .NegatePresetClear("false"), .enable("true"), .NewFFLayout("false")) d_ff_2 (
    .clk(IRB), .D(1'b1), .Q(d_ff_2_q), .reset(IR2_q));  // open: Qn, preset, en
  D_Flip_Flop #(.trigger("rising"), .Pre_Clr_Positions("LEGACY"), .NegatePresetClear("false"), .enable("true"), .NewFFLayout("false")) d_ff_3 (
    .clk(IRC), .D(1'b1), .Q(d_ff_3_q), .reset(IR3_q));  // open: Qn, preset, en
  Hex_Digit_Display hex_digit_display_2 (.value(LedData[27:24]));  // open: dp
  Hex_Digit_Display hex_digit_display_3 (.value(LedData[23:20]));  // open: dp
  or or_4 (or_4_out, JMP, JR, Branch);
  or or_5 (or_5_out, d_ff_1_q, IR1_q);
  or or_6 (or_6_out, d_ff_2_q, IR2_q);
  or or_7 (or_7_out, d_ff_3_q, IR3_q);
  Hex_Digit_Display hex_digit_display_4 (.value(LedData[19:16]));  // open: dp
  Hex_Digit_Display hex_digit_display_5 (.value(LedData[15:12]));  // open: dp
  Multiplexer #(.select(1), .width(32), .disabled("Z"), .enable("false")) multiplexer_1 (
    .in0(adder_2_out), .in1(controlled_buffer_1_out), .out(multiplexer_1_out), .sel(or_4_out));
  and and_1 (and_1_out, or_5_out, ~Clr1);  // AND_Gate
  and and_2 (and_2_out, or_6_out, ~Clr2);  // AND_Gate
  and and_3 (and_3_out, or_7_out, ~Clr3);  // AND_Gate
  Hex_Digit_Display hex_digit_display_6 (.value(LedData[11:8]));  // open: dp
  Hex_Digit_Display hex_digit_display_7 (.value(LedData[7:4]));  // open: dp
  // Probe on \总周期数 
  Multiplexer #(.select(1), .width(32), .disabled("Z"), .enable("false")) multiplexer_2 (
    .in0(multiplexer_1_out), .in1(EPCout), .out(EPCin), .sel(ERET));
  D_Flip_Flop #(.trigger("rising"), .Pre_Clr_Positions("LEGACY"), .NegatePresetClear("false"), .enable("true"), .NewFFLayout("false")) u_IR1 (
    .clk(CLK), .D(and_1_out), .Q(IR1_q));  // open: Qn, preset, en, reset
  D_Flip_Flop #(.trigger("rising"), .Pre_Clr_Positions("LEGACY"), .NegatePresetClear("false"), .enable("true"), .NewFFLayout("false")) u_IR2 (
    .clk(CLK), .D(and_2_out), .Q(IR2_q));  // open: Qn, preset, en, reset
  D_Flip_Flop #(.trigger("rising"), .Pre_Clr_Positions("LEGACY"), .NegatePresetClear("false"), .enable("true"), .NewFFLayout("false")) u_IR3 (
    .clk(CLK), .D(and_3_out), .Q(IR3_q));  // open: Qn, preset, en, reset
  Hex_Digit_Display hex_digit_display_8 (.value(LedData[3:0]));  // open: dp
  Multiplexer #(.select(1), .width(32), .disabled("Z"), .enable("false")) multiplexer_3 (
    .in0(EPCin), .in1(\中断入口地址 ), .out(multiplexer_3_out), .sel(\接收中断 ));
  Priority_Encoder #(.select(2), .disabled("Z")) priority_encoder_1 (
    .in0(1'b0), .in1(IR1_q), .in2(IR2_q), .in3(IR3_q), .out(IntNo), .gs(priority_encoder_1_gs));  // open: en_out, en_in
  not not_1 (not_1_out, Pause);
  Register #(.width(32), .trigger("rising"), .Select("low")) u_PC (
    .D(multiplexer_3_out), .en(not_1_out), .Q(PC), .clk(CLK));  // open: clr
  or or_8 (or_8_out, \接收中断 , ERET);
  or or_9 (IR1_t, IR1, IRA);
  or or_10 (or_10_out, \接收中断 , ERET, MTC0, MFC0);
  Multiplexer #(.select(1), .width(32), .disabled("Z"), .enable("false")) multiplexer_4 (
    .in0(EPCin), .in1(EPC2_q), .out(multiplexer_4_out), .sel(ERET));
  Register #(.width(32), .trigger("rising"), .Select("low")) EPC1 (
    .D(multiplexer_4_out), .en(or_8_out), .Q(EPCout), .clk(CLK));  // open: clr
  or or_11 (IR2_t, IR2, IRB);
  Adder #(.width(32)) adder_2 (.a(PC), .b(32'h4), .out(adder_2_out));  // open: cin, cout
  Comparator #(.width(2), .mode("unsigned")) comparator_1 (
    .a(IntNow), .b(IntNo), .lt(comparator_1_lt));  // open: gt, eq
  or or_12 (or_12_out, \接收中断 , MTC0);
  Register #(.width(1), .trigger("rising"), .Select("low")) IE (
    .D(or_12_out), .en(or_10_out), .Q(IE_q), .clk(CLK));  // open: clr
  Multiplexer #(.select(1), .width(32), .disabled("Z"), .enable("false")) multiplexer_5 (
    .in0(EPCout), .in1(EPC3_q), .out(multiplexer_5_out), .sel(ERET));
  // Mips_Probe mips_probe_1: pin names not known; wires that end beside it: IR
  ROM #(.addrWidth(10), .dataWidth(32), .Select("high")) rom_1 (.addr(PC[11:2]), .data(IR));
  and and_4 (\接收中断 , comparator_1_lt, priority_encoder_1_gs, ~IE_q);  // AND_Gate
  Register #(.width(32), .trigger("rising"), .Select("low")) EPC2 (
    .D(multiplexer_5_out), .en(or_8_out), .Q(EPC2_q), .clk(CLK));  // open: clr
  or or_13 (IR3_t, IR3, IRC);
  Multiplexer #(.select(1), .width(5), .disabled("Z"), .enable("false")) multiplexer_6 (
    .in0(IR[20:16]), .in1(IR[15:11]), .out(multiplexer_6_out), .sel(RegDst));
  Register #(.width(32), .trigger("rising"), .Select("low")) EPC3 (
    .D(multiplexer_7_out), .en(or_8_out), .Q(EPC3_q), .clk(CLK));  // open: clr
  Multiplexer #(.select(1), .width(32), .disabled("Z"), .enable("false")) multiplexer_7 (
    .in0(EPC2_q), .in1(EPC4_q), .out(multiplexer_7_out), .sel(ERET));
  not not_2 (not_2_out, Syscall);
  Multiplexer #(.select(1), .width(5), .disabled("Z"), .enable("false")) multiplexer_8 (
    .in0({5{1'b1}}), .in1(multiplexer_6_out), .out(multiplexer_8_out), .sel(not_3_out));
  not not_3 (not_3_out, JAL);
  assign bit_extender_1_out = {{16{1'b0}}, IR[15:0]};  // Bit_Extender bit_extender_1
  assign bit_extender_2_out = {{16{IR[15]}}, IR[15:0]};  // Bit_Extender bit_extender_2
  Register #(.width(1), .trigger("rising"), .Select("low")) register_1 (
    .D(\接收中断 ), .Q(register_1_q), .clk(CLK));  // open: en, clr
  Multiplexer #(.select(1), .width(32), .disabled("Z"), .enable("false")) multiplexer_9 (
    .in0(EPC3_q), .in1({32{1'b0}}), .out(multiplexer_9_out), .sel(ERET));
  Multiplexer #(.select(1), .width(5), .disabled("Z"), .enable("false")) multiplexer_10 (
    .in0(5'b00010), .in1(IR[25:21]), .out(multiplexer_10_out), .sel(not_2_out));
  Multiplexer #(.select(1), .width(5), .disabled("Z"), .enable("false")) multiplexer_11 (
    .in0(5'b00100), .in1(IR[20:16]), .out(multiplexer_11_out), .sel(not_2_out));
  Multiplexer #(.select(1), .width(32), .disabled("Z"), .enable("false")) multiplexer_12 (
    .in0(multiplexer_20_out), .in1(adder_2_out), .out(RDin), .sel(JAL));
  Multiplexer #(.select(1), .width(32), .disabled("Z"), .enable("false")) multiplexer_13 (
    .in0(bit_extender_1_out), .in1(bit_extender_2_out), .out(multiplexer_13_out), .sel(SignedExt));
  Decoder #(.select(2), .tristate("false"), .disabled(0), .enable("true")) decoder_1 (
    .out1(Clr1), .out2(Clr2), .out3(Clr3), .sel(IntNo), .en(register_1_q));  // open: out0
  Register #(.width(32), .trigger("rising"), .Select("low")) EPC4 (
    .D(multiplexer_9_out), .en(or_8_out), .Q(EPC4_q), .clk(CLK));  // open: clr
  MIPS_Regifile mips_regifile_1 (
    .Din(RDin), .Clk(CLK), .R1(v0), .R2(MDin), .WE(RegWrite), .W_num(multiplexer_8_out),
    .R1_num(multiplexer_10_out), .R2_num(multiplexer_11_out));
  or or_14 (or_14_out, \接收中断 , ERET);
  Multiplexer #(.select(1), .width(2), .disabled("Z"), .enable("false")) multiplexer_14 (
    .in0(IntNo), .in1(IntNo_2_q), .out(multiplexer_14_out), .sel(ERET));
  Multiplexer #(.select(1), .width(32), .disabled("Z"), .enable("false")) multiplexer_15 (
    .in0(MDin), .in1(multiplexer_13_out), .out(multiplexer_15_out), .sel(AluSrc));
  Shifter #(.width(32), .shift("ll")) shifter_1 (.in(multiplexer_13_out), .\dist (5'b00010), .out(target_offset));
  Register #(.width(2), .trigger("rising"), .Select("low")) IntNo_1 (
    .D(multiplexer_14_out), .en(or_14_out), .Q(IntNow), .clk(CLK));  // open: clr
  and and_5 (and_5_out, Syscall, comparator_2_eq);
  Comparator #(.width(32), .mode("unsigned")) comparator_2 (.a(32'h22), .b(v0), .eq(comparator_2_eq));  // open: gt, lt
  and and_6 (and_6_out, Syscall, ~comparator_2_eq);  // AND_Gate
  MIPS_ALU mips_alu_1 (
    .X(v0), .Y(multiplexer_15_out), .AluOP(AluOP), .Equal(mips_alu_1_equal), .Result(mips_alu_1_result),
    .shamt(IR[10:6]));  // open: Result_2
  Multiplexer #(.select(2), .width(32), .disabled("Z"), .enable("false")) multiplexer_16 (
    .in1(32'h30ac), .in2(32'h3158), .in3(32'h3204), .out(\中断入口地址 ), .sel(IntNo));  // open: in0
  Register #(.width(2), .trigger("rising"), .Select("low")) IntNo_2 (
    .D(multiplexer_17_out), .en(or_14_out), .Q(IntNo_2_q), .clk(CLK));  // open: clr
  Multiplexer #(.select(1), .width(2), .disabled("Z"), .enable("false")) multiplexer_17 (
    .in0(IntNow), .in1(IntNo_3_q), .out(multiplexer_17_out), .sel(ERET));
  Register #(.width(32), .trigger("falling"), .Select("low")) register_2 (
    .D(MDin), .Q(LedData), .clk(and_5_out));  // open: en, clr
  Register #(.width(1), .trigger("rising"), .Select("low")) register_3 (
    .D(and_6_out), .en(and_6_out), .Q(Pause), .clk(CLK), .clr(Go));
  Multiplexer #(.select(1), .width(2), .disabled("Z"), .enable("false")) multiplexer_18 (
    .in0(IntNo_2_q), .in1(IntNo_4_q), .out(multiplexer_18_out), .sel(ERET));
  Register #(.width(2), .trigger("rising"), .Select("low")) IntNo_3 (
    .D(multiplexer_18_out), .en(or_14_out), .Q(IntNo_3_q), .clk(CLK));  // open: clr
  Comparator #(.width(16), .mode("twosComplement")) comparator_3 (
    .a(\总周期数 ), .b(16'h7), .eq(comparator_3_eq));  // open: gt, lt
  Comparator #(.width(16), .mode("twosComplement")) comparator_4 (
    .a(\总周期数 ), .b(16'h241), .eq(comparator_4_eq));  // open: gt, lt
  and and_7 (and_7_out, BEQ, mips_alu_1_equal);
  and and_8 (and_8_out, BNE, ~mips_alu_1_equal);  // AND_Gate
  RAM #(.addrWidth(10), .dataWidth(32), .bus("separate"), .Select("high")) ram_1 (
    .addr(mips_alu_1_result[11:2]), .din(MDin), .data(ram_1_data), .str(MemWrite), .clk(CLK));  // open: sel, ld, clr
  \单周期硬布线控制器  \u_单周期硬布线控制器_1  (
    .Func(IR[5:0]), .OP(IR[31:26]), .ALU_OP(AluOP), .MemToReg(MemToReg), .MemWrite(MemWrite),
    .ALU_SRC(AluSrc), .RegWrite(RegWrite), .SysCALL(Syscall), .SignedExt(SignedExt), .RegDst(RegDst),
    .JR(JR), .JMP(JMP), .Beq(BEQ), .JAL(JAL), .Bne(BNE), .ERET(ERET), .MFC0(MFC0), .MTC0(MTC0), .MF(IR[25:21]));  // open: SRAV, SUBU, LHU, BGTZ
  Register #(.width(2), .trigger("rising"), .Select("low")) IntNo_4 (
    .D(multiplexer_19_out), .en(or_14_out), .Q(IntNo_4_q), .clk(CLK));  // open: clr
  Multiplexer #(.select(1), .width(2), .disabled("Z"), .enable("false")) multiplexer_19 (
    .in0(IntNo_3_q), .in1(2'b00), .out(multiplexer_19_out), .sel(ERET));
  Comparator #(.width(16), .mode("twosComplement")) comparator_5 (
    .a(16'h258), .b(\总周期数 ), .eq(comparator_5_eq));  // open: gt, lt
  or or_15 (or_15_out, comparator_5_eq, comparator_6_eq);
  Comparator #(.width(16), .mode("twosComplement")) comparator_6 (
    .a(\总周期数 ), .b(16'h1), .eq(comparator_6_eq));  // open: gt, lt
  Comparator #(.width(16), .mode("twosComplement")) comparator_7 (
    .a(\总周期数 ), .b(16'h4), .eq(comparator_7_eq));  // open: gt, lt
  or or_16 (or_16_out, comparator_3_eq, comparator_4_eq);
  or or_17 (Branch, and_7_out, and_8_out);
  Multiplexer #(.select(1), .width(32), .disabled("Z"), .enable("false")) multiplexer_20 (
    .in0(mips_alu_1_result), .in1(ram_1_data), .out(multiplexer_20_out), .sel(MemToReg));
  Pull_Resistor #(.pull(0)) pull_resistor_1 (.node(IRA));
  assign IRA = or_15_out ? ~CLK : 1'bz;  // Controlled_Inverter controlled_inverter_1
  Pull_Resistor #(.pull(0)) pull_resistor_2 (.node(IRB));
  assign IRB = comparator_7_eq ? ~CLK : 1'bz;  // Controlled_Inverter controlled_inverter_2
  Pull_Resistor #(.pull(0)) pull_resistor_3 (.node(IRC));
  assign IRC = or_16_out ? ~CLK : 1'bz;  // Controlled_Inverter controlled_inverter_3
  not not_4 (not_4_out, Pause);
  Counter #(.width(16), .max('hffff), .ongoal("wrap"), .trigger("rising"), .behavior("new")) counter_1 (
    .count(not_4_out), .Q(\总周期数 ), .clk(CLK));  // open: load, D, carry, clr, preset, down

  // Other names for the same wires on the sheet: a0[31:0] = MDin; Func[5:0] = IR[5:0]; index[25:0] = IR[25:0];
  //   Shamt[4:0] = IR[10:6]; MF[4:0] = IR[25:21]; OP[5:0] = IR[31:26]; PC31_28[3:0] = PC[31:28]

  // Notes on the sheet:
  //   中断源
  //   中断等待指示
  //   总复位信号应将除ROM以外所有存储组件全部清零
  //   数码管输出
  //   Reset 
  //   Reset 
  //   Reset 
  //   数码管输出应该用寄存器锁存，否则显示数据只能一闪而过
  //   指令存储器
  //   指令字
  //   contents of rom_1 (hex, n*v repeats v):
  //   201d07d0 20100001 109fc0 139fc3 8021 2012000c 24160008 26100001 3210000f 20080008 20090001 139900
  //   2709825 132020 20020022 c 1094022 1500fff9 22100001 2018000f 2188024 108700 20080008 20090001 139902
  //   2709825 132021 20020022 c 1094022 1500fff9 108702 2c9b022 12c00001 8000c07 4020 1084027 84400
  //   3508ffff 82021 20020022 c 8000c01 afa20000 23bd0004 afa40000 23bd0004 afb00000 23bd0004 afb30000
  //   23bd0004 afb40000 23bd0004 afb50000 23bd0004 afb60000 23bd0004 40000000 20160001 20140003 20150001
  //   168020 108100 2149825 132020 20020022 c 1600fffa 295a022 1680fff7 40800000 23bdfffc 8fb60000
  //   23bdfffc 8fb50000 23bdfffc 8fb40000 23bdfffc 8fb30000 23bdfffc 8fb00000 23bdfffc 8fa40000 23bdfffc
  //   8fa20000 42000018 afa20000 23bd0004 afa40000 23bd0004 afb00000 23bd0004 afb30000 23bd0004 afb40000
  //   23bd0004 afb50000 23bd0004 afb60000 23bd0004 40000000 20160002 20140003 20150001 168020 108100
  //   2149825 132020 20020022 c 1600fffa 295a022 1680fff7 40800000 23bdfffc 8fb60000 23bdfffc 8fb50000
  //   23bdfffc 8fb40000 23bdfffc 8fb30000 23bdfffc 8fb00000 23bdfffc 8fa40000 23bdfffc 8fa20000 42000018
  //   afa20000 23bd0004 afa40000 23bd0004 afb00000 23bd0004 afb30000 23bd0004 afb40000 23bd0004 afb50000
  //   23bd0004 afb60000 23bd0004 40000000 20160003 20140003 20150001 168020 108100 2149825 132020 20020022
  //   c 1600fffa 295a022 1680fff7 40800000 23bdfffc 8fb60000 23bdfffc 8fb50000 23bdfffc 8fb40000 23bdfffc
  //   8fb30000 23bdfffc 8fb00000 23bdfffc 8fa40000 23bdfffc 8fa20000 42000018
  //   OP
  //   Func
  //   rs
  //   rt
  //   rd
  //   sa
  //   Imm
  //   instr_index
  //   为方便自动评测，需要输出PC，IR，寄存器堆写如数据RDin
  //   RAM写使能MemWrite、RAM写入数据MDin等信号
  //   多级中断测试信号模拟器
  //   Beq
  //   JMP
  //   JR
  //   Bne
  //   OP
  //   JAL
  //   Func
  //   Syscall
  //   MemToReg
  //   MemWrite
  //   AluOP
  //   AluSrcB
  //   RegWrite
  //   RegDst
endmodule

module \封装正确性测试  (
);

  wire IR1, IR2, IR3, MemW, RegW;
  wire [31:0] EX_PC, ID_PC, IF_PC, IR, LED, MDin, MDinr, MEM_PC, PC, RDin, RDinr, WB_PC;

  \单周期MIPS  \u_单周期mips_1  (
    .RegWrite(RegW), .MemWrite(MemW), .PC(PC), .IR(IR), .RDin(RDin), .MDin(MDin), .LedData(LED));  // open: IR1, IR2, IR3
  \气泡流水线  \u_气泡流水线_1  (
    .RegWrite(RegW), .MemWrite(MemW), .IF_PC(IF_PC), .ID_PC(ID_PC), .EX_PC(EX_PC), .M_PC(MEM_PC),
    .WB_PC(WB_PC), .RDin(RDinr), .MDin(MDinr), .LedData(LED));
  \单周期MIPS_单级中断  \u_单周期mips_单级中断_1  (
    .IR1(IR1), .IR2(IR2), .IR3(IR3), .RegWrite(RegW), .MemWrite(MemW), .PC(PC), .IR(IR), .RDin(RDin),
    .MDin(MDin), .LedData(LED));
  \理想流水线  \u_理想流水线_1  (
    .RegWrite(RegW), .MemWrite(MemW), .IF_PC(IF_PC), .ID_PC(ID_PC), .EX_PC(EX_PC), .M_PC(MEM_PC),
    .WB_PC(WB_PC), .RDin(RDinr), .MDin(MDinr), .LedData(LED));
  \重定向流水线  \u_重定向流水线_1  (
    .RegWrite(RegW), .MemWrite(MemW), .IF_PC(IF_PC), .ID_PC(ID_PC), .EX_PC(EX_PC), .M_PC(MEM_PC),
    .WB_PC(WB_PC), .RDin(RDinr), .MDin(MDinr), .LedData(LED));
  \单周期MIPS_多级中断  \u_单周期mips_多级中断_1  (
    .IR1(IR1), .IR2(IR2), .IR3(IR3), .RegWrite(RegW), .MemWrite(MemW), .PC(PC), .IR(IR), .RDin(RDin),
    .MDin(MDin), .LedData(LED));

  // Notes on the sheet:
  //   单周期封装测试
  //   气泡流水封装测试
  //   单周期+单级中断封装测试
  //   请检查上面封装有无位宽不匹配，引脚标签是否和连接的标签相对应，否则无法在educoder平台上正确测试
  //   理想流水封装测试
  //   重定向流水封装测试
  //   单周期+多级中断封装测试
endmodule

module \动态分支预测  (
  output RegWrite,
  output MemWrite,
  output [31:0] IF_PC,
  output [31:0] ID_PC,
  output [31:0] EX_PC,
  output [31:0] M_PC,
  output [31:0] WB_PC,
  output [31:0] RDin,
  output [31:0] MDin,
  output [31:0] LedData
);

  wire AluSrc, and_1_out, and_2_out, and_3_out, and_4_out, and_6_out, and_7_out, and_8_out, and_9_out,
       and_10_out, and_11_out, and_12_out, and_13_out, BEQ, BGTZ, BNE, BraCLR, Branch, BranchTaken,
       btb_1_preditjump, CLK, clock_1_out, clock_2_out, comparator_1_eq, comparator_1_lt, comparator_2_lt,
       comparator_3_eq, d_ff_1_q, EX_AluSrc, EX_BEQ, EX_BGTZ, EX_BNE, EX_JAL, EX_JMP, EX_JR, EX_MemToReg,
       EX_RegDst, EX_RegW, EX_SRAV, failed, Go, id_ex_1_lhu_2, id_ex_1_memwrite_2, id_ex_1_preditjump_2,
       id_ex_1_syscall_out, id_ex_2_lhu_2, id_ex_2_memtoreg_out, id_ex_2_syscall_out, if_id_1_preditjump_2,
       IR1, IR2, IR3, JAL, JMP, JR, LHU, LoadUse, MEM_JAL, MEM_RegDst, MEM_RegW, MemToReg, MemWrite_t,
       mips_alu_1_equal, nand_1_out, not_1_out, not_2_out, not_3_out, not_4_out, or_2_out, or_3_out,
       or_4_out, or_5_out, or_6_out, or_7_out, or_10_out, or_11_out, or_12_out, or_13_out, Pause, RegDst,
       RegW, RST, SignedExt, SRAV, SUBU, Syscall, W1, W2, W3, WB_JAL, WB_LHU, WB_MemtoReg, WB_RegDst,
       WB_Syscall, \源寄存器使用情况_1_r1_used , \源寄存器使用情况_1_r2_used ;
  wire [1:0] R1_OP, R2_OP, \重定向相关处理逻辑_1_r1_ex , \重定向相关处理逻辑_1_r2_ex ;
  wire [3:0] AluOP, EX_AluOP;
  wire [4:0] id_ex_1_shamt_2, multiplexer_4_out, multiplexer_10_out, multiplexer_12_out, multiplexer_13_out,
       multiplexer_14_out, multiplexer_15_out, multiplexer_16_out, multiplexer_17_out, R1_num, R2_num;
  wire [5:0] Func;
  wire [12:0] CNT_num;
  wire [15:0] counter_6_q, \LoadUse次数 , \分支总数 , \总周期数 , \插入气泡数 , \无条件分支数 , \条件分支成功数 , \条件分支数 , \预测失败数 ,
       \预测成功数 ;
  wire [31:0] adder_1_out, adder_2_out, adder_3_out, adder_4_out, bit_extender_1_out, bit_extender_2_out,
       bit_extender_3_out, bit_extender_4_out, btb_1_jumpaddr, controlled_buffer_1_out, EX_IR, id_ex_1_a_out,
       id_ex_1_b_out, id_ex_1_imm_out, id_ex_2_a_out, id_ex_3_a_out, id_ex_3_alu_out, id_ex_3_b_out,
       id_ex_3_md_out, IF_IR, MEM_Alu, MEM_IR, mips_alu_1_result, mips_regifile_1_r1, mips_regifile_1_r2,
       multiplexer_1_out, multiplexer_2_out, multiplexer_3_out, multiplexer_8_out, multiplexer_9_out,
       multiplexer_11_out, multiplexer_18_out, multiplexer_19_out, multiplexer_20_out, ram_1_data,
       target_offset, WB_IR;
  wire [31:5] multiplexer_10_out_2;
  wire [31:6] ID_IR;

  Button \u_总复位  (.out(RST));
  Button _1 (.out(IR1));
  Button _2 (.out(IR2));
  Button _3 (.out(IR3));
  // Probe on \总周期数 
  // Probe on \总周期数 
  Button \u_继续运行  (.out(Go));
  LED #(.active("true")) led_1 (.in(W1));
  LED #(.active("true")) led_2 (.in(W2));
  LED #(.active("true")) led_3 (.in(W3));
  // Probe on \分支总数 
  // Probe on \预测成功数 
  Hex_Digit_Display hex_digit_display_1 (.value(LedData[31:28]));  // open: dp
  // Probe on IF_PC[19:0]
  // Mips_Probe mips_probe_1: pin names not known; wires that end beside it: IF_IR
  Adder #(.width(32)) adder_1 (.a(32'h4), .b(EX_PC), .out(adder_1_out));  // open: cin, cout
  Hex_Digit_Display hex_digit_display_2 (.value(LedData[27:24]));  // open: dp
  Hex_Digit_Display hex_digit_display_3 (.value(LedData[23:20]));  // open: dp
  // Probe on ID_PC[19:0]
  // Mips_Probe mips_probe_2: pin names not known; wires that end beside it: {ID_IR, Func}
  assign controlled_buffer_1_out = EX_JR ? {multiplexer_10_out_2, multiplexer_10_out} : 32'bz;  // Controlled_Buffer controlled_buffer_1
  assign controlled_buffer_1_out = EX_JMP ? {EX_PC[31:28], EX_IR[25:0], 2'b00} : 32'bz;  // Controlled_Buffer controlled_buffer_2
  assign controlled_buffer_1_out = Branch ? adder_2_out : 32'bz;  // Controlled_Buffer controlled_buffer_3
  Adder #(.width(32)) adder_2 (.a(adder_1_out), .b(target_offset), .out(adder_2_out));  // open: cin, cout
  Hex_Digit_Display hex_digit_display_4 (.value(LedData[19:16]));  // open: dp
  Hex_Digit_Display hex_digit_display_5 (.value(LedData[15:12]));  // open: dp
  // Probe on \条件分支数 
  // Probe on \预测失败数 
  Hex_Digit_Display hex_digit_display_6 (.value(LedData[7:4]));  // open: dp
  Hex_Digit_Display hex_digit_display_7 (.value(LedData[11:8]));  // open: dp
  Clock #(.highDuration(1), .lowDuration(1)) clock_1 (.out(clock_1_out));
  // Probe on EX_PC[19:0]
  // Mips_Probe mips_probe_3: pin names not known; wires that end beside it: clock_1_out, EX_IR, CLK
  Multiplexer #(.select(1), .width(32), .disabled("Z"), .enable("false")) multiplexer_1 (
    .in0(adder_1_out), .in1(controlled_buffer_1_out), .out(multiplexer_1_out), .sel(BraCLR));
  or or_1 (BraCLR, EX_JMP, EX_JR, BranchTaken);
  or or_2 (or_2_out, Branch, EX_JMP, EX_JR);
  Hex_Digit_Display hex_digit_display_8 (.value(LedData[3:0]));  // open: dp
  // Probe on \无条件分支数 
  or or_3 (or_3_out, LoadUse, Pause);
  not not_1 (not_1_out, or_3_out);
  Multiplexer #(.select(1), .width(32), .disabled("Z"), .enable("false")) multiplexer_2 (
    .in0(multiplexer_3_out), .in1(multiplexer_1_out), .out(multiplexer_2_out), .sel(failed));
  // Probe on \总周期数 
  // Probe on M_PC[19:0]
  // Mips_Probe mips_probe_4: pin names not known; wires that end beside it: MEM_IR
  Register #(.width(32), .trigger("rising"), .Select("low")) PC (
    .D(multiplexer_2_out), .en(not_1_out), .Q(IF_PC), .clk(CLK));  // open: clr
  BTB btb_1 (
    .PC(IF_PC), .EX_PC(EX_PC), .EX_BranchAddr(controlled_buffer_1_out), .EX_Branch(or_2_out),
    .EX_BranchTaken(BraCLR), .JumpAddr(btb_1_jumpaddr), .PreditJump(btb_1_preditjump), .CLK(CLK));
  // Probe on \总周期数 
  // Probe on \无条件分支数 
  // Probe on \条件分支成功数 
  // Probe on \插入气泡数 
  // Probe on \LoadUse次数 
  Adder #(.width(32)) adder_3 (.a(32'h4), .b(IF_PC), .out(adder_3_out));  // open: cin, cout
  // Probe on IF_PC[11:0]
  // Probe on WB_PC[19:0]
  // Mips_Probe mips_probe_5: pin names not known; wires that end beside it: WB_IR
  ROM #(.addrWidth(10), .dataWidth(32), .Select("high")) rom_1 (.addr(IF_PC[11:2]), .data(IF_IR));
  Multiplexer #(.select(1), .width(32), .disabled(0), .enable("false")) multiplexer_3 (
    .in0(adder_3_out), .in1(btb_1_jumpaddr), .out(multiplexer_3_out), .sel(btb_1_preditjump));
  // Probe on EX_PC[11:0]
  // Probe on ID_PC[11:0]
  IF_ID if_id_1 (
    .CLK(CLK), .CLR(or_4_out), .Stall(or_5_out), .IR_in(IF_IR), .IR_out({ID_IR, Func}), .PC_in(IF_PC),
    .PC_out(ID_PC), .PreditJump(btb_1_preditjump), .PreditJump_2(if_id_1_preditjump_2));
  or or_4 (or_4_out, failed, RST);
  // Probe on M_PC[11:0]
  D_Flip_Flop #(.trigger("high"), .Pre_Clr_Positions("LEGACY"), .NegatePresetClear("false"), .enable("true"), .NewFFLayout("false")) d_ff_1 (.Q(d_ff_1_q));  // open: clk, D, Qn, preset, en, reset
  // Probe on 13'hc
  Adder #(.width(32)) adder_4 (.a(32'h4), .b(WB_PC), .out(adder_4_out));  // open: cin, cout
  or or_5 (or_5_out, LoadUse, Pause);
  // Probe on WB_PC[11:0]
  Comparator #(.width(13), .mode("twosComplement")) comparator_1 (
    .a(CNT_num), .b(13'hc), .eq(comparator_1_eq), .lt(comparator_1_lt));  // open: gt
  Clock #(.highDuration(1), .lowDuration(1)) clock_2 (.out(clock_2_out));
  \单周期硬布线控制器  \u_单周期硬布线控制器_1  (
    .Func(Func), .OP(ID_IR[31:26]), .ALU_OP(AluOP), .MemToReg(MemToReg), .MemWrite(MemWrite_t),
    .ALU_SRC(AluSrc), .RegWrite(RegW), .SysCALL(Syscall), .SignedExt(SignedExt), .RegDst(RegDst), .JR(JR),
    .JMP(JMP), .Beq(BEQ), .JAL(JAL), .Bne(BNE), .SRAV(SRAV), .SUBU(SUBU), .LHU(LHU), .BGTZ(BGTZ));  // open: ERET, MFC0, MTC0, MF
  Multiplexer #(.select(1), .width(5), .disabled("Z"), .enable("false")) multiplexer_4 (
    .in0({5{1'b1}}), .in1(multiplexer_17_out), .out(multiplexer_4_out), .sel(not_2_out));
  not not_2 (not_2_out, WB_JAL);
  nand nand_1 (nand_1_out, d_ff_1_q, comparator_1_eq);
  Counter #(.width(13), .max('h1fff), .ongoal("stay"), .trigger("rising"), .behavior("old")) counter_1 (
    .count(comparator_1_lt), .Q(CNT_num), .clk(clock_2_out));  // open: load, D, carry, clr, preset
  Multiplexer #(.select(1), .width(5), .disabled("Z"), .enable("false")) multiplexer_5 (
    .in0(ID_IR[25:21]), .in1(5'b00010), .out(R1_num), .sel(Syscall));
  Multiplexer #(.select(1), .width(5), .disabled("Z"), .enable("false")) multiplexer_6 (
    .in0(ID_IR[20:16]), .in1(5'b00100), .out(R2_num), .sel(Syscall));
  Multiplexer #(.select(1), .width(32), .disabled("Z"), .enable("false")) multiplexer_7 (
    .in0(multiplexer_20_out), .in1(adder_4_out), .out(RDin), .sel(WB_JAL));
  assign bit_extender_1_out = {{16{1'b0}}, {ID_IR[15:6], Func}};  // Bit_Extender bit_extender_1
  assign bit_extender_2_out = {{16{ID_IR[15]}}, {ID_IR[15:6], Func}};  // Bit_Extender bit_extender_2
  assign CLK = nand_1_out ? clock_2_out : 1'bz;  // Controlled_Buffer controlled_buffer_4
  MIPS_Regifile mips_regifile_1 (
    .Din(RDin), .Clk(CLK), .R1(mips_regifile_1_r1), .R2(mips_regifile_1_r2), .WE(RegWrite),
    .W_num(multiplexer_4_out), .R1_num(R1_num), .R2_num(R2_num));
  Multiplexer #(.select(1), .width(32), .disabled("Z"), .enable("false")) multiplexer_8 (
    .in0(bit_extender_1_out), .in1(bit_extender_2_out), .out(multiplexer_8_out), .sel(SignedExt));
  Pull_Resistor #(.pull(1)) pull_resistor_1 (.node(CLK));
  ID_EX id_ex_1 (
    .RegDst_in(RegDst), .IR_in({ID_IR, Func}), .Syscall_in(Syscall), .RegWrite_in(RegW), .PC_in(ID_PC),
    .JMP_in(JMP), .MemToReg_in(MemToReg), .A_in(mips_regifile_1_r1), .JR_in(JR), .AluOP_in(AluOP),
    .JAL_in(JAL), .AluSrc_in(AluSrc), .B_in(mips_regifile_1_r2), .SignedExt_in(SignedExt),
    .MemWrite(MemWrite_t), .Imm_in(multiplexer_8_out), .Beq_in(BEQ), .Shamt(ID_IR[10:6]), .Bne_in(BNE),
    .CLK(CLK), .RegDst_out(EX_RegDst), .IR_out(EX_IR), .Syscall_out(id_ex_1_syscall_out),
    .RegWrite_out(EX_RegW), .PC_out(EX_PC), .JMP_out(EX_JMP), .MemToReg_out(EX_MemToReg),
    .A_out(id_ex_1_a_out), .JR_out(EX_JR), .AluOP_out(EX_AluOP), .JAL_out(EX_JAL), .AluSrc_out(EX_AluSrc),
    .B_out(id_ex_1_b_out), .MemWrite_2(id_ex_1_memwrite_2), .Imm_out(id_ex_1_imm_out), .Beq_out(EX_BEQ),
    .Shamt_2(id_ex_1_shamt_2), .Bne_out(EX_BNE), .CLR(or_6_out), .Stall(Pause), .BGTZ(BGTZ),
    .BGTZ_2(EX_BGTZ), .SUBU(SUBU), .LHU(LHU), .LHU_2(id_ex_1_lhu_2), .SRAV(SRAV), .SRAV_2(EX_SRAV),
    .PreditJump(if_id_1_preditjump_2), .PreditJump_2(id_ex_1_preditjump_2));  // open: SignedExt_out, SUBU_2, MD_in, MD_out, ALU_in, ALU_out
  or or_6 (or_6_out, failed, LoadUse, RST);
  xor xor_1 (failed, id_ex_1_preditjump_2, or_7_out);
  Shifter #(.width(32), .shift("ll")) shifter_1 (.in(id_ex_1_imm_out), .\dist (5'b00010), .out(target_offset));
  or or_7 (or_7_out, BranchTaken, EX_JMP, EX_JR);
  Multiplexer #(.select(2), .width(32), .disabled("Z"), .enable("false")) multiplexer_9 (
    .in0(id_ex_1_b_out), .in1(MEM_Alu), .in2(RDin), .in3(MEM_Alu), .out(multiplexer_9_out), .sel(R2_OP));
  or or_8 (Branch, EX_BEQ, EX_BNE, EX_BGTZ);
  Multiplexer #(.select(2), .width(32), .disabled("Z"), .enable("false")) multiplexer_10 (
    .in0(id_ex_1_a_out), .in1(MEM_Alu), .in2(RDin), .in3(MEM_Alu),
    .out({multiplexer_10_out_2, multiplexer_10_out}), .sel(R1_OP));
  Multiplexer #(.select(1), .width(32), .disabled("Z"), .enable("false")) multiplexer_11 (
    .in0(multiplexer_9_out), .in1(id_ex_1_imm_out), .out(multiplexer_11_out), .sel(EX_AluSrc));
  and and_1 (and_1_out, EX_BEQ, mips_alu_1_equal);
  and and_2 (and_2_out, EX_BNE, ~mips_alu_1_equal);  // AND_Gate
  and and_3 (and_3_out, EX_BGTZ, comparator_2_lt);
  Comparator #(.width(32), .mode("twosComplement")) comparator_2 (
    .a({32{1'b0}}), .b({multiplexer_10_out_2, multiplexer_10_out}), .lt(comparator_2_lt));  // open: gt, eq
  MIPS_ALU mips_alu_1 (
    .X({multiplexer_10_out_2, multiplexer_10_out}), .Y(multiplexer_11_out), .AluOP(EX_AluOP),
    .Equal(mips_alu_1_equal), .Result(mips_alu_1_result), .shamt(multiplexer_12_out));  // open: Result_2
  Multiplexer #(.select(1), .width(5), .disabled("Z"), .enable("false")) multiplexer_12 (
    .in0(id_ex_1_shamt_2), .in1(multiplexer_10_out), .out(multiplexer_12_out), .sel(EX_SRAV));
  Multiplexer #(.select(1), .width(5), .disabled("Z"), .enable("false")) multiplexer_13 (
    .in0(EX_IR[20:16]), .in1(EX_IR[15:11]), .out(multiplexer_13_out), .sel(EX_RegDst));
  Multiplexer #(.select(1), .width(5), .disabled("Z"), .enable("false")) multiplexer_14 (
    .in0(MEM_IR[20:16]), .in1(MEM_IR[15:11]), .out(multiplexer_14_out), .sel(MEM_RegDst));
  or or_9 (BranchTaken, and_1_out, and_2_out, and_3_out);
  \源寄存器使用情况  \u_源寄存器使用情况_1  (
    .OP0(ID_IR[26]), .OP1(ID_IR[27]), .OP2(ID_IR[28]), .OP3(ID_IR[29]), .OP4(ID_IR[30]), .OP5(ID_IR[31]),
    .F0(Func[0]), .F1(Func[1]), .F2(Func[2]), .F3(Func[3]), .F4(Func[4]), .F5(Func[5]),
    .R1_USED(\源寄存器使用情况_1_r1_used ), .R2_USED(\源寄存器使用情况_1_r2_used ));
  Multiplexer #(.select(1), .width(5), .disabled("Z"), .enable("false")) multiplexer_15 (
    .in0(multiplexer_13_out), .in1({5{1'b1}}), .out(multiplexer_15_out), .sel(MEM_JAL));
  Multiplexer #(.select(1), .width(5), .disabled("Z"), .enable("false")) multiplexer_16 (
    .in0(multiplexer_14_out), .in1({5{1'b1}}), .out(multiplexer_16_out), .sel(EX_JAL));
  ID_EX id_ex_2 (
    .RegDst_in(EX_RegDst), .IR_in(EX_IR), .Syscall_in(id_ex_1_syscall_out), .RegWrite_in(EX_RegW),
    .PC_in(EX_PC), .MemToReg_in(EX_MemToReg), .A_in({multiplexer_10_out_2, multiplexer_10_out}),
    .JAL_in(EX_JAL), .B_in(multiplexer_9_out), .MemWrite(id_ex_1_memwrite_2), .CLK(CLK),
    .RegDst_out(MEM_RegDst), .IR_out(MEM_IR), .Syscall_out(id_ex_2_syscall_out), .RegWrite_out(MEM_RegW),
    .PC_out(M_PC), .MemToReg_out(id_ex_2_memtoreg_out), .A_out(id_ex_2_a_out), .JAL_out(MEM_JAL),
    .B_out(MDin), .MemWrite_2(MemWrite), .CLR(RST), .Stall(Pause), .LHU(id_ex_1_lhu_2),
    .LHU_2(id_ex_2_lhu_2), .ALU_in(mips_alu_1_result), .ALU_out(MEM_Alu));  // open: JMP_in, JR_in, AluOP_in, AluSrc_in, SignedExt_in, Imm_in, Beq_in, Shamt, Bne_in, JMP_out, JR_out, AluOP_out, AluSrc_out, SignedExt_out, Imm_out, Beq_out, Shamt_2, Bne_out, BGTZ, BGTZ_2, SUBU, SUBU_2, SRAV, SRAV_2, MD_in, MD_out, PreditJump, PreditJump_2
  \重定向相关处理逻辑  \u_重定向相关处理逻辑_1  (
    .R1_Used(\源寄存器使用情况_1_r1_used ), .R2_Used(\源寄存器使用情况_1_r2_used ), .R1_num(R1_num), .EX_RegWrite(EX_RegW),
    .EX_WriteReg_num(multiplexer_15_out), .R2_num(R2_num), .MEM_WriteReg_num(multiplexer_16_out),
    .MEM_RegWrite(MEM_RegW), .R1_EX(\重定向相关处理逻辑_1_r1_ex [0]), .R2_EX(\重定向相关处理逻辑_1_r2_ex [0]),
    .R1_MEM(\重定向相关处理逻辑_1_r1_ex [1]), .R2_MEM(\重定向相关处理逻辑_1_r2_ex [1]));
  RAM #(.addrWidth(10), .dataWidth(32), .bus("separate"), .Select("high")) ram_1 (
    .addr(MEM_Alu[11:2]), .din(MDin), .data(ram_1_data), .str(MemWrite), .clk(CLK));  // open: sel, ld, clr
  Register #(.width(2), .trigger("rising"), .Select("low")) register_1 (
    .D(\重定向相关处理逻辑_1_r1_ex ), .Q(R1_OP), .clk(CLK));  // open: en, clr
  Register #(.width(2), .trigger("rising"), .Select("low")) register_2 (
    .D(\重定向相关处理逻辑_1_r2_ex ), .Q(R2_OP), .clk(CLK));  // open: en, clr
  ID_EX id_ex_3 (
    .RegDst_in(MEM_RegDst), .IR_in(MEM_IR), .Syscall_in(id_ex_2_syscall_out), .RegWrite_in(MEM_RegW),
    .PC_in(M_PC), .MemToReg_in(id_ex_2_memtoreg_out), .A_in(id_ex_2_a_out), .JAL_in(MEM_JAL), .B_in(MDin),
    .CLK(CLK), .RegDst_out(WB_RegDst), .IR_out(WB_IR), .Syscall_out(WB_Syscall), .RegWrite_out(RegWrite),
    .PC_out(WB_PC), .MemToReg_out(WB_MemtoReg), .A_out(id_ex_3_a_out), .JAL_out(WB_JAL),
    .B_out(id_ex_3_b_out), .CLR(RST), .Stall(Pause), .LHU(id_ex_2_lhu_2), .LHU_2(WB_LHU), .MD_in(ram_1_data),
    .MD_out(id_ex_3_md_out), .ALU_in(MEM_Alu), .ALU_out(id_ex_3_alu_out));  // open: JMP_in, JR_in, AluOP_in, AluSrc_in, SignedExt_in, MemWrite, Imm_in, Beq_in, Shamt, Bne_in, JMP_out, JR_out, AluOP_out, AluSrc_out, SignedExt_out, MemWrite_2, Imm_out, Beq_out, Shamt_2, Bne_out, BGTZ, BGTZ_2, SUBU, SUBU_2, SRAV, SRAV_2, PreditJump, PreditJump_2
  and and_4 (and_4_out, not_3_out, BranchTaken);
  or or_10 (or_10_out, \重定向相关处理逻辑_1_r1_ex [0], \重定向相关处理逻辑_1_r2_ex [0]);
  or or_11 (or_11_out, EX_JR, Branch, EX_JMP);
  Counter #(.width(16), .max('hffff), .ongoal("wrap"), .trigger("falling"), .behavior("new")) counter_2 (
    .count(and_4_out), .Q(\条件分支成功数 ), .clk(CLK));  // open: load, D, carry, clr, preset, down
  Comparator #(.width(32), .mode("unsigned")) comparator_3 (
    .a(32'h22), .b(id_ex_3_a_out), .eq(comparator_3_eq));  // open: gt, lt
  and and_5 (LoadUse, EX_MemToReg, or_10_out);
  not not_3 (not_3_out, Pause);
  Counter #(.width(16), .max('hffff), .ongoal("wrap"), .trigger("falling"), .behavior("new")) counter_3 (
    .count(not_3_out), .Q(\总周期数 ), .clk(CLK));  // open: load, D, carry, clr, preset, down
  and and_6 (and_6_out, not_3_out, or_11_out);
  Counter #(.width(16), .max('hffff), .ongoal("wrap"), .trigger("falling"), .behavior("new")) counter_4 (
    .count(and_6_out), .Q(\分支总数 ), .clk(CLK));  // open: load, D, carry, clr, preset, down
  and and_7 (and_7_out, not_3_out, Branch);
  Counter #(.width(16), .max('hffff), .ongoal("wrap"), .trigger("falling"), .behavior("new")) counter_5 (
    .count(and_7_out), .Q(\条件分支数 ), .clk(CLK));  // open: load, D, carry, clr, preset, down
  and and_8 (and_8_out, WB_Syscall, comparator_3_eq);
  and and_9 (and_9_out, WB_Syscall, ~comparator_3_eq);  // AND_Gate
  Multiplexer #(.select(1), .width(5), .disabled("Z"), .enable("false")) multiplexer_17 (
    .in0(WB_IR[20:16]), .in1(WB_IR[15:11]), .out(multiplexer_17_out), .sel(WB_RegDst));
  Register #(.width(32), .trigger("rising"), .Select("low")) register_3 (
    .D(id_ex_3_b_out), .Q(LedData), .clk(and_8_out));  // open: en, clr
  Register #(.width(1), .trigger("rising"), .Select("low")) register_4 (
    .D(and_9_out), .en(and_9_out), .Q(Pause), .clk(CLK), .clr(Go));
  Multiplexer #(.select(1), .width(32), .disabled("Z"), .enable("false")) multiplexer_18 (
    .in0(id_ex_3_alu_out), .in1(id_ex_3_md_out), .out(multiplexer_18_out), .sel(WB_MemtoReg));
  or or_12 (or_12_out, failed, LoadUse);
  assign bit_extender_3_out = {{16{1'b0}}, multiplexer_18_out[15:0]};  // Bit_Extender bit_extender_3
  assign bit_extender_4_out = {{16{1'b0}}, multiplexer_18_out[31:16]};  // Bit_Extender bit_extender_4
  or or_13 (or_13_out, EX_JR, EX_JMP);
  and and_10 (and_10_out, not_4_out, or_12_out);
  Counter #(.width(16), .max('hffff), .ongoal("wrap"), .trigger("falling"), .behavior("new")) counter_6 (
    .count(and_10_out), .Q(counter_6_q), .clk(CLK));  // open: load, D, carry, clr, preset, down
  Multiplexer #(.select(1), .width(32), .disabled("Z"), .enable("false")) multiplexer_19 (
    .in0(bit_extender_3_out), .in1(bit_extender_4_out), .out(multiplexer_19_out), .sel(id_ex_3_alu_out[1]));
  not not_4 (not_4_out, Pause);
  and and_11 (and_11_out, not_4_out, or_13_out);
  Counter #(.width(16), .max('hffff), .ongoal("wrap"), .trigger("falling"), .behavior("new")) counter_7 (
    .count(and_11_out), .Q(\无条件分支数 ), .clk(CLK));  // open: load, D, carry, clr, preset, down
  and and_12 (and_12_out, not_4_out, failed);
  Counter #(.width(16), .max('hffff), .ongoal("wrap"), .trigger("falling"), .behavior("new")) counter_8 (
    .count(and_12_out), .Q(\预测失败数 ), .clk(CLK));  // open: load, D, carry, clr, preset, down
  and and_13 (and_13_out, not_4_out, LoadUse);
  Counter #(.width(16), .max('hffff), .ongoal("wrap"), .trigger("falling"), .behavior("new")) counter_9 (
    .count(and_13_out), .Q(\LoadUse次数 ));  // open: load, D, carry, clk, clr, preset, down
  Adder #(.width(16)) adder_5 (.a(\预测失败数 ), .b(counter_6_q), .out(\插入气泡数 ));  // open: cin, cout
  Multiplexer #(.select(1), .width(32), .disabled("Z"), .enable("false")) multiplexer_20 (
    .in0(multiplexer_18_out), .in1(multiplexer_19_out), .out(multiplexer_20_out), .sel(WB_LHU));
  Subtractor #(.width(16)) subtractor_1 (.a(\分支总数 ), .b(\预测失败数 ), .out(\预测成功数 ));  // open: bin, bout

  // Other names for the same wires on the sheet: index[25:0] = EX_IR[25:0]; PC31_28[3:0] = EX_PC[31:28];
  //   ID_IR[5:0] = Func; OP[5:0] = ID_IR[31:26]; MEM_PC[31:0] = M_PC; MemW = MemWrite

  // Notes on the sheet:
  //   中断源
  //   中断等待指示
  //   数码管输出
  //   指令存储器
  //   contents of rom_1 (hex, n*v repeats v):
  //   20110001 8000c05 20110001 20120002 20130003 8000c09 20110001 20120002 20130003 8000c0d 20110001
  //   20120002 20130003 8000c11 20110001 20120002 20130003 c000cb8 20100001 20110001 118fc0 112020
  //   20020022 c 118882 12200001 8000c15 112020 20020022 c 20110001 118880 112020 20020022 c 12200001
  //   8000c1f 20110001 118fc0 112020 20020022 c 1188c3 112020 20020022 c 118903 112020 20020022 c 118903
  //   112020 20020022 c 118903 112020 20020022 c 118903 112020 20020022 c 118903 112020 20020022 c 118903
  //   112020 20020022 c 118903 112020 20020022 c 20100001 109fc0 139fc3 8021 2012000c 24160003 26100001
  //   3210000f 20080008 20090001 139900 2709825 132020 20020022 c 1094022 1500fff9 22100001 2018000f
  //   2188024 108700 20080008 20090001 139902 2709825 132021 20020022 c 1094022 1500fff9 108702 2c9b022
  //   12c00001 8000c50 4020 1084027 84400 3508ffff 82021 20020022 c 2010ffff 20110000 ae300000 22100001
  //   22310004 ae300000 22100001 22310004 ae300000 22100001 22310004 ae300000 22100001 22310004 ae300000
  //   22100001 22310004 ae300000 22100001 22310004 ae300000 22100001 22310004 ae300000 22100001 22310004
  //   ae300000 22100001 22310004 ae300000 22100001 22310004 ae300000 22100001 22310004 ae300000 22100001
  //   22310004 ae300000 22100001 22310004 ae300000 22100001 22310004 ae300000 22100001 22310004 ae300000
  //   22100001 22310004 22100001 8020 2011003c 8e130000 8e340000 274402a 11000002 ae330000 ae140000
  //   2231fffc 1611fff8 102020 20020022 c 22100004 2011003c 1611fff2 20020032 c 20100000 22100001 102020
  //   20020022 c 22100002 102020 20020022 c 22100003 102020 20020022 c 22100004 102020 20020022 c 22100005
  //   102020 20020022 c 22100006 102020 20020022 c 22100007 102020 20020022 c 22100008 102020 20020022
  //   20020022 c 3e00008
  //   控制位
  //   流水调试日志用
  //   暂停节拍，不能为0
  //   JMP
  //   JR
  //   OP
  //   Func
  //   rs
  //   rt
  //   Imm
  //   sa
  //   可计数暂停的时钟源
  //   为方便自动评测，需要输出流水线各段保存的PC值，注意是PC不是PC+4，另外ID段寄存器写入信息，Mem段内存写入信息也要输出
  //   rd
  //   rd
  //   rt
  //   rd
endmodule

module FSM (
  input  RST,
  input  CLK,
  input  X,
  input  EN,
  output D2,
  output Z,
  output D1
);

  wire and_1_out, and_2_out, and_3_out, and_4_out, D1_qn, D2_qn, or_2_out;

  D_Flip_Flop #(.trigger("rising"), .Pre_Clr_Positions("ABOVE_BELOW"), .NegatePresetClear("false"), .enable("true"), .NewFFLayout("true")) u_D2 (
    .clk(CLK), .D(Z), .Q(D2), .Qn(D2_qn), .preset(RST), .en(EN));  // open: reset
  D_Flip_Flop #(.trigger("rising"), .Pre_Clr_Positions("ABOVE_BELOW"), .NegatePresetClear("false"), .enable("true"), .NewFFLayout("true")) u_D1 (
    .clk(CLK), .D(or_2_out), .Q(D1), .Qn(D1_qn), .preset(RST), .en(EN));  // open: reset
  and and_1 (and_1_out, D2, D1_qn);
  or or_1 (Z, and_1_out, and_2_out);
  and and_2 (and_2_out, X, D1);
  and and_3 (and_3_out, D2_qn, D1_qn, X);
  and and_4 (and_4_out, ~X, D2, D1);  // AND_Gate
  or or_2 (or_2_out, and_3_out, and_4_out);
endmodule

// MAX
module Max (
  input  [15:0] Y,
  input  [15:0] X,
  input  [2:0] Y_num,
  input  [2:0] X_num,
  output [15:0] MAX,
  output [2:0] Max_num
);

  wire comparator_1_eq, comparator_1_gt, or_1_out;

  Multiplexer #(.select(1), .width(16), .disabled("Z"), .enable("false")) multiplexer_1 (
    .in0(Y), .in1(X), .out(MAX), .sel(or_1_out));
  Comparator #(.width(16), .mode("unsigned")) comparator_1 (
    .a(X), .b(Y), .gt(comparator_1_gt), .eq(comparator_1_eq));  // open: lt
  or or_1 (or_1_out, comparator_1_gt, comparator_1_eq);
  Multiplexer #(.select(1), .width(3), .disabled("Z"), .enable("false")) multiplexer_2 (
    .in0(Y_num), .in1(X_num), .out(Max_num), .sel(or_1_out));

  // Notes on the sheet:
  //   输出两个输入中的较大值，并输出较大值的3位编号
endmodule

module \cache槽  (
  input  [31:0] PC,
  input  [31:0] BranchAddr,
  input  CLK,
  input  Replace,
  input  BranchTaken,
  input  Load,
  input  fresh,
  output [31:0] PC_2,
  output [31:0] BranchAddr_2,
  output valid,
  output [15:0] Count,
  output Jump
);

  wire fsm_1_z, not_1_out, or_1_out;
  wire [31:0] DATA_q;

  Register #(.width(1), .trigger("rising"), .Select("low")) u_VALID (
    .D(1'b1), .en(Replace), .Q(valid), .clk(CLK));  // open: clr
  Register #(.width(32), .trigger("rising"), .Select("low")) TAG (
    .D(PC), .en(Replace), .Q(PC_2), .clk(CLK));  // open: clr
  not not_1 (not_1_out, or_1_out);
  FSM fsm_1 (.RST(Replace), .CLK(CLK), .X(BranchTaken), .Z(fsm_1_z), .EN(fresh));  // open: D2, D1
  Counter #(.width(16), .max('hffff), .ongoal("wrap"), .trigger("rising"), .behavior("old")) counter_1 (
    .load(or_1_out), .D({16{1'b0}}), .count(not_1_out), .Q(Count), .clk(CLK));  // open: carry, clr, preset
  or or_1 (or_1_out, Replace, Load);
  assign Jump = Load ? fsm_1_z : 1'bz;  // Controlled_Buffer controlled_buffer_1
  Register #(.width(32), .trigger("rising"), .Select("low")) DATA (
    .D(BranchAddr), .en(Replace), .Q(DATA_q), .clk(CLK));  // open: clr
  assign BranchAddr_2 = Load ? DATA_q : 32'bz;  // Controlled_Buffer controlled_buffer_2
endmodule

module \全相连Cache  (
  input  [31:0] BranchAddr_in,
  input  [31:0] PC,
  input  AddrReady,
  input  CLK,
  input  [31:0] EPC,
  input  BranchTaken,
  output Miss,
  output [31:0] BranchAddr_out,
  output Jump
);

  wire and_1_out, and_2_out, and_3_out, and_4_out, and_5_out, and_6_out, and_7_out, and_8_out, and_9_out,
       and_10_out, and_11_out, and_12_out, and_13_out, and_14_out, and_15_out, and_16_out, and_17_out,
       and_18_out, and_19_out, and_20_out, and_21_out, and_22_out, and_23_out, and_24_out, and_25_out,
       \cache槽_1_valid , \cache槽_2_valid , \cache槽_3_valid , \cache槽_4_valid , \cache槽_5_valid ,
       \cache槽_6_valid , \cache槽_7_valid , \cache槽_8_valid , comparator_1_eq, comparator_2_eq,
       comparator_3_eq, comparator_4_eq, comparator_5_eq, comparator_6_eq, comparator_7_eq, comparator_8_eq,
       comparator_9_eq, comparator_10_eq, comparator_11_eq, comparator_12_eq, comparator_13_eq,
       comparator_14_eq, comparator_15_eq, comparator_16_eq, decoder_1_out0, decoder_1_out1, decoder_1_out2,
       decoder_1_out3, decoder_1_out4, decoder_1_out5, decoder_1_out6, decoder_1_out7, exMiss;
  wire [2:0] max_1_max_num, max_2_max_num, max_3_max_num, max_4_max_num, max_5_max_num, max_6_max_num,
       max_7_max_num;
  wire [15:0] Count0, Count1, Count2, Count3, Count4, Count5, Count6, Count7, max_1_max, max_2_max,
       max_3_max, max_4_max, max_5_max, max_6_max;
  wire [31:0] \cache槽_1_pc_2 , \cache槽_2_pc_2 , \cache槽_3_pc_2 , \cache槽_4_pc_2 , \cache槽_5_pc_2 ,
       \cache槽_6_pc_2 , \cache槽_7_pc_2 , \cache槽_8_pc_2 ;

  Max max_1 (.Y(Count0), .X(Count1), .Y_num(3'b000), .X_num(3'b001), .MAX(max_1_max), .Max_num(max_1_max_num));
  Max max_2 (.Y(Count2), .X(Count3), .Y_num(3'b010), .X_num(3'b011), .MAX(max_2_max), .Max_num(max_2_max_num));
  Max max_3 (.Y(Count4), .X(Count5), .Y_num(3'b100), .X_num(3'b101), .MAX(max_3_max), .Max_num(max_3_max_num));
  Max max_4 (.Y(Count6), .X(Count7), .Y_num(3'b110), .X_num(3'b111), .MAX(max_4_max), .Max_num(max_4_max_num));
  Max max_5 (
    .Y(max_1_max), .X(max_2_max), .Y_num(max_1_max_num), .X_num(max_2_max_num), .MAX(max_5_max),
    .Max_num(max_5_max_num));
  Max max_6 (
    .Y(max_3_max), .X(max_4_max), .Y_num(max_3_max_num), .X_num(max_4_max_num), .MAX(max_6_max),
    .Max_num(max_6_max_num));
  Decoder #(.select(3), .tristate("false"), .disabled(0), .enable("true")) decoder_1 (
    .out0(decoder_1_out0), .out1(decoder_1_out1), .out2(decoder_1_out2), .out3(decoder_1_out3),
    .out4(decoder_1_out4), .out5(decoder_1_out5), .out6(decoder_1_out6), .out7(decoder_1_out7),
    .sel(max_7_max_num), .en(and_1_out));
  Max max_7 (
    .Y(max_5_max), .X(max_6_max), .Y_num(max_5_max_num), .X_num(max_6_max_num), .Max_num(max_7_max_num));  // open: MAX
  and and_1 (and_1_out, AddrReady, exMiss);
  and and_2 (and_2_out, and_1_out, decoder_1_out0);
  and and_3 (and_3_out, and_1_out, decoder_1_out1);
  and and_4 (and_4_out, and_1_out, decoder_1_out2);
  and and_5 (and_5_out, and_1_out, decoder_1_out3);
  and and_6 (and_6_out, and_1_out, decoder_1_out4);
  and and_7 (and_7_out, and_1_out, decoder_1_out5);
  and and_8 (and_8_out, and_1_out, decoder_1_out6);
  and and_9 (and_9_out, and_1_out, decoder_1_out7);
  \cache槽  \cache槽_1  (
    .PC(EPC), .CLK(CLK), .Replace(and_2_out), .valid(\cache槽_1_valid ), .PC_2(\cache槽_1_pc_2 ),
    .Count(Count0), .BranchAddr_2(BranchAddr_out), .Load(and_10_out), .BranchAddr(BranchAddr_in),
    .BranchTaken(BranchTaken), .Jump(Jump), .fresh(and_18_out));
  \cache槽  \cache槽_2  (
    .PC(EPC), .CLK(CLK), .Replace(and_3_out), .valid(\cache槽_2_valid ), .PC_2(\cache槽_2_pc_2 ),
    .Count(Count1), .BranchAddr_2(BranchAddr_out), .Load(and_11_out), .BranchAddr(BranchAddr_in),
    .BranchTaken(BranchTaken), .Jump(Jump), .fresh(and_19_out));
  \cache槽  \cache槽_3  (
    .PC(EPC), .CLK(CLK), .Replace(and_4_out), .valid(\cache槽_3_valid ), .PC_2(\cache槽_3_pc_2 ),
    .Count(Count2), .BranchAddr_2(BranchAddr_out), .Load(and_12_out), .BranchAddr(BranchAddr_in),
    .BranchTaken(BranchTaken), .Jump(Jump), .fresh(and_20_out));
  \cache槽  \cache槽_4  (
    .PC(EPC), .CLK(CLK), .Replace(and_5_out), .valid(\cache槽_4_valid ), .PC_2(\cache槽_4_pc_2 ),
    .Count(Count3), .BranchAddr_2(BranchAddr_out), .Load(and_13_out), .BranchAddr(BranchAddr_in),
    .BranchTaken(BranchTaken), .Jump(Jump), .fresh(and_21_out));
  \cache槽  \cache槽_5  (
    .PC(EPC), .CLK(CLK), .Replace(and_6_out), .valid(\cache槽_5_valid ), .PC_2(\cache槽_5_pc_2 ),
    .Count(Count4), .BranchAddr_2(BranchAddr_out), .Load(and_14_out), .BranchAddr(BranchAddr_in),
    .BranchTaken(BranchTaken), .Jump(Jump), .fresh(and_22_out));
  \cache槽  \cache槽_6  (
    .PC(EPC), .CLK(CLK), .Replace(and_7_out), .valid(\cache槽_6_valid ), .PC_2(\cache槽_6_pc_2 ),
    .Count(Count5), .BranchAddr_2(BranchAddr_out), .Load(and_15_out), .BranchAddr(BranchAddr_in),
    .BranchTaken(BranchTaken), .Jump(Jump), .fresh(and_23_out));
  \cache槽  \cache槽_7  (
    .PC(EPC), .CLK(CLK), .Replace(and_8_out), .valid(\cache槽_7_valid ), .PC_2(\cache槽_7_pc_2 ),
    .Count(Count6), .BranchAddr_2(BranchAddr_out), .Load(and_16_out), .BranchAddr(BranchAddr_in),
    .BranchTaken(BranchTaken), .Jump(Jump), .fresh(and_24_out));
  \cache槽  \cache槽_8  (
    .PC(EPC), .CLK(CLK), .Replace(and_9_out), .valid(\cache槽_8_valid ), .PC_2(\cache槽_8_pc_2 ),
    .Count(Count7), .BranchAddr_2(BranchAddr_out), .Load(and_17_out), .BranchAddr(BranchAddr_in),
    .BranchTaken(BranchTaken), .Jump(Jump), .fresh(and_25_out));
  Comparator #(.width(32), .mode("twosComplement")) comparator_1 (
    .a(\cache槽_1_pc_2 ), .b(PC), .eq(comparator_1_eq));  // open: gt, lt
  Comparator #(.width(32), .mode("twosComplement")) comparator_2 (
    .a(\cache槽_2_pc_2 ), .b(PC), .eq(comparator_2_eq));  // open: gt, lt
  Comparator #(.width(32), .mode("twosComplement")) comparator_3 (
    .a(\cache槽_3_pc_2 ), .b(PC), .eq(comparator_3_eq));  // open: gt, lt
  Comparator #(.width(32), .mode("twosComplement")) comparator_4 (
    .a(\cache槽_4_pc_2 ), .b(PC), .eq(comparator_4_eq));  // open: gt, lt
  Comparator #(.width(32), .mode("twosComplement")) comparator_5 (
    .a(\cache槽_5_pc_2 ), .b(PC), .eq(comparator_5_eq));  // open: gt, lt
  Comparator #(.width(32), .mode("twosComplement")) comparator_6 (
    .a(\cache槽_6_pc_2 ), .b(PC), .eq(comparator_6_eq));  // open: gt, lt
  Comparator #(.width(32), .mode("twosComplement")) comparator_7 (
    .a(\cache槽_7_pc_2 ), .b(PC), .eq(comparator_7_eq));  // open: gt, lt
  Comparator #(.width(32), .mode("twosComplement")) comparator_8 (
    .a(\cache槽_8_pc_2 ), .b(PC), .eq(comparator_8_eq));  // open: gt, lt
  and and_10 (and_10_out, comparator_1_eq, \cache槽_1_valid );
  and and_11 (and_11_out, comparator_2_eq, \cache槽_2_valid );
  and and_12 (and_12_out, comparator_3_eq, \cache槽_3_valid );
  and and_13 (and_13_out, comparator_4_eq, \cache槽_4_valid );
  and and_14 (and_14_out, comparator_5_eq, \cache槽_5_valid );
  and and_15 (and_15_out, comparator_6_eq, \cache槽_6_valid );
  and and_16 (and_16_out, comparator_7_eq, \cache槽_7_valid );
  and and_17 (and_17_out, comparator_8_eq, \cache槽_8_valid );
  nor nor_1 (Miss, and_10_out, and_11_out, and_12_out, and_13_out, and_14_out, and_15_out, and_16_out, and_17_out);
  Comparator #(.width(32), .mode("twosComplement")) comparator_9 (
    .a(EPC), .b(\cache槽_1_pc_2 ), .eq(comparator_9_eq));  // open: gt, lt
  Comparator #(.width(32), .mode("twosComplement")) comparator_10 (
    .a(EPC), .b(PC), .eq(comparator_10_eq));  // open: gt, lt
  Comparator #(.width(32), .mode("twosComplement")) comparator_11 (
    .a(EPC), .b(PC), .eq(comparator_11_eq));  // open: gt, lt
  Comparator #(.width(32), .mode("twosComplement")) comparator_12 (
    .a(EPC), .b(\cache槽_4_pc_2 ), .eq(comparator_12_eq));  // open: gt, lt
  Comparator #(.width(32), .mode("twosComplement")) comparator_13 (
    .a(EPC), .b(\cache槽_5_pc_2 ), .eq(comparator_13_eq));  // open: gt, lt
  Comparator #(.width(32), .mode("twosComplement")) comparator_14 (
    .a(EPC), .b(\cache槽_6_pc_2 ), .eq(comparator_14_eq));  // open: gt, lt
  Comparator #(.width(32), .mode("twosComplement")) comparator_15 (
    .a(EPC), .b(\cache槽_7_pc_2 ), .eq(comparator_15_eq));  // open: gt, lt
  Comparator #(.width(32), .mode("twosComplement")) comparator_16 (
    .a(EPC), .b(\cache槽_8_pc_2 ), .eq(comparator_16_eq));  // open: gt, lt
  and and_18 (and_18_out, comparator_9_eq, \cache槽_1_valid );
  and and_19 (and_19_out, comparator_10_eq, \cache槽_2_valid );
  and and_20 (and_20_out, comparator_11_eq, \cache槽_3_valid );
  and and_21 (and_21_out, comparator_12_eq, \cache槽_4_valid );
  and and_22 (and_22_out, comparator_13_eq, \cache槽_5_valid );
  and and_23 (and_23_out, comparator_14_eq, \cache槽_6_valid );
  and and_24 (and_24_out, comparator_15_eq, \cache槽_7_valid );
  and and_25 (and_25_out, comparator_16_eq, \cache槽_8_valid );
  nor nor_2 (exMiss, and_18_out, and_19_out, and_20_out, and_21_out, and_22_out, and_23_out, and_24_out, and_25_out);

  // Other names for the same wires on the sheet: BraAddr[31:0] = BranchAddr_in; EPC_in[31:0] = EPC; PC_in[31:0] = PC

  // Notes on the sheet:
  //   输入引脚区
  //   输出引脚区
endmodule

module BTB (
  input  [31:0] PC,
  input  [31:0] EX_PC,
  input  [31:0] EX_BranchAddr,
  input  EX_Branch,
  input  EX_BranchTaken,
  input  CLK,
  output [31:0] JumpAddr,
  output PreditJump
);

  wire \全相连cache_1_jump , \全相连cache_1_miss ;

  \全相连Cache  \u_全相连cache_1  (
    .BranchAddr_in(EX_BranchAddr), .AddrReady(EX_Branch), .CLK(CLK), .Miss(\全相连cache_1_miss ),
    .BranchAddr_out(JumpAddr), .BranchTaken(EX_BranchTaken), .Jump(\全相连cache_1_jump ), .PC(PC), .EPC(EX_PC));
  and and_1 (PreditJump, ~\全相连cache_1_miss , \全相连cache_1_jump );  // AND_Gate

  // Other names for the same wires on the sheet: EX_Addr[31:0] = EX_BranchAddr
endmodule
