// Logisim project cpu24_copy.circ as structural Verilog: 6 circuits, main circuit single_mips
module single_mips (
  input  Go_signal,
  input  RST,
  output [7:0] SEG,
  output [7:0] AN
);

  wire ALU_equal, AluSrc, and_1_out, and_2_out, and_3_out, and_4_out, and_5_out, BEQ, BGTZ, BNE, Branch, CLK,
       comparator_1_eq, comparator_2_lt, JAL, JMP, JR, LHU, MemToReg, MemWrite, not_1_out, not_2_out,
       or_1_out, or_2_out, Pause, RegDst, RegWrite, SignedExt, SRAV, SUBU, Syscall;
  wire [3:0] AluOP, PC31_28;
  wire [4:0] multiplexer_4_out, multiplexer_5_out, multiplexer_6_out, multiplexer_7_out, multiplexer_11_out;
  wire [5:0] Func, OP;
  wire [25:6] index;
  wire [27:0] PC_R_q;
  wire [31:0] adder_1_out, adder_2_out, ALU_result, bit_extender_1_out, bit_extender_2_out,
       bit_extender_3_out, bit_extender_4_out, DATA_storage_data, LedData, MDin, multiplexer_1_out,
       multiplexer_2_out, multiplexer_3_out, multiplexer_9_out, multiplexer_10_out, multiplexer_12_out,
       multiplexer_13_out, multiplexer_14_out, RDin, Reg_File_r1, target_offset;

  Clock #(.highDuration(1), .lowDuration(1)) clock_1 (.out(CLK));
  Multiplexer #(.select(1), .width(32), .disabled(0), .enable("false")) multiplexer_1 (
    .in0(Reg_File_r1), .in1({PC31_28, index, Func, 2'b00}), .out(multiplexer_1_out), .sel(JMP));
  Adder #(.width(32)) adder_1 (.a(adder_2_out), .b(target_offset), .out(adder_1_out), .cin(1'b0));  // open: cout
  Multiplexer #(.select(1), .width(32), .disabled(0), .enable("false")) multiplexer_2 (
    .in0(multiplexer_1_out), .in1(adder_1_out), .out(multiplexer_2_out), .sel(Branch));
  or or_1 (or_1_out, JMP, JR, Branch);
  not not_1 (not_1_out, Pause);
  Multiplexer #(.select(1), .width(32), .disabled(0), .enable("false")) multiplexer_3 (
    .in0(adder_2_out), .in1(multiplexer_2_out), .out(multiplexer_3_out), .sel(or_1_out));
  Register #(.width(32), .trigger("rising"), .Select("low")) PC_R (
    .D(multiplexer_3_out), .en(not_1_out), .Q({PC31_28, PC_R_q}), .clk(CLK), .clr(RST), .cs(1'b0),
    .preset(1'b0));
  Adder #(.width(32)) adder_2 (.a({PC31_28, PC_R_q}), .b(32'h4), .out(adder_2_out), .cin(1'b0));  // open: cout
  control control_1 (
    .Func(Func), .OP(OP), .ALU_OP(AluOP), .MemToReg(MemToReg), .MemWrite(MemWrite), .ALU_SRC(AluSrc),
    .RegWrite(RegWrite), .SysCALL(Syscall), .SignedExt(SignedExt), .RegDst(RegDst), .JR(JR), .JMP(JMP),
    .Beq(BEQ), .JAL(JAL), .Bne(BNE), .MF({5{1'b0}}), .SRAV(SRAV), .SUBU(SUBU), .LHU(LHU), .BGTZ(BGTZ));  // open: ERET, MFC0, MTC0
  ROM #(.addrWidth(10), .dataWidth(32)) IR_storage (.addr(PC_R_q[11:2]), .data({OP, index, Func}), .sel(1'b1));
  Multiplexer #(.select(1), .width(5), .disabled(0), .enable("false")) multiplexer_4 (
    .in0(index[20:16]), .in1(index[15:11]), .out(multiplexer_4_out), .sel(RegDst));
  not not_2 (not_2_out, Syscall);
  Multiplexer #(.select(1), .width(5), .disabled(0), .enable("false")) multiplexer_5 (
    .in0(5'b00010), .in1(index[25:21]), .out(multiplexer_5_out), .sel(not_2_out));
  Multiplexer #(.select(1), .width(5), .disabled(0), .enable("false")) multiplexer_6 (
    .in0(5'b00100), .in1(index[20:16]), .out(multiplexer_6_out), .sel(not_2_out));
  Multiplexer #(.select(1), .width(5), .disabled(0), .enable("false")) multiplexer_7 (
    .in0(multiplexer_4_out), .in1({5{1'b1}}), .out(multiplexer_7_out), .sel(JAL));
  Multiplexer #(.select(1), .width(32), .disabled(0), .enable("false")) multiplexer_8 (
    .in0(multiplexer_14_out), .in1(adder_2_out), .out(RDin), .sel(JAL));
  assign bit_extender_1_out = {{16{1'b0}}, {index[15:6], Func}};  // Bit_Extender bit_extender_1
  assign bit_extender_2_out = {{16{index[15]}}, {index[15:6], Func}};  // Bit_Extender bit_extender_2
  Multiplexer #(.select(1), .width(32), .disabled(0), .enable("false")) multiplexer_9 (
    .in0(bit_extender_1_out), .in1(bit_extender_2_out), .out(multiplexer_9_out), .sel(SignedExt));
  MIPS_Regifile Reg_File (
    .Din(RDin), .Clk(CLK), .R1(Reg_File_r1), .R2(MDin), .WE(RegWrite), .WAdr(multiplexer_7_out),
    .R1Adr(multiplexer_5_out), .R2Adr(multiplexer_6_out));
  Comparator #(.width(32), .mode("unsigned")) comparator_1 (
    .a(32'h22), .b(Reg_File_r1), .eq(comparator_1_eq));  // open: gt, lt
  Multiplexer #(.select(1), .width(32), .disabled(0), .enable("false")) multiplexer_10 (
    .in0(MDin), .in1(multiplexer_9_out), .out(multiplexer_10_out), .sel(AluSrc));
  Multiplexer #(.select(1), .width(5), .disabled(0), .enable("false")) multiplexer_11 (
    .in0(index[10:6]), .in1(Reg_File_r1[4:0]), .out(multiplexer_11_out), .sel(SRAV));
  Shifter #(.width(32), .shift("ll")) shifter_1 (.in(multiplexer_9_out), .\dist (5'b00010), .out(target_offset));
  and and_1 (and_1_out, Syscall, comparator_1_eq);
  and and_2 (and_2_out, Syscall, ~comparator_1_eq);  // AND_Gate
  MIPS_ALU ALU (
    .X(Reg_File_r1), .Y(multiplexer_10_out), .AluOP(AluOP), .Equal(ALU_equal), .Result(ALU_result),
    .shamt(multiplexer_11_out));  // open: Result_2
  Register #(.width(32), .trigger("falling"), .Select("low")) register_1 (
    .D(MDin), .en(and_1_out), .Q(LedData), .clk(CLK), .clr(RST), .cs(1'b0), .preset(1'b0));
  Register #(.width(1), .trigger("rising"), .Select("low")) register_2 (
    .D(and_2_out), .en(and_2_out), .Q(Pause), .clk(CLK), .clr(or_2_out), .cs(1'b0), .preset(1'b0));
  or or_2 (or_2_out, Go_signal, RST);
  Comparator #(.width(32), .mode("twosComplement")) comparator_2 (
    .a({32{1'b0}}), .b(Reg_File_r1), .lt(comparator_2_lt));  // open: gt, eq
  // FPGADigit #(.trigger("rising")) FPGAD: pin names not known; wires that end beside it: ALU_result, LedData, CLK, SEG, AN
  and and_3 (and_3_out, BEQ, ALU_equal);
  and and_4 (and_4_out, BNE, ~ALU_equal);  // AND_Gate
  and and_5 (and_5_out, BGTZ, comparator_2_lt);
  RAM #(.addrWidth(10), .dataWidth(32), .bus("separate"), .Select("high")) DATA_storage (
    .addr(ALU_result[11:2]), .din(MDin), .data(DATA_storage_data), .str(MemWrite), .sel(1'b1), .clk(CLK),
    .ld(1'b1), .clr(RST));
  or or_3 (Branch, and_3_out, and_4_out, and_5_out);
  Multiplexer #(.select(1), .width(32), .disabled(0), .enable("false")) multiplexer_12 (
    .in0(ALU_result), .in1(DATA_storage_data), .out(multiplexer_12_out), .sel(MemToReg));
  assign bit_extender_3_out = {{16{1'b0}}, multiplexer_12_out[15:0]};  // Bit_Extender bit_extender_3
  Multiplexer #(.select(1), .width(32), .disabled(0), .enable("false")) multiplexer_13 (
    .in0(bit_extender_3_out), .in1(bit_extender_4_out), .out(multiplexer_13_out), .sel(ALU_result[1]));
  assign bit_extender_4_out = {{16{1'b0}}, multiplexer_12_out[31:16]};  // Bit_Extender bit_extender_4
  Multiplexer #(.select(1), .width(32), .disabled(0), .enable("false")) multiplexer_14 (
    .in0(multiplexer_12_out), .in1(multiplexer_13_out), .out(multiplexer_14_out), .sel(LHU));

  // Other names for the same wires on the sheet: index[5:0] = Func; Shamt[4:0] = index[10:6]; Go = Go_signal

  // Notes on the sheet:
  //   JMP
  //   JR
  //   OP
  //   Func
  //   Beq
  //   Bne
  //   MemToReg
  //   MemWrite
  //   AluOP
  //   AluSrcB
  //   RegWrite
  //   JAL
  //   RegDst
  //   Syscall
  //   contents of IR_storage (hex, n*v repeats v):
  //   20110001 8000c05 20110001 20120002 20130003 8000c09 20110001 20120002 20130003 8000c0d 20110001
  //   20120002 20130003 8000c11 20110001 20120002 20130003 c000cb8 20100001 20110001 118fc0 112020
  //   20020022 c 118882 12200001 8000c15 112020 20020022 c 20110001 118880 112020 20020022 c 12200001
  //   8000c1f 20110001 118fc0 112020 20020022 c 1188c3 112020 20020022 c 118903 112020 20020022 c 118903
  //   112020 20020022 c 118903 112020 20020022 c 118903 112020 20020022 c 118903 112020 20020022 c 118903
  //   112020 20020022 c 118903 112020 20020022 c 20100001 109fc0 139fc3 8021 2012000c 24160003 26100001
  //   3210000f 20080008 20090001 139900 2709825 132020 20020022 c 1094022 1500fff9 22100001 2018000f
  //   2188024 108700 20080008 20090001 139902 2709825 132021 20020022 c 1094022 1500fff9 108702 2c9b022
  //   12c00001 8000c50 4020 1084027 84400 3508ffff 82021 20020022 c 2010ffff 20110000 ae300000 22100001
  //   22310004 ae300000 22100001 22310004 ae300000 22100001 22310004 ae300000 22100001 22310004 ae300000
  //   22100001 22310004 ae300000 22100001 22310004 ae300000 22100001 22310004 ae300000 22100001 22310004
  //   ae300000 22100001 22310004 ae300000 22100001 22310004 ae300000 22100001 22310004 ae300000 22100001
  //   22310004 ae300000 22100001 22310004 ae300000 22100001 22310004 ae300000 22100001 22310004 ae300000
  //   22100001 22310004 22100001 8020 2011003c 8e130000 8e340000 274402a 11000002 ae330000 ae140000
  //   2231fffc 1611fff8 102020 20020022 c 22100004 2011003c 1611fff2 20020032 c 20100000 22100001 102020
  //   20020022 c 22100002 102020 20020022 c 22100003 102020 20020022 c 22100004 102020 20020022 c 22100005
  //   102020 20020022 c 22100006 102020 20020022 c 22100007 102020 20020022 c 22100008 102020 20020022
  //   20020022 c 3e00008
  //   OP
  //   Func
  //   rs
  //   rt
  //   rd
  //   sa
  //   Imm
  //   instr_index
endmodule

module control (
  input  [5:0] OP,
  input  [5:0] Func,
  input  [4:0] MF,
  output [3:0] ALU_OP,
  output MemToReg,
  output MemWrite,
  output ALU_SRC,
  output RegWrite,
  output SysCALL,
  output SignedExt,
  output RegDst,
  output Beq,
  output Bne,
  output JR,
  output JMP,
  output JAL,
  output SRAV,
  output SUBU,
  output LHU,
  output BGTZ,
  output MFC0,
  output MTC0,
  output ERET
);

  control_signal control_signal_1 (
    .OP0(OP[0]), .OP1(OP[1]), .OP2(OP[2]), .OP3(OP[3]), .OP4(OP[4]), .OP5(OP[5]), .F0(Func[0]), .F1(Func[1]),
    .F2(Func[2]), .F3(Func[3]), .F4(Func[4]), .F5(Func[5]), .S0(ALU_OP[0]), .S1(ALU_OP[1]), .S2(ALU_OP[2]),
    .S3(ALU_OP[3]));
  signal_auto signal_auto_1 (
    .OP0(OP[0]), .OP1(OP[1]), .OP2(OP[2]), .OP3(OP[3]), .OP4(OP[4]), .OP5(OP[5]), .F0(Func[0]), .F1(Func[1]),
    .F2(Func[2]), .F3(Func[3]), .F4(Func[4]), .F5(Func[5]), .MemToReg(MemToReg), .MemWrite(MemWrite),
    .ALU_SRC(ALU_SRC), .RegWrite(RegWrite), .SysCALL(SysCALL), .SignedExt(SignedExt), .RegDst(RegDst),
    .BEQ(Beq), .BNE(Bne), .JR(JR), .JUMP(JMP), .JAL(JAL), .SRAV(SRAV), .SUBU(SUBU), .LHU(LHU), .BGTZ(BGTZ));
  and and_1 (ERET, ~OP[0], ~OP[1], ~OP[2], ~OP[3], OP[4], ~OP[5], ~Func[0], ~Func[1], ~Func[2], Func[3], Func[4], ~Func[5]);  // AND_Gate
  and and_2 (MFC0, ~OP[0], ~OP[1], ~OP[2], ~OP[3], OP[4], ~OP[5], ~MF[0], ~MF[1], ~MF[2], ~MF[3], ~MF[4]);  // AND_Gate
  and and_3 (MTC0, ~OP[0], ~OP[1], ~OP[2], ~OP[3], OP[4], ~OP[5], ~MF[0], ~MF[1], MF[2], ~MF[3], ~MF[4]);  // AND_Gate

  // Other names for the same wires on the sheet: OP_CODE[5:0] = OP
endmodule

module control_signal (
  input  OP0,
  input  OP1,
  input  OP2,
  input  OP3,
  input  OP4,
  input  OP5,
  input  F0,
  input  F1,
  input  F2,
  input  F3,
  input  F4,
  input  F5,
  output S0,
  output S1,
  output S2,
  output S3
);

  wire and_1_out, and_2_out, and_3_out, and_4_out, and_5_out, and_6_out, and_7_out, and_8_out, and_9_out,
       and_10_out, and_11_out, and_12_out, and_13_out, and_14_out, and_15_out, and_16_out, and_17_out,
       and_18_out, and_19_out, and_20_out, and_21_out, and_22_out, and_23_out, and_24_out, and_25_out,
       and_26_out, not_1_out, not_2_out, not_3_out, not_4_out, not_5_out, not_6_out, not_7_out, not_8_out,
       not_9_out, not_10_out, not_11_out, not_12_out, not_13_out, not_14_out, not_15_out, not_16_out,
       not_17_out, not_18_out, not_19_out, not_20_out, not_21_out, not_22_out, not_23_out, not_24_out,
       not_25_out, not_26_out, not_27_out, not_28_out, not_29_out, not_30_out, not_31_out, not_32_out,
       not_33_out, not_34_out, not_35_out, not_36_out, not_37_out, not_38_out, not_39_out, not_40_out,
       not_41_out, not_42_out, not_43_out, not_44_out, not_45_out, not_46_out, not_47_out, not_48_out,
       not_49_out, not_50_out, not_51_out, not_52_out, not_53_out, not_54_out, not_55_out, not_56_out,
       not_57_out, not_58_out, not_59_out, not_60_out, not_61_out, not_62_out, not_63_out, not_64_out,
       not_65_out, not_66_out, not_67_out, not_68_out, not_69_out, not_70_out, not_71_out, not_72_out,
       not_73_out, not_74_out, not_75_out, not_76_out, not_77_out, not_78_out, not_79_out, not_80_out,
       not_81_out, not_82_out, not_83_out, not_84_out, not_85_out, not_86_out, not_87_out, not_88_out,
       not_89_out, not_90_out, not_91_out, not_92_out, not_93_out, not_94_out, not_95_out, not_96_out,
       not_97_out, not_98_out, not_99_out, not_100_out, not_101_out, not_102_out, not_103_out, not_104_out,
       not_105_out, not_106_out, not_107_out, not_108_out, not_109_out, not_110_out, not_111_out,
       not_112_out, not_113_out, not_114_out, not_115_out, not_116_out, not_117_out, not_118_out,
       not_119_out, not_120_out, not_121_out, not_122_out, not_123_out, not_124_out, not_125_out,
       not_126_out, not_127_out, not_128_out, not_129_out, not_130_out, not_131_out, not_132_out,
       not_133_out, not_134_out, not_135_out, not_136_out, not_137_out, not_138_out, not_139_out,
       not_140_out, not_141_out, not_142_out, not_143_out, not_144_out, not_145_out, not_146_out,
       not_147_out, not_148_out, not_149_out, not_150_out, not_151_out, not_152_out, not_153_out,
       not_154_out, not_155_out, not_156_out;

  not not_1 (not_1_out, OP0);
  not not_2 (not_2_out, OP1);
  not not_3 (not_3_out, OP2);
  not not_4 (not_4_out, OP4);
  not not_5 (not_5_out, OP5);
  not not_6 (not_6_out, F0);
  not not_7 (not_7_out, F1);
  not not_8 (not_8_out, F3);
  not not_9 (not_9_out, F4);
  not not_10 (not_10_out, OP0);
  not not_11 (not_11_out, OP1);
  not not_12 (not_12_out, OP2);
  not not_13 (not_13_out, OP4);
  not not_14 (not_14_out, OP5);
  not not_15 (not_15_out, F1);
  not not_16 (not_16_out, F2);
  not not_17 (not_17_out, F3);
  not not_18 (not_18_out, F4);
  not not_19 (not_19_out, OP0);
  not not_20 (not_20_out, OP1);
  not not_21 (not_21_out, OP2);
  not not_22 (not_22_out, OP4);
  not not_23 (not_23_out, OP5);
  not not_24 (not_24_out, F0);
  not not_25 (not_25_out, F2);
  not not_26 (not_26_out, F4);
  not not_27 (not_27_out, OP0);
  not not_28 (not_28_out, OP1);
  not not_29 (not_29_out, OP2);
  not not_30 (not_30_out, OP4);
  not not_31 (not_31_out, OP5);
  not not_32 (not_32_out, F3);
  not not_33 (not_33_out, F4);
  not not_34 (not_34_out, F5);
  not not_35 (not_35_out, OP0);
  not not_36 (not_36_out, OP1);
  not not_37 (not_37_out, OP4);
  not not_38 (not_38_out, OP5);
  not not_39 (not_39_out, OP0);
  not not_40 (not_40_out, OP2);
  not not_41 (not_41_out, OP4);
  not not_42 (not_42_out, OP5);
  not not_43 (not_43_out, OP1);
  not not_44 (not_44_out, OP2);
  not not_45 (not_45_out, OP4);
  not not_46 (not_46_out, OP5);
  not not_47 (not_47_out, OP1);
  not not_48 (not_48_out, OP3);
  not not_49 (not_49_out, OP4);
  not not_50 (not_50_out, OP2);
  not not_51 (not_51_out, OP4);
  not not_52 (not_52_out, OP0);
  not not_53 (not_53_out, OP1);
  not not_54 (not_54_out, OP2);
  not not_55 (not_55_out, OP3);
  not not_56 (not_56_out, OP4);
  not not_57 (not_57_out, OP5);
  not not_58 (not_58_out, F0);
  not not_59 (not_59_out, F1);
  not not_60 (not_60_out, F3);
  not not_61 (not_61_out, F4);
  not not_62 (not_62_out, OP0);
  not not_63 (not_63_out, OP1);
  not not_64 (not_64_out, OP2);
  not not_65 (not_65_out, OP3);
  not not_66 (not_66_out, OP4);
  not not_67 (not_67_out, OP5);
  not not_68 (not_68_out, F0);
  not not_69 (not_69_out, F2);
  not not_70 (not_70_out, F3);
  not not_71 (not_71_out, F4);
  not not_72 (not_72_out, OP0);
  not not_73 (not_73_out, OP1);
  not not_74 (not_74_out, OP2);
  not not_75 (not_75_out, OP3);
  not not_76 (not_76_out, OP4);
  not not_77 (not_77_out, OP5);
  not not_78 (not_78_out, F0);
  not not_79 (not_79_out, F2);
  not not_80 (not_80_out, F4);
  not not_81 (not_81_out, OP0);
  not not_82 (not_82_out, OP1);
  not not_83 (not_83_out, OP2);
  not not_84 (not_84_out, OP3);
  not not_85 (not_85_out, OP4);
  not not_86 (not_86_out, OP5);
  not not_87 (not_87_out, F3);
  not not_88 (not_88_out, F4);
  not not_89 (not_89_out, OP0);
  not not_90 (not_90_out, OP1);
  not not_91 (not_91_out, OP4);
  not not_92 (not_92_out, OP5);
  not not_93 (not_93_out, OP0);
  not not_94 (not_94_out, OP2);
  not not_95 (not_95_out, OP4);
  not not_96 (not_96_out, OP5);
  not not_97 (not_97_out, OP0);
  not not_98 (not_98_out, OP1);
  not not_99 (not_99_out, OP2);
  not not_100 (not_100_out, OP4);
  not not_101 (not_101_out, OP5);
  not not_102 (not_102_out, F0);
  not not_103 (not_103_out, F1);
  not not_104 (not_104_out, F3);
  not not_105 (not_105_out, F4);
  not not_106 (not_106_out, OP0);
  not not_107 (not_107_out, OP1);
  not not_108 (not_108_out, OP2);
  not not_109 (not_109_out, OP4);
  not not_110 (not_110_out, OP5);
  not not_111 (not_111_out, F2);
  not not_112 (not_112_out, F3);
  not not_113 (not_113_out, F4);
  not not_114 (not_114_out, OP0);
  not not_115 (not_115_out, OP1);
  not not_116 (not_116_out, OP2);
  not not_117 (not_117_out, OP4);
  not not_118 (not_118_out, OP5);
  not not_119 (not_119_out, F2);
  not not_120 (not_120_out, F4);
  not not_121 (not_121_out, OP0);
  not not_122 (not_122_out, OP1);
  not not_123 (not_123_out, OP4);
  not not_124 (not_124_out, OP5);
  not not_125 (not_125_out, OP1);
  not not_126 (not_126_out, OP2);
  not not_127 (not_127_out, OP4);
  not not_128 (not_128_out, OP5);
  not not_129 (not_129_out, OP1);
  not not_130 (not_130_out, OP3);
  not not_131 (not_131_out, OP4);
  not not_132 (not_132_out, OP2);
  not not_133 (not_133_out, OP4);
  not not_134 (not_134_out, OP0);
  not not_135 (not_135_out, OP1);
  not not_136 (not_136_out, OP2);
  not not_137 (not_137_out, OP3);
  not not_138 (not_138_out, OP4);
  not not_139 (not_139_out, OP5);
  not not_140 (not_140_out, F2);
  not not_141 (not_141_out, F4);
  not not_142 (not_142_out, OP0);
  not not_143 (not_143_out, OP1);
  not not_144 (not_144_out, OP2);
  not not_145 (not_145_out, OP3);
  not not_146 (not_146_out, OP4);
  not not_147 (not_147_out, OP5);
  not not_148 (not_148_out, F3);
  not not_149 (not_149_out, F4);
  not not_150 (not_150_out, OP0);
  not not_151 (not_151_out, OP2);
  not not_152 (not_152_out, OP4);
  not not_153 (not_153_out, OP5);
  not not_154 (not_154_out, OP1);
  not not_155 (not_155_out, OP4);
  not not_156 (not_156_out, OP5);
  and and_1 (and_1_out, not_1_out, not_2_out, not_3_out, not_4_out, not_5_out, not_6_out, not_7_out, not_8_out, not_9_out, F5);
  and and_2 (and_2_out, not_10_out, not_11_out, not_12_out, not_13_out, not_14_out, not_15_out, not_16_out, not_17_out, not_18_out, F5);
  and and_3 (and_3_out, not_19_out, not_20_out, not_21_out, not_22_out, not_23_out, not_24_out, F1, not_25_out, F3, not_26_out, F5);
  and and_4 (and_4_out, not_27_out, not_28_out, not_29_out, not_30_out, not_31_out, F0, F1, not_32_out, not_33_out, not_34_out);
  and and_5 (and_5_out, not_35_out, not_36_out, OP3, not_37_out, not_38_out);
  and and_6 (and_6_out, not_39_out, not_40_out, OP3, not_41_out, not_42_out);
  and and_7 (and_7_out, not_43_out, not_44_out, OP3, not_45_out, not_46_out);
  and and_8 (and_8_out, OP0, not_47_out, OP2, not_48_out, not_49_out, OP5);
  and and_9 (and_9_out, OP0, OP1, not_50_out, not_51_out, OP5);
  and and_10 (and_10_out, not_52_out, not_53_out, not_54_out, not_55_out, not_56_out, not_57_out, not_58_out, not_59_out, F2, not_60_out, not_61_out, F5);
  and and_11 (and_11_out, not_62_out, not_63_out, not_64_out, not_65_out, not_66_out, not_67_out, not_68_out, F1, not_69_out, not_70_out, not_71_out);
  and and_12 (and_12_out, not_72_out, not_73_out, not_74_out, not_75_out, not_76_out, not_77_out, not_78_out, F1, not_79_out, not_80_out, F5);
  and and_13 (and_13_out, not_81_out, not_82_out, not_83_out, not_84_out, not_85_out, not_86_out, F0, F1, not_87_out, not_88_out, F5);
  and and_14 (and_14_out, not_89_out, not_90_out, OP2, OP3, not_91_out, not_92_out);
  and and_15 (and_15_out, not_93_out, OP1, not_94_out, OP3, not_95_out, not_96_out);
  and and_16 (and_16_out, not_97_out, not_98_out, not_99_out, not_100_out, not_101_out, not_102_out, not_103_out, not_104_out, not_105_out, F5);
  and and_17 (and_17_out, not_106_out, not_107_out, not_108_out, not_109_out, not_110_out, not_111_out, not_112_out, not_113_out, F5);
  and and_18 (and_18_out, not_114_out, not_115_out, not_116_out, not_117_out, not_118_out, F0, F1, not_119_out, not_120_out, F5);
  and and_19 (and_19_out, not_121_out, not_122_out, OP3, not_123_out, not_124_out);
  and and_20 (and_20_out, not_125_out, not_126_out, OP3, not_127_out, not_128_out);
  and and_21 (and_21_out, OP0, not_129_out, OP2, not_130_out, not_131_out, OP5);
  and and_22 (and_22_out, OP0, OP1, not_132_out, not_133_out, OP5);
  and and_23 (and_23_out, not_134_out, not_135_out, not_136_out, not_137_out, not_138_out, not_139_out, F1, not_140_out, F3, not_141_out, F5);
  and and_24 (and_24_out, not_142_out, not_143_out, not_144_out, not_145_out, not_146_out, not_147_out, F0, F2, not_148_out, not_149_out, F5);
  and and_25 (and_25_out, not_150_out, OP1, not_151_out, OP3, not_152_out, not_153_out);
  and and_26 (and_26_out, OP0, not_154_out, OP2, OP3, not_155_out, not_156_out);
  or or_1 (S0, and_1_out, and_2_out, and_3_out, and_4_out, and_5_out, and_6_out, and_7_out, and_8_out, and_9_out);
  or or_2 (S1, and_10_out, and_11_out, and_12_out, and_13_out, and_14_out, and_15_out);
  or or_3 (S2, and_16_out, and_17_out, and_18_out, and_19_out, and_20_out, and_21_out, and_22_out);
  or or_4 (S3, and_23_out, and_24_out, and_25_out, and_26_out);
endmodule

module signal_auto (
  input  OP0,
  input  OP1,
  input  OP2,
  input  OP3,
  input  OP4,
  input  OP5,
  input  F0,
  input  F1,
  input  F2,
  input  F3,
  input  F4,
  input  F5,
  output MemToReg,
  output MemWrite,
  output ALU_SRC,
  output RegWrite,
  output SysCALL,
  output SignedExt,
  output RegDst,
  output BEQ,
  output BNE,
  output JR,
  output JUMP,
  output JAL,
  output SRAV,
  output SUBU,
  output LHU,
  output BGTZ
);

  wire and_1_out, and_2_out, and_4_out, and_5_out, and_6_out, and_7_out, and_8_out, and_9_out, and_10_out,
       and_11_out, and_12_out, and_13_out, and_14_out, and_15_out, and_17_out, and_18_out, and_19_out,
       and_20_out, and_21_out, and_22_out, and_23_out, and_24_out, not_1_out, not_2_out, not_3_out,
       not_4_out, not_5_out, not_6_out, not_7_out, not_8_out, not_9_out, not_10_out, not_11_out, not_12_out,
       not_13_out, not_14_out, not_15_out, not_16_out, not_17_out, not_18_out, not_19_out, not_20_out,
       not_21_out, not_22_out, not_23_out, not_24_out, not_25_out, not_26_out, not_27_out, not_28_out,
       not_29_out, not_30_out, not_31_out, not_32_out, not_33_out, not_34_out, not_35_out, not_36_out,
       not_37_out, not_38_out, not_39_out, not_40_out, not_41_out, not_42_out, not_43_out, not_44_out,
       not_45_out, not_46_out, not_47_out, not_48_out, not_49_out, not_50_out, not_51_out, not_52_out,
       not_53_out, not_54_out, not_55_out, not_56_out, not_57_out, not_58_out, not_59_out, not_60_out,
       not_61_out, not_62_out, not_63_out, not_64_out, not_65_out, not_66_out, not_67_out, not_68_out,
       not_69_out, not_70_out, not_71_out, not_72_out, not_73_out, not_74_out, not_75_out, not_76_out,
       not_77_out, not_78_out, not_79_out, not_80_out, not_81_out, not_82_out, not_83_out, not_84_out,
       not_85_out, not_86_out, not_87_out, not_88_out, not_89_out, not_90_out, not_91_out, not_92_out,
       not_93_out, not_94_out, not_95_out, not_96_out, not_97_out, not_98_out, not_99_out, not_100_out,
       not_101_out, not_102_out, not_103_out, not_104_out, not_105_out, not_106_out, not_107_out,
       not_108_out, not_109_out, not_110_out, not_111_out, not_112_out, not_113_out, not_114_out,
       not_115_out, not_116_out, not_117_out, not_118_out, not_119_out, not_120_out, not_121_out,
       not_122_out, not_123_out, not_124_out, not_125_out, not_126_out, not_127_out, not_128_out,
       not_129_out, not_130_out, not_131_out, not_132_out, not_133_out, not_134_out, not_135_out,
       not_136_out, not_137_out, not_138_out, not_139_out, not_140_out, not_141_out, not_142_out,
       not_143_out, not_144_out, not_145_out, not_146_out, not_147_out, not_148_out, not_149_out,
       not_150_out, not_151_out, not_152_out, not_153_out, not_154_out, not_155_out, not_156_out,
       not_157_out, not_158_out, not_159_out, not_160_out, not_161_out, not_162_out, not_163_out,
       not_164_out, not_165_out, not_166_out, not_167_out, not_168_out, not_169_out, not_170_out,
       not_171_out, not_172_out, not_173_out, not_174_out, not_175_out, not_176_out;

  not not_1 (not_1_out, OP1);
  not not_2 (not_2_out, OP3);
  not not_3 (not_3_out, OP4);
  not not_4 (not_4_out, OP2);
  not not_5 (not_5_out, OP3);
  not not_6 (not_6_out, OP4);
  not not_7 (not_7_out, OP2);
  not not_8 (not_8_out, OP4);
  not not_9 (not_9_out, OP0);
  not not_10 (not_10_out, OP2);
  not not_11 (not_11_out, OP4);
  not not_12 (not_12_out, OP5);
  not not_13 (not_13_out, OP1);
  not not_14 (not_14_out, OP4);
  not not_15 (not_15_out, OP5);
  not not_16 (not_16_out, OP1);
  not not_17 (not_17_out, OP3);
  not not_18 (not_18_out, OP4);
  not not_19 (not_19_out, OP2);
  not not_20 (not_20_out, OP4);
  not not_21 (not_21_out, OP0);
  not not_22 (not_22_out, OP1);
  not not_23 (not_23_out, OP2);
  not not_24 (not_24_out, OP4);
  not not_25 (not_25_out, OP5);
  not not_26 (not_26_out, F0);
  not not_27 (not_27_out, F2);
  not not_28 (not_28_out, F3);
  not not_29 (not_29_out, F4);
  not not_30 (not_30_out, OP0);
  not not_31 (not_31_out, OP1);
  not not_32 (not_32_out, OP2);
  not not_33 (not_33_out, OP4);
  not not_34 (not_34_out, OP5);
  not not_35 (not_35_out, F1);
  not not_36 (not_36_out, F3);
  not not_37 (not_37_out, F4);
  not not_38 (not_38_out, OP0);
  not not_39 (not_39_out, OP1);
  not not_40 (not_40_out, OP2);
  not not_41 (not_41_out, OP4);
  not not_42 (not_42_out, OP5);
  not not_43 (not_43_out, F2);
  not not_44 (not_44_out, F4);
  not not_45 (not_45_out, OP0);
  not not_46 (not_46_out, OP1);
  not not_47 (not_47_out, OP2);
  not not_48 (not_48_out, OP4);
  not not_49 (not_49_out, OP5);
  not not_50 (not_50_out, F3);
  not not_51 (not_51_out, F4);
  not not_52 (not_52_out, OP0);
  not not_53 (not_53_out, OP2);
  not not_54 (not_54_out, OP4);
  not not_55 (not_55_out, OP5);
  not not_56 (not_56_out, OP1);
  not not_57 (not_57_out, OP4);
  not not_58 (not_58_out, OP5);
  not not_59 (not_59_out, OP1);
  not not_60 (not_60_out, OP3);
  not not_61 (not_61_out, OP4);
  not not_62 (not_62_out, OP2);
  not not_63 (not_63_out, OP3);
  not not_64 (not_64_out, OP4);
  not not_65 (not_65_out, OP0);
  not not_66 (not_66_out, OP1);
  not not_67 (not_67_out, OP2);
  not not_68 (not_68_out, OP3);
  not not_69 (not_69_out, OP4);
  not not_70 (not_70_out, OP5);
  not not_71 (not_71_out, F0);
  not not_72 (not_72_out, F1);
  not not_73 (not_73_out, F4);
  not not_74 (not_74_out, F5);
  not not_75 (not_75_out, OP0);
  not not_76 (not_76_out, OP2);
  not not_77 (not_77_out, OP4);
  not not_78 (not_78_out, OP5);
  not not_79 (not_79_out, OP1);
  not not_80 (not_80_out, OP2);
  not not_81 (not_81_out, OP4);
  not not_82 (not_82_out, OP5);
  not not_83 (not_83_out, OP1);
  not not_84 (not_84_out, OP3);
  not not_85 (not_85_out, OP4);
  not not_86 (not_86_out, OP5);
  not not_87 (not_87_out, OP3);
  not not_88 (not_88_out, OP4);
  not not_89 (not_89_out, OP5);
  not not_90 (not_90_out, OP0);
  not not_91 (not_91_out, OP1);
  not not_92 (not_92_out, OP2);
  not not_93 (not_93_out, OP3);
  not not_94 (not_94_out, OP4);
  not not_95 (not_95_out, OP5);
  not not_96 (not_96_out, F0);
  not not_97 (not_97_out, F2);
  not not_98 (not_98_out, F3);
  not not_99 (not_99_out, F4);
  not not_100 (not_100_out, OP0);
  not not_101 (not_101_out, OP1);
  not not_102 (not_102_out, OP2);
  not not_103 (not_103_out, OP3);
  not not_104 (not_104_out, OP4);
  not not_105 (not_105_out, OP5);
  not not_106 (not_106_out, F1);
  not not_107 (not_107_out, F3);
  not not_108 (not_108_out, F4);
  not not_109 (not_109_out, OP0);
  not not_110 (not_110_out, OP1);
  not not_111 (not_111_out, OP2);
  not not_112 (not_112_out, OP3);
  not not_113 (not_113_out, OP4);
  not not_114 (not_114_out, OP5);
  not not_115 (not_115_out, F2);
  not not_116 (not_116_out, F4);
  not not_117 (not_117_out, OP0);
  not not_118 (not_118_out, OP1);
  not not_119 (not_119_out, OP2);
  not not_120 (not_120_out, OP3);
  not not_121 (not_121_out, OP4);
  not not_122 (not_122_out, OP5);
  not not_123 (not_123_out, F3);
  not not_124 (not_124_out, F4);
  not not_125 (not_125_out, OP0);
  not not_126 (not_126_out, OP1);
  not not_127 (not_127_out, OP3);
  not not_128 (not_128_out, OP4);
  not not_129 (not_129_out, OP5);
  not not_130 (not_130_out, OP1);
  not not_131 (not_131_out, OP3);
  not not_132 (not_132_out, OP4);
  not not_133 (not_133_out, OP5);
  not not_134 (not_134_out, OP0);
  not not_135 (not_135_out, OP1);
  not not_136 (not_136_out, OP2);
  not not_137 (not_137_out, OP3);
  not not_138 (not_138_out, OP4);
  not not_139 (not_139_out, OP5);
  not not_140 (not_140_out, F0);
  not not_141 (not_141_out, F1);
  not not_142 (not_142_out, F2);
  not not_143 (not_143_out, F4);
  not not_144 (not_144_out, F5);
  not not_145 (not_145_out, OP2);
  not not_146 (not_146_out, OP3);
  not not_147 (not_147_out, OP4);
  not not_148 (not_148_out, OP5);
  not not_149 (not_149_out, OP2);
  not not_150 (not_150_out, OP3);
  not not_151 (not_151_out, OP4);
  not not_152 (not_152_out, OP5);
  not not_153 (not_153_out, OP0);
  not not_154 (not_154_out, OP1);
  not not_155 (not_155_out, OP2);
  not not_156 (not_156_out, OP3);
  not not_157 (not_157_out, OP4);
  not not_158 (not_158_out, OP5);
  not not_159 (not_159_out, F3);
  not not_160 (not_160_out, F4);
  not not_161 (not_161_out, F5);
  not not_162 (not_162_out, OP0);
  not not_163 (not_163_out, OP1);
  not not_164 (not_164_out, OP2);
  not not_165 (not_165_out, OP3);
  not not_166 (not_166_out, OP4);
  not not_167 (not_167_out, OP5);
  not not_168 (not_168_out, F2);
  not not_169 (not_169_out, F3);
  not not_170 (not_170_out, F4);
  not not_171 (not_171_out, OP1);
  not not_172 (not_172_out, OP3);
  not not_173 (not_173_out, OP4);
  not not_174 (not_174_out, OP3);
  not not_175 (not_175_out, OP4);
  not not_176 (not_176_out, OP5);
  and and_1 (and_1_out, OP0, not_1_out, OP2, not_2_out, not_3_out, OP5);
  and and_2 (and_2_out, OP0, OP1, not_4_out, not_5_out, not_6_out, OP5);
  and and_3 (MemWrite, OP0, OP1, not_7_out, OP3, not_8_out, OP5);
  and and_4 (and_4_out, not_9_out, not_10_out, OP3, not_11_out, not_12_out);
  and and_5 (and_5_out, not_13_out, OP3, not_14_out, not_15_out);
  and and_6 (and_6_out, OP0, not_16_out, OP2, not_17_out, not_18_out, OP5);
  and and_7 (and_7_out, OP0, OP1, not_19_out, not_20_out, OP5);
  and and_8 (and_8_out, not_21_out, not_22_out, not_23_out, not_24_out, not_25_out, not_26_out, not_27_out, not_28_out, not_29_out);
  and and_9 (and_9_out, not_30_out, not_31_out, not_32_out, not_33_out, not_34_out, not_35_out, not_36_out, not_37_out, F5);
  and and_10 (and_10_out, not_38_out, not_39_out, not_40_out, not_41_out, not_42_out, F1, not_43_out, not_44_out, F5);
  and and_11 (and_11_out, not_45_out, not_46_out, not_47_out, not_48_out, not_49_out, F0, F1, not_50_out, not_51_out);
  and and_12 (and_12_out, not_52_out, not_53_out, OP3, not_54_out, not_55_out);
  and and_13 (and_13_out, not_56_out, OP3, not_57_out, not_58_out);
  and and_14 (and_14_out, OP0, not_59_out, OP2, not_60_out, not_61_out, OP5);
  and and_15 (and_15_out, OP0, OP1, not_62_out, not_63_out, not_64_out);
  and and_16 (SysCALL, not_65_out, not_66_out, not_67_out, not_68_out, not_69_out, not_70_out, not_71_out, not_72_out, F2, F3, not_73_out, not_74_out);
  and and_17 (and_17_out, not_75_out, not_76_out, OP3, not_77_out, not_78_out);
  and and_18 (and_18_out, not_79_out, not_80_out, OP3, not_81_out, not_82_out);
  and and_19 (and_19_out, not_83_out, OP2, not_84_out, not_85_out, not_86_out);
  and and_20 (and_20_out, OP0, OP2, not_87_out, not_88_out, not_89_out);
  and and_21 (and_21_out, not_90_out, not_91_out, not_92_out, not_93_out, not_94_out, not_95_out, not_96_out, not_97_out, not_98_out, not_99_out);
  and and_22 (and_22_out, not_100_out, not_101_out, not_102_out, not_103_out, not_104_out, not_105_out, not_106_out, not_107_out, not_108_out, F5);
  and and_23 (and_23_out, not_109_out, not_110_out, not_111_out, not_112_out, not_113_out, not_114_out, F1, not_115_out, not_116_out, F5);
  and and_24 (and_24_out, not_117_out, not_118_out, not_119_out, not_120_out, not_121_out, not_122_out, F0, F1, not_123_out, not_124_out);
  and and_25 (BEQ, not_125_out, not_126_out, OP2, not_127_out, not_128_out, not_129_out);
  and and_26 (BNE, OP0, not_130_out, OP2, not_131_out, not_132_out, not_133_out);
  and and_27 (JR, not_134_out, not_135_out, not_136_out, not_137_out, not_138_out, not_139_out, not_140_out, not_141_out, not_142_out, F3, not_143_out, not_144_out);
  and and_28 (JUMP, OP1, not_145_out, not_146_out, not_147_out, not_148_out);
  and and_29 (JAL, OP0, OP1, not_149_out, not_150_out, not_151_out, not_152_out);
  and and_30 (SRAV, not_153_out, not_154_out, not_155_out, not_156_out, not_157_out, not_158_out, F0, F1, F2, not_159_out, not_160_out, not_161_out);
  and and_31 (SUBU, not_162_out, not_163_out, not_164_out, not_165_out, not_166_out, not_167_out, F0, F1, not_168_out, not_169_out, not_170_out, F5);
  and and_32 (LHU, OP0, not_171_out, OP2, not_172_out, not_173_out, OP5);
  and and_33 (BGTZ, OP0, OP1, OP2, not_174_out, not_175_out, not_176_out);
  or or_1 (MemToReg, and_1_out, and_2_out);
  or or_2 (ALU_SRC, and_4_out, and_5_out, and_6_out, and_7_out);
  or or_3 (RegWrite, and_8_out, and_9_out, and_10_out, and_11_out, and_12_out, and_13_out, and_14_out, and_15_out);
  or or_4 (SignedExt, and_17_out, and_18_out, and_19_out, and_20_out);
  or or_5 (RegDst, and_21_out, and_22_out, and_23_out, and_24_out);
endmodule

// ALU
module MIPS_ALU (
  input  [4:0] shamt,
  input  [31:0] X,
  input  [31:0] Y,
  input  [3:0] AluOP,
  output Equal,
  output [31:0] Result,
  output [31:0] Result_2
);

  wire [0:0] comparator_1_lt, comparator_2_lt;
  wire [31:0] adder_1_out, AND_out, divider_1_out, divider_1_rem, multiplier_1_cout, multiplier_1_out,
       NOR_out, OR_out, shifter_1_out, shifter_2_out, shifter_3_out, subtractor_1_out, XOR_out;

  assign AND_out = X & Y;  // AND_Gate AND, 32 bits wide
  assign OR_out = X | Y;  // OR_Gate OR, 32 bits wide
  Shifter #(.width(32), .shift("ll")) shifter_1 (.in(Y), .\dist (shamt), .out(shifter_1_out));
  Shifter #(.width(32), .shift("ar")) shifter_2 (.in(Y), .\dist (shamt), .out(shifter_2_out));
  Shifter #(.width(32), .shift("lr")) shifter_3 (.in(Y), .\dist (shamt), .out(shifter_3_out));
  Multiplier #(.width(32)) multiplier_1 (.a(X), .b(Y), .out(multiplier_1_out), .cout(multiplier_1_cout));  // open: cin
  Divider #(.width(32)) divider_1 (.a(X), .b(Y), .out(divider_1_out), .rem(divider_1_rem));  // open: upper
  Adder #(.width(32)) adder_1 (.a(X), .b(Y), .out(adder_1_out));  // open: cin, cout
  Subtractor #(.width(32)) subtractor_1 (.a(X), .b(Y), .out(subtractor_1_out));  // open: bin, bout
  assign XOR_out = X ^ Y;  // XOR_Gate XOR, 32 bits wide
  assign NOR_out = ~(X | Y);  // NOR_Gate NOR, 32 bits wide
  Comparator #(.width(32), .mode("twosComplement")) comparator_1 (
    .a(X), .b(Y), .eq(Equal), .lt(comparator_1_lt[0]));  // open: gt
  Comparator #(.width(32), .mode("unsigned")) comparator_2 (.a(X), .b(Y), .lt(comparator_2_lt[0]));  // open: gt, eq
  Multiplexer #(.select(4), .width(32), .disabled("Z"), .enable("false")) multiplexer_1 (
    .in0(shifter_1_out), .in1(shifter_2_out), .in2(shifter_3_out), .in3(multiplier_1_out),
    .in4(divider_1_out), .in5(adder_1_out), .in6(subtractor_1_out), .in7(AND_out), .in8(OR_out),
    .in9(XOR_out), .in10(NOR_out), .in11({{31{1'b0}}, comparator_1_lt[0]}),
    .in12({{31{1'b0}}, comparator_2_lt[0]}), .in13({32{1'b0}}), .in14({32{1'b0}}), .in15({32{1'b0}}),
    .out(Result), .sel(AluOP));
  Multiplexer #(.select(4), .width(32), .disabled("Z"), .enable("false")) multiplexer_2 (
    .in0({32{1'b0}}), .in1({32{1'b0}}), .in2({32{1'b0}}), .in3(multiplier_1_cout), .in4(divider_1_rem),
    .in5({32{1'b0}}), .in6({32{1'b0}}), .in7({32{1'b0}}), .in8({32{1'b0}}), .in9({32{1'b0}}),
    .in10({32{1'b0}}), .in11({32{1'b0}}), .in12({32{1'b0}}), .in13({32{1'b0}}), .in14({32{1'b0}}),
    .in15({32{1'b0}}), .out(Result_2), .sel(AluOP));

  // Other names for the same wires on the sheet: Result2[31:0] = Result_2; S[3:0] = AluOP

  // Notes on the sheet:
  //   不要改变此引脚区域内容，也不要改变ALU封装形式
  //   输入引脚
  //   输出引脚
endmodule

module MIPS_Regifile (
  input  [31:0] Din,
  input  Clk,
  input  WE,
  input  [4:0] R1Adr,
  input  [4:0] WAdr,
  input  [4:0] R2Adr,
  output [31:0] R1,
  output [31:0] R2
);

  // RegisterFile registerfile_1: pin names not known; wires that end beside it: Din, Clk, WE, WAdr, R1Adr, R2Adr, R1, R2
endmodule
